// Logisim project GameCirc.circ as structural Verilog: 3 circuits, main circuit game
module game (
  input  EN,
  input  CLK,
  input  RST,
  input  UP,
  input  DN,
  input  CLICK,
  output WIN
);

  wire and_1_out, and_2_out, comparator_1_eq, counter_2_carry, d_ff_1_q, not_1_out, or_1_out, undriven,
       xor_1_out;
  wire [5:0] counter_1_q, shuffler_1_out_3;

  xor xor_1 (xor_1_out, WIN, EN);
  or or_1 (or_1_out, UP, DN);
  D_Flip_Flop d_ff_1 (.D(xor_1_out), .clk(CLK), .Q(d_ff_1_q));  // open: Qn, preset, reset
  and and_1 (and_1_out, ~d_ff_1_q, xor_1_out);  // AND_Gate
  not not_1 (not_1_out, DN);
  shuffler shuffler_1 (.RST(undriven), .SHUF(and_1_out), .out_3(shuffler_1_out_3));
  Counter #(.width(6), .max('h3f)) counter_1 (
    .clr(RST), .up(not_1_out), .clk(or_1_out), .Q(counter_1_q));  // open: load, count, D, carry
  // Probe on shuffler_1_out_3
  // Probe on counter_1_q
  Comparator #(.width(6)) comparator_1 (.a(shuffler_1_out_3), .b(counter_1_q), .eq(comparator_1_eq));  // open: gt, lt
  and and_2 (and_2_out, comparator_1_eq, CLICK);
  Counter #(.width(12), .max('hfff)) counter_2 (
    .clr(CLICK), .clk(CLK), .carry(counter_2_carry));  // open: load, up, count, D, Q
  D_Flip_Flop d_ff_2 (.Q(WIN), .preset(and_2_out), .reset(counter_2_carry));  // open: D, clk, Qn
endmodule

module shuffler (
  input  RST,
  input  SHUF,
  output [5:0] out_3
);

  wire and_1_out, d_ff_1_q;

  D_Flip_Flop d_ff_1 (.D(SHUF), .Q(d_ff_1_q));  // open: clk, Qn, preset, reset
  and and_1 (and_1_out, ~d_ff_1_q, SHUF);  // AND_Gate
  Random #(.width(6)) random_1 (.clr(RST), .next(and_1_out), .clk(and_1_out), .out(out_3));
endmodule

module shufDec (
  input  b0,
  input  b1,
  input  b2,
  input  b3,
  output SHUF
);

  wire not_1_out, not_2_out;

  not not_1 (not_1_out, b0);
  not not_2 (not_2_out, b1);
  and and_1 (SHUF, not_1_out, not_2_out, b2, b3);
endmodule
