// Logisim project LogicAlarm.circ as structural Verilog: 57 circuits, main circuit main
module main (
  input  chB,
  input  chA,
  input  chC,
  output vcc,
  output gnd,
  output BUZZER
);

  wire AL_SET_EN, Alarm_1_buzz, and_2_out, and_3_out, and_4_out, and_5_out, and_6_out, and_7_out,
       bitselector_1_out, bitselector_2_out, bitselector_3_out, bitselector_4_out, bitselector_5_out,
       bitselector_6_out, bitselector_7_out, bitselector_8_out, bitselector_9_out, Button_1_out,
       Button_2_out, CHRONO_EN, CLK_SEC, clock_1_out, Debounce_1_bttn_out, Debounce_2_bttn_out,
       decod_rotation_1_ccw, decod_rotation_1_click, decod_rotation_1_cw, decod_rotation_1_en,
       detect_pos_edge_1_pos_edge, detect_pos_edge_2_pos_edge, EN_AL, FUN_buzz, FUN_EN, GAME_EN, HMS_EN,
       HMS_SET_EN, or_2_out, or_3_out, or_4_out, SET_HMS_1_set_hms, switch_chrono, TONE_SEL_EN,
       ToneSelect_1_buzz, ToneSelect_1_set_tone;
  wire [2:0] FSM_1_sel;
  wire [3:0] bit_extender_1_out, dip_switch_sw1, ToneSelect_1_tone;
  wire [5:0] Alarm_1_dsp_h0, Alarm_1_dsp_h1, Alarm_1_dsp_m0, Alarm_1_dsp_m1, Alarm_1_dsp_s0, Alarm_1_dsp_s1,
       CHRONO_1_disp0, CHRONO_1_disp1, CHRONO_1_disp2, CHRONO_1_disp3, CHRONO_1_disp4, CHRONO_1_disp5, H_BIN,
       hms24_1_hms0, hms24_1_hms1, hms24_1_hms2, hms24_1_hms3, hms24_1_hms4, hms24_1_hms5, M_BIN, S_BIN,
       SET_HMS_1_ch_hour, SET_HMS_1_ch_min, SET_HMS_1_ch_sec, SET_HMS_1_chhms0, SET_HMS_1_chhms1,
       SET_HMS_1_chhms2, SET_HMS_1_chhms3, SET_HMS_1_chhms4, SET_HMS_1_chhms5, ToneSelect_1_d0,
       ToneSelect_1_d1, ToneSelect_1_d2, ToneSelect_1_d3, ToneSelect_1_d4, ToneSelect_1_d5;
  wire [7:0] DISP_SEL_1_disp0, DISP_SEL_1_disp1, DISP_SEL_1_disp2, DISP_SEL_1_disp3, DISP_SEL_1_disp4,
       DISP_SEL_1_disp5, Rot_decode_selector_1_ccw_out, Rot_decode_selector_1_click_out,
       Rot_decode_selector_1_cw_out, Rot_decode_selector_1_en_out, sixSegDriver_1_out0, sixSegDriver_1_out1,
       sixSegDriver_1_out2, sixSegDriver_1_out3, sixSegDriver_1_out4, sixSegDriver_1_out5,
       sixSegDriver_2_out0, sixSegDriver_2_out1, sixSegDriver_2_out2, sixSegDriver_2_out3,
       sixSegDriver_2_out4, sixSegDriver_2_out5, sixSegDriver_3_out0, sixSegDriver_3_out1,
       sixSegDriver_3_out2, sixSegDriver_3_out3, sixSegDriver_3_out4, sixSegDriver_3_out5,
       sixSegDriver_4_out0, sixSegDriver_4_out1, sixSegDriver_4_out2, sixSegDriver_4_out3,
       sixSegDriver_4_out4, sixSegDriver_4_out5, sixSegDriver_6_out0, sixSegDriver_6_out1,
       sixSegDriver_6_out2, sixSegDriver_6_out3, sixSegDriver_6_out4, sixSegDriver_6_out5;
  wire [9:0] FUN_LEDS;

  Clock clock_1 (.out(clock_1_out));
  Button Button_1 (.out(Button_1_out));
  Button Button_2 (.out(Button_2_out));
  DipSwitch #(.number(10)) dip_switch (
    .sw1(dip_switch_sw1[0]), .sw2(dip_switch_sw1[1]), .sw3(dip_switch_sw1[2]), .sw4(dip_switch_sw1[3]),
    .sw9(switch_chrono), .sw10(EN_AL));  // open: sw5, sw6, sw7, sw8
  decod_rotation decod_rotation_1 (
    .ChB(chB), .ChA(chA), .CLK(clock_1_out), .ChC(chC), .EN(decod_rotation_1_en), .CW(decod_rotation_1_cw),
    .CCW(decod_rotation_1_ccw), .Click(decod_rotation_1_click));
  Debounce Debounce_1 (.BTTN(Button_1_out), .CLK(clock_1_out), .BTTN_OUT(Debounce_1_bttn_out));
  Debounce Debounce_2 (.BTTN(Button_2_out), .CLK(clock_1_out), .BTTN_OUT(Debounce_2_bttn_out));
  Rot_decode_selector Rot_decode_selector_1 (
    .SEL(FSM_1_sel), .EN(decod_rotation_1_en), .CW(decod_rotation_1_cw), .CCW(decod_rotation_1_ccw),
    .Click(decod_rotation_1_click), .EN_OUT(Rot_decode_selector_1_en_out),
    .CW_OUT(Rot_decode_selector_1_cw_out), .CCW_OUT(Rot_decode_selector_1_ccw_out),
    .CLICK_OUT(Rot_decode_selector_1_click_out));
  assign bit_extender_1_out = {{3{TONE_SEL_EN}}, TONE_SEL_EN};  // Bit_Extender bit_extender_1
  detect_pos_edge detect_pos_edge_1 (
    .in_in(Debounce_1_bttn_out), .clk(clock_1_out), .pos_edge(detect_pos_edge_1_pos_edge));
  detect_pos_edge detect_pos_edge_2 (
    .in_in(Debounce_2_bttn_out), .clk(clock_1_out), .pos_edge(detect_pos_edge_2_pos_edge));
  clk_div clk_div_1 (.CLK_IN(clock_1_out), .CLK_SEL(4'b1010), .CLK_OUT(CLK_SEC));
  // AND_Gate and_1 has open pins: in0=bit_extender_1_out, out=open
  Demultiplexer #(.select(3), .enable("false")) demultiplexer_1 (
    .out0(HMS_EN), .out1(HMS_SET_EN), .out2(AL_SET_EN), .out3(CHRONO_EN), .out4(TONE_SEL_EN), .out5(FUN_EN),
    .out6(GAME_EN), .in(1'b1), .sel(FSM_1_sel));  // open: out7
  FSM FSM_1 (.Bfwd(detect_pos_edge_1_pos_edge), .BBack(detect_pos_edge_2_pos_edge), .CIN(clock_1_out), .SEL(FSM_1_sel));
  BitSelector bitselector_1 (.in(Rot_decode_selector_1_en_out), .out(bitselector_1_out), .sel(3'b001));
  BitSelector bitselector_2 (.in(Rot_decode_selector_1_cw_out), .out(bitselector_2_out), .sel(3'b001));
  BitSelector bitselector_3 (.in(Rot_decode_selector_1_ccw_out), .out(bitselector_3_out), .sel(3'b001));
  BitSelector bitselector_4 (.in(Rot_decode_selector_1_click_out), .out(bitselector_4_out), .sel(3'b001));
  BitSelector bitselector_5 (.in(Rot_decode_selector_1_en_out), .out(bitselector_5_out), .sel(3'b010));
  BitSelector bitselector_6 (.in(Rot_decode_selector_1_cw_out), .out(bitselector_6_out), .sel(3'b010));
  BitSelector bitselector_7 (.in(Rot_decode_selector_1_ccw_out), .out(bitselector_7_out), .sel(3'b010));
  BitSelector bitselector_8 (.in(Rot_decode_selector_1_click_out), .out(bitselector_8_out), .sel(3'b010));
  BitSelector bitselector_9 (.in(Rot_decode_selector_1_click_out), .out(bitselector_9_out), .sel(3'b011));
  and and_2 (and_2_out, bitselector_1_out, bitselector_2_out);
  and and_3 (and_3_out, bitselector_1_out, bitselector_3_out);
  and and_4 (and_4_out, bitselector_5_out, bitselector_6_out);
  and and_5 (and_5_out, bitselector_5_out, bitselector_7_out);
  HMS24 hms24_1 (
    .h0_set(SET_HMS_1_ch_hour), .HMS3(hms24_1_hms3), .SECS_B(S_BIN), .RST(1'b0), .MINS_B(M_BIN),
    .HMS2(hms24_1_hms2), .UP_DN(1'b0), .s0_set(SET_HMS_1_ch_sec), .SET(SET_HMS_1_set_hms),
    .HMS5(hms24_1_hms5), .HOURS_B(H_BIN), .EN(HMS_EN), .CLK(CLK_SEC), .HMS4(hms24_1_hms4),
    .m0_set(SET_HMS_1_ch_min), .HMS1(hms24_1_hms1), .HMS0(hms24_1_hms0), .SYS_CLK(clock_1_out));
  CHRONO CHRONO_1 (
    .EN(CHRONO_EN), .Click(bitselector_9_out), .clk_sec(CLK_SEC), .clk(clock_1_out),
    .DP_Switch(switch_chrono), .disp0(CHRONO_1_disp0), .disp1(CHRONO_1_disp1), .disp2(CHRONO_1_disp2),
    .disp3(CHRONO_1_disp3), .disp4(CHRONO_1_disp4), .disp5(CHRONO_1_disp5));
  FUN FUN_1 (.EN(FUN_EN), .leds(FUN_LEDS), .buzz(FUN_buzz));
  SET_HMS SET_HMS_1 (
    .EN(HMS_SET_EN), .CLK(clock_1_out), .h_in(H_BIN), .m_in(M_BIN), .s_in(S_BIN), .UP(and_2_out),
    .DOWN(and_3_out), .CLICK(bitselector_4_out), .set_hms(SET_HMS_1_set_hms), .ch_hour(SET_HMS_1_ch_hour),
    .ch_min(SET_HMS_1_ch_min), .ch_sec(SET_HMS_1_ch_sec), .chHMS5(SET_HMS_1_chhms5),
    .chHMS4(SET_HMS_1_chhms4), .chHMS3(SET_HMS_1_chhms3), .chHMS2(SET_HMS_1_chhms2),
    .chHMS1(SET_HMS_1_chhms1), .chHMS0(SET_HMS_1_chhms0));
  ALARM Alarm_1 (
    .EN(AL_SET_EN), .HIN(H_BIN), .MIN(M_BIN), .SIN(S_BIN), .UP(and_4_out), .DN(and_5_out),
    .CLICK(bitselector_8_out), .CLK(clock_1_out), .AL_RST(decod_rotation_1_click), .EN_AL(EN_AL),
    .TONE_SEL(ToneSelect_1_tone), .set_tone(ToneSelect_1_set_tone), .DSP_H1(Alarm_1_dsp_h1),
    .DSP_H0(Alarm_1_dsp_h0), .DSP_M1(Alarm_1_dsp_m1), .DSP_M0(Alarm_1_dsp_m0), .DSP_S1(Alarm_1_dsp_s1),
    .DSP_S0(Alarm_1_dsp_s0), .BUZZ(Alarm_1_buzz));
  TONE_SELECT ToneSelect_1 (
    .EN(TONE_SEL_EN), .dp_switch(dip_switch_sw1), .TONE(ToneSelect_1_tone), .D0(ToneSelect_1_d0),
    .D1(ToneSelect_1_d1), .D2(ToneSelect_1_d2), .D3(ToneSelect_1_d3), .D4(ToneSelect_1_d4),
    .D5(ToneSelect_1_d5), .buzz(ToneSelect_1_buzz), .set_tone(ToneSelect_1_set_tone));
  or or_1 (BUZZER, Alarm_1_buzz, ToneSelect_1_buzz, FUN_buzz);
  sixSegDriver sixSegDriver_1 (
    .dsp0(hms24_1_hms5), .dsp1(hms24_1_hms4), .dsp2(hms24_1_hms3), .dsp3(hms24_1_hms2), .dsp4(hms24_1_hms1),
    .dsp5(hms24_1_hms0), .Out0(sixSegDriver_1_out0), .Out1(sixSegDriver_1_out1), .Out2(sixSegDriver_1_out2),
    .Out3(sixSegDriver_1_out3), .Out4(sixSegDriver_1_out4), .Out5(sixSegDriver_1_out5));
  sixSegDriver sixSegDriver_2 (
    .dsp0(SET_HMS_1_chhms5), .dsp1(SET_HMS_1_chhms4), .dsp2(SET_HMS_1_chhms3), .dsp3(SET_HMS_1_chhms2),
    .dsp4(SET_HMS_1_chhms1), .dsp5(SET_HMS_1_chhms0), .Out0(sixSegDriver_2_out0), .Out1(sixSegDriver_2_out1),
    .Out2(sixSegDriver_2_out2), .Out3(sixSegDriver_2_out3), .Out4(sixSegDriver_2_out4),
    .Out5(sixSegDriver_2_out5));
  sixSegDriver sixSegDriver_3 (
    .dsp0(Alarm_1_dsp_h1), .dsp1(Alarm_1_dsp_h0), .dsp2(Alarm_1_dsp_m1), .dsp3(Alarm_1_dsp_m0),
    .dsp4(Alarm_1_dsp_s1), .dsp5(Alarm_1_dsp_s0), .Out0(sixSegDriver_3_out0), .Out1(sixSegDriver_3_out1),
    .Out2(sixSegDriver_3_out2), .Out3(sixSegDriver_3_out3), .Out4(sixSegDriver_3_out4),
    .Out5(sixSegDriver_3_out5));
  sixSegDriver sixSegDriver_4 (
    .dsp0(ToneSelect_1_d0), .dsp1(ToneSelect_1_d1), .dsp2(ToneSelect_1_d2), .dsp3(ToneSelect_1_d3),
    .dsp4(ToneSelect_1_d4), .dsp5(ToneSelect_1_d5), .Out0(sixSegDriver_4_out0), .Out1(sixSegDriver_4_out1),
    .Out2(sixSegDriver_4_out2), .Out3(sixSegDriver_4_out3), .Out4(sixSegDriver_4_out4),
    .Out5(sixSegDriver_4_out5));
  sixSegDriver sixSegDriver_6 (
    .dsp0(CHRONO_1_disp0), .dsp1(CHRONO_1_disp1), .dsp2(CHRONO_1_disp2), .dsp3(CHRONO_1_disp3),
    .dsp4(CHRONO_1_disp4), .dsp5(CHRONO_1_disp5), .Out0(sixSegDriver_6_out0), .Out1(sixSegDriver_6_out1),
    .Out2(sixSegDriver_6_out2), .Out3(sixSegDriver_6_out3), .Out4(sixSegDriver_6_out4),
    .Out5(sixSegDriver_6_out5));
  DISP_SEL DISP_SEL_1 (
    .HMS0(sixSegDriver_1_out0), .HMS1(sixSegDriver_1_out1), .HMS2(sixSegDriver_1_out2),
    .HMS3(sixSegDriver_1_out3), .HMS4(sixSegDriver_1_out4), .HMS5(sixSegDriver_1_out5),
    .chHMS0(sixSegDriver_2_out0), .chHMS1(sixSegDriver_2_out1), .chHMS2(sixSegDriver_2_out2),
    .chHMS3(sixSegDriver_2_out3), .chHMS4(sixSegDriver_2_out4), .chHMS5(sixSegDriver_2_out5),
    .alSet0(sixSegDriver_3_out0), .alSet1(sixSegDriver_3_out1), .alSet2(sixSegDriver_3_out2),
    .alSet3(sixSegDriver_3_out3), .alSet4(sixSegDriver_3_out4), .alSet5(sixSegDriver_3_out5),
    .tone0(sixSegDriver_4_out0), .tone1(sixSegDriver_4_out1), .tone2(sixSegDriver_4_out2),
    .tone3(sixSegDriver_4_out3), .tone4(sixSegDriver_4_out4), .tone5(sixSegDriver_4_out5),
    .game0(sixSegDriver_6_out0), .game1(sixSegDriver_6_out1), .game2(sixSegDriver_6_out2),
    .game3(sixSegDriver_6_out3), .game4(sixSegDriver_6_out4), .game5(sixSegDriver_6_out5),
    .disp0(DISP_SEL_1_disp0), .disp1(DISP_SEL_1_disp1), .disp2(DISP_SEL_1_disp2), .disp3(DISP_SEL_1_disp3),
    .disp4(DISP_SEL_1_disp4), .disp5(DISP_SEL_1_disp5));
  _7_Segment_Display L_7_Segment_Display_1 (
    .g(DISP_SEL_1_disp0[6]), .f(DISP_SEL_1_disp0[5]), .a(DISP_SEL_1_disp0[0]), .b(DISP_SEL_1_disp0[1]),
    .e(DISP_SEL_1_disp0[4]), .d(DISP_SEL_1_disp0[3]), .c(DISP_SEL_1_disp0[2]), .dp(DISP_SEL_1_disp0[7]));
  and and_6 (and_6_out, EN_AL, ~FUN_EN);  // AND_Gate
  or or_2 (or_2_out, and_6_out, FUN_LEDS[9]);
  LED LED_1 (.in(or_2_out));
  and and_7 (and_7_out, switch_chrono, ~FUN_EN);  // AND_Gate
  LED LED_2 (.in(or_3_out));
  or or_3 (or_3_out, and_7_out, FUN_LEDS[8]);
  _7_Segment_Display L_7_Segment_Display_2 (
    .g(DISP_SEL_1_disp1[6]), .f(DISP_SEL_1_disp1[5]), .a(DISP_SEL_1_disp1[0]), .b(DISP_SEL_1_disp1[1]),
    .e(DISP_SEL_1_disp1[4]), .d(DISP_SEL_1_disp1[3]), .c(DISP_SEL_1_disp1[2]), .dp(DISP_SEL_1_disp1[7]));
  LED LED_3 (.in(FUN_LEDS[7]));
  LED LED_4 (.in(FUN_LEDS[6]));
  _7_Segment_Display L_7_Segment_Display_4 (
    .g(DISP_SEL_1_disp3[6]), .f(DISP_SEL_1_disp3[5]), .a(DISP_SEL_1_disp3[0]), .b(DISP_SEL_1_disp3[1]),
    .e(DISP_SEL_1_disp3[4]), .d(DISP_SEL_1_disp3[3]), .c(DISP_SEL_1_disp3[2]), .dp(DISP_SEL_1_disp3[7]));
  _7_Segment_Display L_7_Segment_Display_3 (
    .g(DISP_SEL_1_disp2[6]), .f(DISP_SEL_1_disp2[5]), .a(DISP_SEL_1_disp2[0]), .b(DISP_SEL_1_disp2[1]),
    .e(DISP_SEL_1_disp2[4]), .d(DISP_SEL_1_disp2[3]), .c(DISP_SEL_1_disp2[2]), .dp(DISP_SEL_1_disp2[7]));
  LED LED_6 (.in(FUN_LEDS[4]));
  LED LED_5 (.in(FUN_LEDS[5]));
  _7_Segment_Display L_7_Segment_Display_5 (
    .g(DISP_SEL_1_disp4[6]), .f(DISP_SEL_1_disp4[5]), .a(DISP_SEL_1_disp4[0]), .b(DISP_SEL_1_disp4[1]),
    .e(DISP_SEL_1_disp4[4]), .d(DISP_SEL_1_disp4[3]), .c(DISP_SEL_1_disp4[2]), .dp(DISP_SEL_1_disp4[7]));
  LED LED_8 (.in(FUN_LEDS[2]));
  LED LED_7 (.in(FUN_LEDS[3]));
  _7_Segment_Display L_7_Segment_Display_6 (
    .g(DISP_SEL_1_disp5[6]), .f(DISP_SEL_1_disp5[5]), .a(DISP_SEL_1_disp5[0]), .b(DISP_SEL_1_disp5[1]),
    .e(DISP_SEL_1_disp5[4]), .d(DISP_SEL_1_disp5[3]), .c(DISP_SEL_1_disp5[2]), .dp(DISP_SEL_1_disp5[7]));
  or or_4 (or_4_out, FUN_LEDS[0], BUZZER);
  LED LED_10 (.in(or_4_out));
  LED LED_9 (.in(FUN_LEDS[1]));

  assign gnd = 1'b0;
  assign vcc = 1'b1;

  // Other names for the same wires on the sheet: buzz = BUZZER

  // Notes on the sheet:
  //   (disp0 : gauche)
endmodule

module segDriver (
  input  B5,
  input  B4,
  input  B3,
  input  B2,
  input  B1,
  input  B0,
  output a,
  output b,
  output c,
  output d,
  output e,
  output f,
  output g,
  output decimal
);

  wire nand_1_out, nand_2_out, nand_3_out, nand_4_out, nand_5_out, nand_6_out, nand_7_out, nand_8_out,
       nand_9_out, nand_10_out, nand_11_out, nand_12_out, nand_13_out, nand_14_out, nand_15_out, nand_16_out,
       nand_17_out, nand_18_out, nand_19_out, nand_20_out, nand_21_out, nand_22_out, nand_23_out,
       nand_24_out, nand_25_out, nand_26_out, nand_27_out, nand_28_out, nand_29_out, nand_30_out,
       nand_31_out, nand_32_out, nand_33_out, nand_34_out, nand_35_out, nand_36_out, nand_37_out,
       nand_38_out, nand_39_out, nand_40_out, nand_41_out, nand_42_out, nand_43_out, nand_44_out,
       nand_45_out, nand_46_out, nand_47_out, nand_48_out, nand_49_out, nand_50_out, nand_51_out,
       nand_52_out, nand_53_out, nand_54_out, nand_55_out, nand_56_out, nand_57_out, nand_58_out,
       nand_59_out, nand_60_out, nand_61_out, nand_62_out, nand_63_out, nand_64_out, nand_65_out,
       nand_66_out, nand_67_out, nand_68_out, nand_69_out, nand_70_out, nand_71_out, nand_72_out,
       nand_73_out, nand_74_out, nand_75_out, nand_76_out, nand_77_out, nand_78_out, nand_79_out,
       nand_80_out, nand_81_out, nand_82_out, nand_83_out, nand_84_out, nand_85_out, nand_86_out,
       nand_87_out, nand_88_out, nand_89_out, nand_90_out, nand_91_out, nand_92_out, nand_93_out,
       nand_94_out, nand_95_out, nand_96_out, nand_97_out, nand_98_out, nand_99_out, nand_100_out,
       nand_101_out, nand_102_out, nand_103_out, nand_104_out, nand_105_out, nand_106_out, nand_107_out,
       nand_108_out, nand_109_out, nand_110_out, nand_111_out, nand_112_out, nand_113_out, nand_114_out,
       nand_115_out, nand_116_out, nand_117_out, nand_118_out, nand_119_out, nand_120_out, nand_121_out,
       nand_122_out, nand_123_out, nand_124_out, nand_125_out, nand_126_out, nand_127_out, nand_128_out,
       nand_129_out, nand_130_out, nand_131_out, nand_132_out, nand_133_out, nand_134_out, nand_135_out,
       nand_136_out, nand_137_out, nand_138_out, nand_139_out, nand_140_out, nand_141_out, nand_142_out,
       nand_143_out, nand_144_out, nand_145_out, nand_146_out, nand_147_out, nand_148_out, nand_149_out,
       nand_150_out, nand_151_out, nand_152_out, nand_153_out, nand_154_out, nand_155_out, nand_156_out,
       nand_157_out, nand_158_out, nand_159_out, nand_160_out, nand_161_out, nand_162_out, nand_163_out,
       nand_164_out, nand_165_out, nand_166_out, nand_167_out, nand_168_out;

  nand nand_1 (nand_1_out, B2, B2);
  nand nand_2 (nand_2_out, B1, B1);
  nand nand_3 (nand_3_out, B0, B0);
  nand nand_4 (nand_4_out, B4, B4);
  nand nand_5 (nand_5_out, B3, B3);
  nand nand_6 (nand_6_out, B4, B4);
  nand nand_7 (nand_7_out, B3, B3);
  nand nand_8 (nand_8_out, B4, B4);
  nand nand_9 (nand_9_out, B3, B3);
  nand nand_10 (nand_10_out, B4, B4);
  nand nand_11 (nand_11_out, B2, B2);
  nand nand_12 (nand_12_out, B1, B1);
  nand nand_13 (nand_13_out, B4, B4);
  nand nand_14 (nand_14_out, B0, B0);
  nand nand_15 (nand_15_out, B2, B2);
  nand nand_16 (nand_16_out, B0, B0);
  nand nand_17 (nand_17_out, B4, B4);
  nand nand_18 (nand_18_out, B3, B3);
  nand nand_19 (nand_19_out, B1, B1);
  nand nand_20 (nand_20_out, B0, B0);
  nand nand_21 (nand_21_out, B4, B4);
  nand nand_22 (nand_22_out, B2, B2);
  nand nand_23 (nand_23_out, B0, B0);
  nand nand_24 (nand_24_out, B3, B3);
  nand nand_25 (nand_25_out, B2, B2);
  nand nand_26 (nand_26_out, B3, B3);
  nand nand_27 (nand_27_out, B4, B4);
  nand nand_28 (nand_28_out, B1, B1);
  nand nand_29 (nand_29_out, B1, B1);
  nand nand_30 (nand_30_out, B0, B0);
  nand nand_31 (nand_31_out, B1, B1);
  nand nand_32 (nand_32_out, B4, B4);
  nand nand_33 (nand_33_out, B3, B3);
  nand nand_34 (nand_34_out, B1, B1);
  nand nand_35 (nand_35_out, B4, B4);
  nand nand_36 (nand_36_out, B3, B3);
  nand nand_37 (nand_37_out, B4, B4);
  nand nand_38 (nand_38_out, B3, B3);
  nand nand_39 (nand_39_out, B1, B1);
  nand nand_40 (nand_40_out, B4, B4);
  nand nand_41 (nand_41_out, B2, B2);
  nand nand_42 (nand_42_out, B3, B3);
  nand nand_43 (nand_43_out, B2, B2);
  nand nand_44 (nand_44_out, B2, B2);
  nand nand_45 (nand_45_out, B0, B0);
  nand nand_46 (nand_46_out, B3, B3);
  nand nand_47 (nand_47_out, B0, B0);
  nand nand_48 (nand_48_out, B1, B1);
  nand nand_49 (nand_49_out, B0, B0);
  nand nand_50 (nand_50_out, B4, B4);
  nand nand_51 (nand_51_out, B3, B3);
  nand nand_52 (nand_52_out, B2, B2);
  nand nand_53 (nand_53_out, B0, B0);
  nand nand_54 (nand_54_out, B3, B3);
  nand nand_55 (nand_55_out, B2, B2);
  nand nand_56 (nand_56_out, B4, B4);
  nand nand_57 (nand_57_out, B1, B1);
  nand nand_58 (nand_58_out, B4, B4);
  nand nand_59 (nand_59_out, B0, B0);
  nand nand_60 (nand_60_out, B4, B4);
  nand nand_61 (nand_61_out, B1, B1);
  nand nand_62 (nand_62_out, B4, B4);
  nand nand_63 (nand_63_out, B2, B2);
  nand nand_64 (nand_64_out, B1, B1);
  nand nand_65 (nand_65_out, B3, B3);
  nand nand_66 (nand_66_out, B1, B1);
  nand nand_67 (nand_67_out, B0, B0);
  nand nand_68 (nand_68_out, B3, B3);
  nand nand_69 (nand_69_out, B0, B0);
  nand nand_70 (nand_70_out, B2, B2);
  nand nand_71 (nand_71_out, B0, B0);
  nand nand_72 (nand_72_out, B4, B4);
  nand nand_73 (nand_73_out, B2, B2);
  nand nand_74 (nand_74_out, B0, B0);
  nand nand_75 (nand_75_out, B4, B4);
  nand nand_76 (nand_76_out, B0, B0);
  nand nand_77 (nand_77_out, B4, B4);
  nand nand_78 (nand_78_out, B4, B4);
  nand nand_79 (nand_79_out, B2, B2);
  nand nand_80 (nand_80_out, B3, B3);
  nand nand_81 (nand_81_out, B1, B1);
  nand nand_82 (nand_82_out, B0, B0);
  nand nand_83 (nand_83_out, B1, B1);
  nand nand_84 (nand_84_out, B0, B0);
  nand nand_85 (nand_85_out, B4, B4);
  nand nand_86 (nand_86_out, B3, B3);
  nand nand_87 (nand_87_out, B1, B1);
  nand nand_88 (nand_88_out, B4, B4);
  nand nand_89 (nand_89_out, B0, B0);
  nand nand_90 (nand_90_out, B4, B4);
  nand nand_91 (nand_91_out, B2, B2);
  nand nand_92 (nand_92_out, B4, B4);
  nand nand_93 (nand_93_out, B2, B2);
  nand nand_94 (nand_94_out, B3, B3);
  nand nand_95 (nand_95_out, B2, B2);
  nand nand_96 (nand_96_out, B1, B1);
  nand nand_97 (nand_97_out, B3, B3);
  nand nand_98 (nand_98_out, B1, B1);
  nand nand_99 (nand_99_out, B4, B4);
  nand nand_100 (nand_100_out, B2, B2);
  nand nand_101 (nand_101_out, B4, B4);
  nand nand_102 (nand_102_out, B3, B3);
  nand nand_103 (nand_103_out, B1, B1);
  nand nand_104 (nand_104_out, B1, B1);
  nand nand_105 (nand_105_out, B0, B0);
  nand nand_106 (nand_106_out, B2, B2);
  nand nand_107 (nand_107_out, B4, B4);
  nand nand_108 (nand_108_out, B2, B2);
  nand nand_109 (nand_109_out, B1, B1);
  nand nand_110 (nand_110_out, B3, B3);
  nand nand_111 (nand_111_out, nand_1_out, nand_2_out, nand_3_out);
  nand nand_112 (nand_112_out, nand_4_out, nand_5_out, B1);
  nand nand_113 (nand_113_out, nand_6_out, nand_7_out, B2, B0);
  nand nand_114 (nand_114_out, nand_8_out, B2, B1);
  nand nand_115 (nand_115_out, nand_9_out, B2, B1, B0);
  nand nand_116 (nand_116_out, nand_10_out, B3, nand_11_out, nand_12_out);
  nand nand_117 (nand_117_out, nand_13_out, B3, nand_14_out);
  nand nand_118 (nand_118_out, B3, nand_15_out, nand_16_out);
  nand nand_119 (nand_119_out, nand_17_out, nand_18_out, nand_19_out, nand_20_out);
  nand nand_120 (nand_120_out, nand_21_out, nand_22_out, nand_23_out);
  nand nand_121 (nand_121_out, nand_24_out, nand_25_out);
  nand nand_122 (nand_122_out, nand_26_out, B1, B0);
  nand nand_123 (nand_123_out, nand_27_out, B3, nand_28_out, B0);
  nand nand_124 (nand_124_out, B4, B3, nand_29_out, nand_30_out);
  nand nand_125 (nand_125_out, B4, B3, B2, nand_31_out);
  nand nand_126 (nand_126_out, nand_32_out, nand_33_out, nand_34_out);
  nand nand_127 (nand_127_out, nand_35_out, nand_36_out, B0);
  nand nand_128 (nand_128_out, nand_37_out, nand_38_out, B2);
  nand nand_129 (nand_129_out, B2, nand_39_out, B0);
  nand nand_130 (nand_130_out, nand_40_out, B3, nand_41_out);
  nand nand_131 (nand_131_out, B4, nand_42_out, nand_43_out);
  nand nand_132 (nand_132_out, B4, nand_44_out, nand_45_out);
  nand nand_133 (nand_133_out, B4, nand_46_out, B1, nand_47_out);
  nand nand_134 (nand_134_out, B4, B3, nand_48_out, nand_49_out);
  nand nand_135 (nand_135_out, nand_50_out, nand_51_out, nand_52_out, nand_53_out);
  nand nand_136 (nand_136_out, nand_54_out, nand_55_out, B1, B0);
  nand nand_137 (nand_137_out, nand_56_out, B2, nand_57_out, B0);
  nand nand_138 (nand_138_out, nand_58_out, B2, B1, nand_59_out);
  nand nand_139 (nand_139_out, nand_60_out, B3, nand_61_out);
  nand nand_140 (nand_140_out, nand_62_out, B3, nand_63_out, B0);
  nand nand_141 (nand_141_out, B3, B2, nand_64_out);
  nand nand_142 (nand_142_out, B4, nand_65_out, nand_66_out, nand_67_out);
  nand nand_143 (nand_143_out, B4, nand_68_out, B2, nand_69_out);
  nand nand_144 (nand_144_out, B4, B3, nand_70_out, B1, nand_71_out);
  nand nand_145 (nand_145_out, nand_72_out, nand_73_out, nand_74_out);
  nand nand_146 (nand_146_out, nand_75_out, B1, nand_76_out);
  nand nand_147 (nand_147_out, nand_77_out, B3, B1);
  nand nand_148 (nand_148_out, nand_78_out, B3, B2);
  nand nand_149 (nand_149_out, B4, nand_79_out, B0);
  nand nand_150 (nand_150_out, B4, nand_80_out, B2);
  nand nand_151 (nand_151_out, B4, B2, nand_81_out, nand_82_out);
  nand nand_152 (nand_152_out, nand_83_out, nand_84_out);
  nand nand_153 (nand_153_out, nand_85_out, nand_86_out, B2, nand_87_out);
  nand nand_154 (nand_154_out, nand_88_out, B2, nand_89_out);
  nand nand_155 (nand_155_out, nand_90_out, B3, nand_91_out);
  nand nand_156 (nand_156_out, nand_92_out, B3, B1);
  nand nand_157 (nand_157_out, B3, nand_93_out, B1);
  nand nand_158 (nand_158_out, B4, nand_94_out, nand_95_out, nand_96_out);
  nand nand_159 (nand_159_out, B4, nand_97_out, B2, B1, B0);
  nand nand_160 (nand_160_out, B4, B3, B2, nand_98_out);
  nand nand_161 (nand_161_out, nand_99_out, nand_100_out, B1);
  nand nand_162 (nand_162_out, nand_101_out, nand_102_out, B2, nand_103_out);
  nand nand_163 (nand_163_out, B2, nand_104_out, B0);
  nand nand_164 (nand_164_out, B2, B1, nand_105_out);
  nand nand_165 (nand_165_out, B3, nand_106_out);
  nand nand_166 (nand_166_out, nand_107_out, B3, B1);
  nand nand_167 (nand_167_out, B4, nand_108_out, nand_109_out);
  nand nand_168 (nand_168_out, B4, nand_110_out, B2, B1);
  nand nand_169 (a, nand_111_out, nand_112_out, nand_113_out, nand_114_out, nand_115_out, nand_116_out, nand_117_out, nand_118_out);
  nand nand_170 (b, nand_119_out, nand_120_out, nand_121_out, nand_122_out, nand_123_out, nand_124_out, nand_125_out);
  nand nand_171 (c, nand_126_out, nand_127_out, nand_128_out, nand_129_out, nand_130_out, nand_131_out, nand_132_out, nand_133_out, nand_134_out);
  nand nand_172 (d, nand_135_out, nand_136_out, nand_137_out, nand_138_out, nand_139_out, nand_140_out, nand_141_out, nand_142_out, nand_143_out, nand_144_out);
  nand nand_173 (e, nand_145_out, nand_146_out, nand_147_out, nand_148_out, nand_149_out, nand_150_out, nand_151_out);
  nand nand_174 (f, nand_152_out, nand_153_out, nand_154_out, nand_155_out, nand_156_out, nand_157_out, nand_158_out, nand_159_out, nand_160_out);
  nand nand_175 (g, nand_161_out, nand_162_out, nand_163_out, nand_164_out, nand_165_out, nand_166_out, nand_167_out, nand_168_out);

  assign decimal = B5;
endmodule

module sixSegDriver (
  input  [5:0] dsp0,
  input  [5:0] dsp1,
  input  [5:0] dsp2,
  input  [5:0] dsp3,
  input  [5:0] dsp4,
  input  [5:0] dsp5,
  output [7:0] Out0,
  output [7:0] Out1,
  output [7:0] Out2,
  output [7:0] Out3,
  output [7:0] Out4,
  output [7:0] Out5
);

  segDriverSplit segDriverSplit_1 (.segIn(dsp0), .segOut(Out0));
  segDriverSplit segDriverSplit_2 (.segIn(dsp1), .segOut(Out1));
  segDriverSplit segDriverSplit_3 (.segIn(dsp2), .segOut(Out2));
  segDriverSplit segDriverSplit_4 (.segIn(dsp3), .segOut(Out3));
  segDriverSplit segDriverSplit_5 (.segIn(dsp4), .segOut(Out4));
  segDriverSplit segDriverSplit_6 (.segIn(dsp5), .segOut(Out5));
endmodule

module segDriverSplit (
  input  [5:0] segIn,
  output [7:0] segOut
);

  segDriver segDriver_1 (
    .B5(segIn[5]), .B4(segIn[4]), .B3(segIn[3]), .B2(segIn[2]), .B1(segIn[1]), .B0(segIn[0]), .a(segOut[0]),
    .b(segOut[1]), .c(segOut[2]), .d(segOut[3]), .e(segOut[4]), .f(segOut[5]), .g(segOut[6]),
    .decimal(segOut[7]));
endmodule

module base_60_count (
  input  RST,
  input  UP_DN,
  input  CIN,
  input  SET,
  input  [5:0] SVAL,
  output COUT,
  output [5:0] VAL
);

  wire clock_1_out, counter_1_carry, d_ff_1_qn, d_ff_2_q, d_ff_3_q, detect_neg_edge_1_neg_edge, or_1_out;

  Clock clock_1 (.out(clock_1_out));
  D_Flip_Flop d_ff_1 (.D(UP_DN), .clk(clock_1_out), .Qn(d_ff_1_qn));  // open: Q, preset, reset
  D_Flip_Flop d_ff_2 (.D(CIN), .clk(clock_1_out), .Q(d_ff_2_q));  // open: Qn, preset, reset
  D_Flip_Flop d_ff_3 (.D(SET), .clk(clock_1_out), .Q(d_ff_3_q));  // open: Qn, preset, reset
  or or_1 (or_1_out, d_ff_2_q, d_ff_3_q);
  Counter #(.width(6), .max('h3b)) counter_1 (
    .clr(RST), .load(d_ff_3_q), .up(d_ff_1_qn), .clk(or_1_out), .D(SVAL), .carry(counter_1_carry), .Q(VAL));  // open: count
  detect_neg_edge detect_neg_edge_1 (.in_in(counter_1_carry), .clk(clock_1_out), .neg_edge(detect_neg_edge_1_neg_edge));
  D_Flip_Flop d_ff_4 (.D(detect_neg_edge_1_neg_edge), .clk(clock_1_out), .Q(COUT), .reset(RST));  // open: Qn, preset
endmodule

module base_24_count (
  input  RST,
  input  UP_DN,
  input  CIN,
  input  SET,
  input  [5:0] SVAL,
  output COUT,
  output [5:0] VAL
);

  wire clock_1_out, counter_1_carry, d_ff_1_q, d_ff_2_q, d_ff_3_q, detect_neg_edge_1_neg_edge, not_1_out,
       or_1_out;

  Clock clock_1 (.out(clock_1_out));
  D_Flip_Flop d_ff_1 (.D(UP_DN), .clk(clock_1_out), .Q(d_ff_1_q));  // open: Qn, preset, reset
  D_Flip_Flop d_ff_2 (.D(CIN), .clk(clock_1_out), .Q(d_ff_2_q));  // open: Qn, preset, reset
  D_Flip_Flop d_ff_3 (.D(SET), .clk(clock_1_out), .Q(d_ff_3_q));  // open: Qn, preset, reset
  not not_1 (not_1_out, d_ff_1_q);
  or or_1 (or_1_out, d_ff_2_q, d_ff_3_q);
  Counter #(.width(6), .max('h17)) counter_1 (
    .clr(RST), .load(d_ff_3_q), .up(not_1_out), .clk(or_1_out), .D(SVAL), .carry(counter_1_carry), .Q(VAL));  // open: count
  detect_neg_edge detect_neg_edge_1 (.in_in(counter_1_carry), .clk(clock_1_out), .neg_edge(detect_neg_edge_1_neg_edge));
  D_Flip_Flop d_ff_4 (.D(detect_neg_edge_1_neg_edge), .clk(clock_1_out), .Q(COUT), .reset(RST));  // open: Qn, preset
endmodule

module HMS24 (
  input  EN,
  input  SYS_CLK,
  input  RST,
  input  UP_DN,
  input  CLK,
  input  SET,
  input  [5:0] h0_set,
  input  [5:0] m0_set,
  input  [5:0] s0_set,
  output [5:0] HMS5,
  output [5:0] HMS4,
  output [5:0] HOURS_B,
  output [5:0] HMS3,
  output [5:0] HMS2,
  output [5:0] MINS_B,
  output [5:0] HMS1,
  output [5:0] SECS_B,
  output [5:0] HMS0
);

  wire and_1_out, base_24_count_1_cout, base_60_count_1_cout, base_60_count_2_cout, or_1_out;
  wire [1:0] txtFSM_1_txt;
  wire [5:0] decod_tens_units_1_tens, decod_tens_units_1_unites, decod_tens_units_2_tens,
       decod_tens_units_2_unites, decod_tens_units_3_tens, decod_tens_units_3_unites,
       tDispTxt_1_output_bus_1, tDispTxt_1_output_bus_2, tDispTxt_1_output_bus_3, tDispTxt_1_output_bus_4,
       tDispTxt_1_output_bus_5, tDispTxt_1_output_bus_6;

  or or_1 (or_1_out, RST, and_1_out);
  and and_1 (and_1_out, base_24_count_1_cout, ~SET);  // AND_Gate
  txtFSM txtFSM_1 (.EN(EN), .CLK(SYS_CLK), .TXT(txtFSM_1_txt));
  base_24_count base_24_count_1 (
    .RST(or_1_out), .UP_DN(UP_DN), .CIN(base_60_count_1_cout), .SET(SET), .SVAL(h0_set),
    .COUT(base_24_count_1_cout), .VAL(HOURS_B));
  base_60_count base_60_count_1 (
    .RST(or_1_out), .UP_DN(UP_DN), .CIN(base_60_count_2_cout), .SET(SET), .SVAL(m0_set),
    .COUT(base_60_count_1_cout), .VAL(MINS_B));
  base_60_count base_60_count_2 (
    .RST(or_1_out), .UP_DN(UP_DN), .CIN(CLK), .SET(SET), .SVAL(s0_set), .COUT(base_60_count_2_cout),
    .VAL(SECS_B));
  tDispTxt tDispTxt_1 (
    .Output_bus_1(tDispTxt_1_output_bus_1), .Output_bus_2(tDispTxt_1_output_bus_2),
    .Output_bus_3(tDispTxt_1_output_bus_3), .Output_bus_4(tDispTxt_1_output_bus_4),
    .Output_bus_5(tDispTxt_1_output_bus_5), .Output_bus_6(tDispTxt_1_output_bus_6));
  decod_tens_units decod_tens_units_1 (
    .nb_in(HOURS_B), .tens(decod_tens_units_1_tens), .unites(decod_tens_units_1_unites));
  decod_tens_units decod_tens_units_2 (
    .nb_in(MINS_B), .tens(decod_tens_units_2_tens), .unites(decod_tens_units_2_unites));
  decod_tens_units decod_tens_units_3 (
    .nb_in(SECS_B), .tens(decod_tens_units_3_tens), .unites(decod_tens_units_3_unites));
  Multiplexer #(.select(2), .width(6), .enable("false")) multiplexer_1 (
    .in0(6'b011111), .in1(tDispTxt_1_output_bus_1), .in2(decod_tens_units_1_tens),
    .in3(decod_tens_units_1_tens), .out(HMS5), .sel(txtFSM_1_txt));
  Multiplexer #(.select(2), .width(6), .enable("false")) multiplexer_2 (
    .in0(6'b011111), .in1(tDispTxt_1_output_bus_2), .in2(decod_tens_units_1_unites),
    .in3(decod_tens_units_1_unites), .out(HMS4), .sel(txtFSM_1_txt));
  Multiplexer #(.select(2), .width(6), .enable("false")) multiplexer_3 (
    .in0(6'b011111), .in1(tDispTxt_1_output_bus_3), .in2(decod_tens_units_2_tens),
    .in3(decod_tens_units_2_tens), .out(HMS3), .sel(txtFSM_1_txt));
  Multiplexer #(.select(2), .width(6), .enable("false")) multiplexer_4 (
    .in0(6'b011111), .in1(tDispTxt_1_output_bus_4), .in2(decod_tens_units_2_unites),
    .in3(decod_tens_units_2_unites), .out(HMS2), .sel(txtFSM_1_txt));
  Multiplexer #(.select(2), .width(6), .enable("false")) multiplexer_5 (
    .in0(6'b011111), .in1(tDispTxt_1_output_bus_5), .in2(decod_tens_units_3_tens),
    .in3(decod_tens_units_3_tens), .out(HMS1), .sel(txtFSM_1_txt));
  Multiplexer #(.select(2), .width(6), .enable("false")) multiplexer_6 (
    .in0(6'b011111), .in1(tDispTxt_1_output_bus_6), .in2(decod_tens_units_3_unites),
    .in3(decod_tens_units_3_unites), .out(HMS0), .sel(txtFSM_1_txt));
endmodule

module base_100_count (
  input  RST,
  input  UP_ND,
  input  CIN,
  input  SET,
  input  [5:0] SVAL,
  output COUT,
  output [5:0] VAL
);

  wire clock_1_out, counter_1_carry, d_ff_1_qn, d_ff_2_q, d_ff_3_q, detect_neg_edge_1_neg_edge, or_1_out;

  Clock clock_1 (.out(clock_1_out));
  D_Flip_Flop d_ff_1 (.D(UP_ND), .clk(clock_1_out), .Qn(d_ff_1_qn));  // open: Q, preset, reset
  D_Flip_Flop d_ff_2 (.D(CIN), .clk(clock_1_out), .Q(d_ff_2_q));  // open: Qn, preset, reset
  D_Flip_Flop d_ff_3 (.D(SET), .clk(clock_1_out), .Q(d_ff_3_q));  // open: Qn, preset, reset
  or or_1 (or_1_out, d_ff_2_q, d_ff_3_q);
  Counter #(.width(6), .max('h23)) counter_1 (
    .clr(RST), .load(d_ff_3_q), .up(d_ff_1_qn), .clk(or_1_out), .D(SVAL), .carry(counter_1_carry), .Q(VAL));  // open: count
  detect_neg_edge detect_neg_edge_1 (.in_in(counter_1_carry), .clk(clock_1_out), .neg_edge(detect_neg_edge_1_neg_edge));
  D_Flip_Flop d_ff_4 (.D(detect_neg_edge_1_neg_edge), .clk(clock_1_out), .Q(COUT), .reset(RST));  // open: Qn, preset
endmodule

module sixteen_count (
  input  RST,
  input  UP_DN,
  input  CIN,
  input  SET,
  input  [3:0] SVAL,
  output COUT,
  output [3:0] VAL
);

  wire counter_1_carry, not_1_out, or_1_out;

  not not_1 (not_1_out, UP_DN);
  or or_1 (or_1_out, CIN, SET);
  Counter #(.width(4), .max('h0)) counter_1 (
    .clr(RST), .load(SET), .up(not_1_out), .clk(or_1_out), .D(SVAL), .carry(counter_1_carry), .Q(VAL));  // open: count
  D_Flip_Flop d_ff_1 (.D(counter_1_carry), .clk(or_1_out), .Q(COUT), .reset(RST));  // open: Qn, preset
endmodule

module clk_div (
  input  CLK_IN,
  input  [3:0] CLK_SEL,
  output CLK_OUT
);

  wire d_ff_1_q, d_ff_1_qn, d_ff_2_q, d_ff_2_qn, d_ff_3_q, d_ff_3_qn, d_ff_4_q, d_ff_4_qn, d_ff_5_q,
       d_ff_5_qn, d_ff_6_q, d_ff_6_qn, d_ff_7_q, d_ff_7_qn, d_ff_8_q, d_ff_8_qn, d_ff_9_q, d_ff_9_qn,
       d_ff_10_q, d_ff_10_qn, not_1_out;

  not not_1 (not_1_out, CLK_IN);
  D_Flip_Flop d_ff_1 (.D(d_ff_1_qn), .clk(CLK_IN), .Q(d_ff_1_q), .Qn(d_ff_1_qn));  // open: preset, reset
  D_Flip_Flop d_ff_2 (.D(d_ff_2_qn), .clk(d_ff_1_qn), .Q(d_ff_2_q), .Qn(d_ff_2_qn));  // open: preset, reset
  D_Flip_Flop d_ff_3 (.D(d_ff_3_qn), .clk(d_ff_2_qn), .Q(d_ff_3_q), .Qn(d_ff_3_qn));  // open: preset, reset
  D_Flip_Flop d_ff_4 (.D(d_ff_4_qn), .clk(d_ff_3_qn), .Q(d_ff_4_q), .Qn(d_ff_4_qn));  // open: preset, reset
  D_Flip_Flop d_ff_5 (.D(d_ff_5_qn), .clk(d_ff_4_qn), .Q(d_ff_5_q), .Qn(d_ff_5_qn));  // open: preset, reset
  D_Flip_Flop d_ff_6 (.D(d_ff_6_qn), .clk(d_ff_5_qn), .Q(d_ff_6_q), .Qn(d_ff_6_qn));  // open: preset, reset
  D_Flip_Flop d_ff_7 (.D(d_ff_7_qn), .clk(d_ff_6_qn), .Q(d_ff_7_q), .Qn(d_ff_7_qn));  // open: preset, reset
  D_Flip_Flop d_ff_8 (.D(d_ff_8_qn), .clk(d_ff_7_qn), .Q(d_ff_8_q), .Qn(d_ff_8_qn));  // open: preset, reset
  D_Flip_Flop d_ff_9 (.D(d_ff_9_qn), .clk(d_ff_8_qn), .Q(d_ff_9_q), .Qn(d_ff_9_qn));  // open: preset, reset
  D_Flip_Flop d_ff_10 (.D(d_ff_10_qn), .clk(d_ff_9_qn), .Q(d_ff_10_q), .Qn(d_ff_10_qn));  // open: preset, reset
  Multiplexer #(.select(4), .enable("false")) multiplexer_1 (
    .in0(not_1_out), .in1(d_ff_1_q), .in2(d_ff_2_q), .in3(d_ff_3_q), .in4(d_ff_4_q), .in5(d_ff_5_q),
    .in6(d_ff_6_q), .in7(d_ff_7_q), .in8(d_ff_8_q), .in9(d_ff_9_q), .in10(d_ff_10_q), .in11(d_ff_10_q),
    .in12(d_ff_10_q), .in13(d_ff_10_q), .in14(d_ff_10_q), .in15(d_ff_10_q), .out(CLK_OUT), .sel(CLK_SEL));
endmodule

module FSM (
  input  Bfwd,
  input  BBack,
  input  CIN,
  output [2:0] SEL
);

  wire d_ff_3_q, FSM_transition_1_out0, FSM_transition_1_out1, FSM_transition_1_out2, FSM_transition_1_out3;

  FSM_transition FSM_transition_1 (
    .in3(d_ff_3_q), .in2(SEL[2]), .in1(SEL[1]), .in0(SEL[0]), .BFwd(Bfwd), .BBack(BBack),
    .out3(FSM_transition_1_out3), .out2(FSM_transition_1_out2), .out1(FSM_transition_1_out1),
    .out0(FSM_transition_1_out0));
  D_Flip_Flop d_ff_1 (.D(FSM_transition_1_out1), .clk(CIN), .Q(SEL[1]));  // open: Qn, preset, reset
  D_Flip_Flop d_ff_2 (.D(FSM_transition_1_out0), .clk(CIN), .Q(SEL[0]));  // open: Qn, preset, reset
  D_Flip_Flop d_ff_3 (.D(FSM_transition_1_out3), .clk(CIN), .Q(d_ff_3_q));  // open: Qn, preset, reset
  D_Flip_Flop d_ff_4 (.D(FSM_transition_1_out2), .clk(CIN), .Q(SEL[2]));  // open: Qn, preset, reset
endmodule

module FSM_transition (
  input  in3,
  input  in2,
  input  in1,
  input  in0,
  input  BFwd,
  input  BBack,
  output out3,
  output out2,
  output out1,
  output out0
);

  wire and_1_out, and_2_out, and_3_out, and_4_out, and_5_out, and_6_out, and_7_out, and_8_out, and_9_out,
       and_10_out, and_11_out, and_12_out, and_13_out, and_14_out, and_15_out, and_16_out, and_17_out,
       and_18_out, and_19_out, and_20_out, and_21_out, not_1_out, not_2_out, not_3_out, not_4_out, not_5_out,
       not_6_out, not_7_out, not_8_out, not_9_out, not_10_out, not_11_out, not_12_out, not_13_out,
       not_14_out, not_15_out, not_16_out, not_17_out, not_18_out, not_19_out, not_20_out, not_21_out,
       not_22_out, not_23_out, not_24_out, not_25_out, not_26_out, not_27_out, not_28_out, not_29_out,
       not_30_out, not_31_out, not_32_out, not_33_out, not_34_out, not_35_out, not_36_out, not_37_out,
       not_38_out, not_39_out, not_40_out, not_41_out, not_42_out, not_43_out, not_44_out, not_45_out,
       not_46_out, not_47_out, not_48_out, not_49_out, not_50_out, not_51_out, not_52_out, not_53_out,
       not_54_out, not_55_out, not_56_out, not_57_out, not_58_out, not_59_out, not_60_out, not_61_out,
       not_62_out, not_63_out, not_64_out, not_65_out, not_66_out;

  not not_1 (not_1_out, in3);
  not not_2 (not_2_out, in2);
  not not_3 (not_3_out, in1);
  not not_4 (not_4_out, in0);
  not not_5 (not_5_out, BFwd);
  not not_6 (not_6_out, in3);
  not not_7 (not_7_out, in2);
  not not_8 (not_8_out, BBack);
  not not_9 (not_9_out, in3);
  not not_10 (not_10_out, in1);
  not not_11 (not_11_out, BBack);
  not not_12 (not_12_out, in3);
  not not_13 (not_13_out, in0);
  not not_14 (not_14_out, in3);
  not not_15 (not_15_out, in1);
  not not_16 (not_16_out, in3);
  not not_17 (not_17_out, in0);
  not not_18 (not_18_out, BFwd);
  not not_19 (not_19_out, in3);
  not not_20 (not_20_out, in1);
  not not_21 (not_21_out, in0);
  not not_22 (not_22_out, BFwd);
  not not_23 (not_23_out, in3);
  not not_24 (not_24_out, in1);
  not not_25 (not_25_out, BBack);
  not not_26 (not_26_out, in3);
  not not_27 (not_27_out, in2);
  not not_28 (not_28_out, in0);
  not not_29 (not_29_out, BBack);
  not not_30 (not_30_out, in3);
  not not_31 (not_31_out, in0);
  not not_32 (not_32_out, BFwd);
  not not_33 (not_33_out, BBack);
  not not_34 (not_34_out, in3);
  not not_35 (not_35_out, in0);
  not not_36 (not_36_out, in3);
  not not_37 (not_37_out, in2);
  not not_38 (not_38_out, BFwd);
  not not_39 (not_39_out, in3);
  not not_40 (not_40_out, in2);
  not not_41 (not_41_out, in3);
  not not_42 (not_42_out, in2);
  not not_43 (not_43_out, in0);
  not not_44 (not_44_out, BBack);
  not not_45 (not_45_out, in3);
  not not_46 (not_46_out, in1);
  not not_47 (not_47_out, in0);
  not not_48 (not_48_out, BBack);
  not not_49 (not_49_out, in3);
  not not_50 (not_50_out, in2);
  not not_51 (not_51_out, BFwd);
  not not_52 (not_52_out, BBack);
  not not_53 (not_53_out, in3);
  not not_54 (not_54_out, in1);
  not not_55 (not_55_out, BFwd);
  not not_56 (not_56_out, BBack);
  not not_57 (not_57_out, in3);
  not not_58 (not_58_out, in2);
  not not_59 (not_59_out, in3);
  not not_60 (not_60_out, in1);
  not not_61 (not_61_out, in3);
  not not_62 (not_62_out, in0);
  not not_63 (not_63_out, BFwd);
  not not_64 (not_64_out, in3);
  not not_65 (not_65_out, in0);
  not not_66 (not_66_out, BFwd);
  and and_1 (and_1_out, not_1_out, not_2_out, not_3_out, not_4_out, not_5_out, BBack);
  and and_2 (and_2_out, not_6_out, not_7_out, in1, in0, BFwd, not_8_out);
  and and_3 (and_3_out, not_9_out, in2, not_10_out, not_11_out);
  and and_4 (and_4_out, not_12_out, in2, not_13_out, BFwd, BBack);
  and and_5 (and_5_out, not_14_out, in2, not_15_out, in0);
  and and_6 (and_6_out, not_16_out, in2, in1, not_17_out, not_18_out);
  and and_7 (and_7_out, not_19_out, not_20_out, not_21_out, not_22_out, BBack);
  and and_8 (and_8_out, not_23_out, not_24_out, in0, BFwd, not_25_out);
  and and_9 (and_9_out, not_26_out, not_27_out, in1, not_28_out, not_29_out);
  and and_10 (and_10_out, not_30_out, in1, not_31_out, not_32_out, not_33_out);
  and and_11 (and_11_out, not_34_out, in1, not_35_out, BFwd, BBack);
  and and_12 (and_12_out, not_36_out, not_37_out, in1, in0, not_38_out);
  and and_13 (and_13_out, not_39_out, not_40_out, in1, in0, BBack);
  and and_14 (and_14_out, not_41_out, not_42_out, not_43_out, BFwd, not_44_out);
  and and_15 (and_15_out, not_45_out, not_46_out, not_47_out, BFwd, not_48_out);
  and and_16 (and_16_out, not_49_out, not_50_out, in0, not_51_out, not_52_out);
  and and_17 (and_17_out, not_53_out, not_54_out, in0, not_55_out, not_56_out);
  and and_18 (and_18_out, not_57_out, not_58_out, in0, BFwd, BBack);
  and and_19 (and_19_out, not_59_out, not_60_out, in0, BFwd, BBack);
  and and_20 (and_20_out, not_61_out, in1, not_62_out, not_63_out, BBack);
  and and_21 (and_21_out, not_64_out, in2, not_65_out, not_66_out, BBack);
  or or_1 (out2, and_1_out, and_2_out, and_3_out, and_4_out, and_5_out, and_6_out);
  or or_2 (out1, and_7_out, and_8_out, and_9_out, and_10_out, and_11_out, and_12_out, and_13_out);
  or or_3 (out0, and_14_out, and_15_out, and_16_out, and_17_out, and_18_out, and_19_out, and_20_out, and_21_out);

  assign out3 = 1'b0;
endmodule

module display_MUX (
  input  [2:0] sel,
  input  [5:0] h0,
  input  [5:0] h1,
  input  [5:0] h2,
  input  [5:0] h3,
  input  [5:0] h4,
  input  [5:0] h5,
  input  [5:0] ch0,
  input  [5:0] ch1,
  input  [5:0] ch2,
  input  [5:0] ch3,
  input  [5:0] ch4,
  input  [5:0] ch5,
  input  [5:0] in_14,
  input  [5:0] in_15,
  input  [5:0] in_16,
  input  [5:0] in_17,
  input  [5:0] in_18,
  input  [5:0] in_19,
  input  [5:0] in_20,
  input  [5:0] in_21,
  input  [5:0] in_22,
  input  [5:0] in_23,
  input  [5:0] in_24,
  input  [5:0] in_25,
  input  [5:0] fgrd,
  input  [5:0] in_27,
  input  [5:0] in_28,
  input  [5:0] in_29,
  input  [5:0] in_30,
  input  [5:0] qqqqqq,
  input  [5:0] in_32,
  input  [5:0] in_33,
  input  [5:0] in_34,
  input  [5:0] in_35,
  input  [5:0] in_36,
  input  [5:0] in_37,
  input  [5:0] in_38,
  input  [5:0] in_39,
  input  [5:0] in_40,
  input  [5:0] in_41,
  input  [5:0] in_42,
  input  [5:0] in_43,
  output [5:0] out_44,
  output [5:0] out_45,
  output [5:0] out_46,
  output [5:0] out_47,
  output [5:0] out_48,
  output [5:0] out_49
);

  Multiplexer #(.select(3), .width(6), .enable("false")) multiplexer_1 (
    .in0(h5), .in1(ch5), .in2(in_19), .in3(in_25), .in4(qqqqqq), .in5(in_37), .in6(in_43), .out(out_44),
    .sel(sel));  // open: in7
  Multiplexer #(.select(3), .width(6), .enable("false")) multiplexer_2 (
    .in0(h4), .in1(ch4), .in2(in_18), .in3(in_24), .in4(in_30), .in5(in_36), .in6(in_42), .out(out_45),
    .sel(sel));  // open: in7
  Multiplexer #(.select(3), .width(6), .enable("false")) multiplexer_3 (
    .in0(h3), .in1(ch3), .in2(in_17), .in3(in_23), .in4(in_29), .in5(in_35), .in6(in_41), .out(out_46),
    .sel(sel));  // open: in7
  Multiplexer #(.select(3), .width(6), .enable("false")) multiplexer_4 (
    .in0(h2), .in1(ch2), .in2(in_16), .in3(in_22), .in4(in_28), .in5(in_34), .in6(in_40), .out(out_47),
    .sel(sel));  // open: in7
  Multiplexer #(.select(3), .width(6), .enable("false")) multiplexer_5 (
    .in0(h1), .in1(ch1), .in2(in_15), .in3(in_21), .in4(in_27), .in5(in_33), .in6(in_39), .out(out_48),
    .sel(sel));  // open: in7
  Multiplexer #(.select(3), .width(6), .enable("false")) multiplexer_6 (
    .in0(h0), .in1(ch0), .in2(in_14), .in3(in_20), .in4(fgrd), .in5(in_32), .in6(in_38), .out(out_49),
    .sel(sel));  // open: in7
endmodule

module DISP_SEL (
  input  [7:0] HMS0,
  input  [7:0] HMS1,
  input  [7:0] HMS2,
  input  [7:0] HMS3,
  input  [7:0] HMS4,
  input  [7:0] HMS5,
  input  [7:0] chHMS0,
  input  [7:0] chHMS1,
  input  [7:0] chHMS2,
  input  [7:0] chHMS3,
  input  [7:0] chHMS4,
  input  [7:0] chHMS5,
  input  [7:0] alSet0,
  input  [7:0] alSet1,
  input  [7:0] alSet2,
  input  [7:0] alSet3,
  input  [7:0] alSet4,
  input  [7:0] alSet5,
  input  [7:0] tone0,
  input  [7:0] tone1,
  input  [7:0] tone2,
  input  [7:0] tone3,
  input  [7:0] tone4,
  input  [7:0] tone5,
  input  [7:0] game0,
  input  [7:0] game1,
  input  [7:0] game2,
  input  [7:0] game3,
  input  [7:0] game4,
  input  [7:0] game5,
  output [7:0] disp0,
  output [7:0] disp1,
  output [7:0] disp2,
  output [7:0] disp3,
  output [7:0] disp4,
  output [7:0] disp5
);

  assign disp0 = HMS0 | chHMS0 | alSet0 | tone0 | game0;  // OR_Gate or_1, 8 bits wide
  assign disp1 = HMS1 | chHMS1 | alSet1 | tone1 | game1;  // OR_Gate or_2, 8 bits wide
  assign disp2 = HMS2 | chHMS2 | alSet2 | tone2 | game2;  // OR_Gate or_3, 8 bits wide
  assign disp3 = HMS3 | chHMS3 | alSet3 | tone3 | game3;  // OR_Gate or_4, 8 bits wide
  assign disp4 = HMS4 | chHMS4 | alSet4 | tone4 | game4;  // OR_Gate or_5, 8 bits wide
  assign disp5 = HMS5 | chHMS5 | alSet5 | tone5 | game5;  // OR_Gate or_6, 8 bits wide
endmodule

module Debounce (
  input  BTTN,
  input  CLK,
  output BTTN_OUT
);

  wire and_1_out, and_2_out, d_ff_1_q, d_ff_1_qn, d_ff_2_q, d_ff_2_qn, d_ff_3_q, d_ff_3_qn;

  D_Flip_Flop d_ff_1 (.D(BTTN), .clk(CLK), .Q(d_ff_1_q), .Qn(d_ff_1_qn));  // open: preset, reset
  D_Flip_Flop d_ff_2 (.D(d_ff_1_q), .clk(CLK), .Q(d_ff_2_q), .Qn(d_ff_2_qn));  // open: preset, reset
  D_Flip_Flop d_ff_3 (.D(d_ff_2_q), .clk(CLK), .Q(d_ff_3_q), .Qn(d_ff_3_qn));  // open: preset, reset
  D_Flip_Flop d_ff_4 (.D(d_ff_3_q), .clk(CLK));  // open: Q, Qn, preset, reset
  and and_1 (and_1_out, d_ff_1_q, d_ff_2_q, d_ff_3_q);
  S_R_Flip_Flop s_r_ff_1 (.Q(BTTN_OUT), .reset(and_2_out), .preset(and_1_out));  // open: S, R, clk, Qn
  and and_2 (and_2_out, d_ff_3_qn, d_ff_2_qn, d_ff_1_qn);
endmodule

module timer (
);

  base_60_count base_60_count_1 ();  // open: RST, UP_DN, CIN, SET, SVAL, COUT, VAL
  base_24_count base_24_count_1 ();  // open: RST, UP_DN, CIN, SET, SVAL, COUT, VAL
  base_60_count base_60_count_2 ();  // open: RST, UP_DN, CIN, SET, SVAL, COUT, VAL
  base_24_count base_24_count_2 ();  // open: RST, UP_DN, CIN, SET, SVAL, COUT, VAL
  base_24_count base_24_count_3 ();  // open: RST, UP_DN, CIN, SET, SVAL, COUT, VAL
  base_24_count base_24_count_4 ();  // open: RST, UP_DN, CIN, SET, SVAL, COUT, VAL
endmodule

module SET_HMS (
  input  EN,
  input  CLK,
  input  [5:0] h_in,
  input  [5:0] m_in,
  input  [5:0] s_in,
  input  UP,
  input  DOWN,
  input  CLICK,
  output set_hms,
  output [5:0] ch_hour,
  output [5:0] ch_min,
  output [5:0] ch_sec,
  output [5:0] chHMS5,
  output [5:0] chHMS4,
  output [5:0] chHMS3,
  output [5:0] chHMS2,
  output [5:0] chHMS1,
  output [5:0] chHMS0
);

  wire and_1_out, and_2_out, and_3_out, clk_div_1_clk_out, clock_2_out, demultiplexer_1_out0,
       demultiplexer_1_out1, demultiplexer_1_out2, demultiplexer_2_out0, demultiplexer_2_out1,
       demultiplexer_2_out2, demultiplexer_3_out0, demultiplexer_3_out1, demultiplexer_3_out2,
       detect_pos_edge_1_pos_edge, fsm_select_3_trans_1_s0, fsm_select_3_trans_1_s1, or_1_out, or_2_out,
       or_3_out;
  wire [1:0] select_3;
  wire [5:0] decod_tens_units_1_tens, decod_tens_units_1_unites, decod_tens_units_2_tens,
       decod_tens_units_2_unites, decod_tens_units_3_tens, decod_tens_units_3_unites;

  Clock clock_1 ();  // open: out
  Clock clock_2 (.out(clock_2_out));
  Demultiplexer #(.select(2), .enable("false")) demultiplexer_1 (
    .out0(demultiplexer_1_out0), .out1(demultiplexer_1_out1), .out2(demultiplexer_1_out2), .in(UP),
    .sel(select_3));  // open: out3
  Demultiplexer #(.select(2), .enable("false")) demultiplexer_2 (
    .out0(demultiplexer_2_out0), .out1(demultiplexer_2_out1), .out2(demultiplexer_2_out2), .in(DOWN),
    .sel(select_3));  // open: out3
  D_Flip_Flop d_ff_1 (.D(fsm_select_3_trans_1_s0), .clk(clock_2_out), .Q(select_3[0]));  // open: Qn, preset, reset
  fsm_select_3_trans fsm_select_3_trans_1 (
    .i0(select_3[0]), .i1(select_3[1]), .click(CLICK), .s0(fsm_select_3_trans_1_s0),
    .s1(fsm_select_3_trans_1_s1));
  D_Flip_Flop d_ff_2 (.D(fsm_select_3_trans_1_s1), .clk(clock_2_out), .Q(select_3[1]));  // open: Qn, preset, reset
  detect_pos_edge detect_pos_edge_1 (.in_in(EN), .clk(CLK), .pos_edge(detect_pos_edge_1_pos_edge));
  detect_neg_edge detect_neg_edge_1 (.in_in(EN), .clk(CLK), .neg_edge(set_hms));
  or or_1 (or_1_out, demultiplexer_1_out0, demultiplexer_2_out0);
  or or_2 (or_2_out, demultiplexer_1_out1, demultiplexer_2_out1);
  or or_3 (or_3_out, demultiplexer_1_out2, demultiplexer_2_out2);
  clk_div clk_div_1 (.CLK_IN(clock_2_out), .CLK_SEL(4'b1000), .CLK_OUT(clk_div_1_clk_out));
  base_24_count base_24_count_1 (
    .RST(1'b0), .UP_DN(demultiplexer_2_out0), .CIN(or_1_out), .SET(detect_pos_edge_1_pos_edge), .SVAL(h_in),
    .VAL(ch_hour));  // open: COUT
  base_60_count base_60_count_1 (
    .RST(1'b0), .UP_DN(demultiplexer_2_out1), .CIN(or_2_out), .SET(detect_pos_edge_1_pos_edge), .SVAL(m_in),
    .VAL(ch_min));  // open: COUT
  base_60_count base_60_count_2 (
    .RST(1'b0), .UP_DN(demultiplexer_2_out2), .CIN(or_3_out), .SET(detect_pos_edge_1_pos_edge), .SVAL(s_in),
    .VAL(ch_sec));  // open: COUT
  Demultiplexer #(.select(2), .enable("false")) demultiplexer_3 (
    .out0(demultiplexer_3_out0), .out1(demultiplexer_3_out1), .out2(demultiplexer_3_out2),
    .in(clk_div_1_clk_out), .sel(select_3));  // open: out3
  and and_1 (and_1_out, EN, ~demultiplexer_3_out0);  // AND_Gate
  and and_2 (and_2_out, EN, ~demultiplexer_3_out1);  // AND_Gate
  and and_3 (and_3_out, EN, ~demultiplexer_3_out2);  // AND_Gate
  decod_tens_units decod_tens_units_1 (
    .nb_in(ch_hour), .tens(decod_tens_units_1_tens), .unites(decod_tens_units_1_unites));
  decod_tens_units decod_tens_units_2 (
    .nb_in(ch_min), .tens(decod_tens_units_2_tens), .unites(decod_tens_units_2_unites));
  decod_tens_units decod_tens_units_3 (
    .nb_in(ch_sec), .tens(decod_tens_units_3_tens), .unites(decod_tens_units_3_unites));
  Multiplexer #(.width(6), .enable("false")) multiplexer_1 (
    .in0(6'b011111), .in1(decod_tens_units_1_tens), .out(chHMS5), .sel(and_1_out));
  Multiplexer #(.width(6), .enable("false")) multiplexer_2 (
    .in0(6'b011111), .in1(decod_tens_units_1_unites), .out(chHMS4), .sel(and_1_out));
  Multiplexer #(.width(6), .enable("false")) multiplexer_3 (
    .in0(6'b011111), .in1(decod_tens_units_2_tens), .out(chHMS3), .sel(and_2_out));
  Multiplexer #(.width(6), .enable("false")) multiplexer_4 (
    .in0(6'b011111), .in1(decod_tens_units_2_unites), .out(chHMS2), .sel(and_2_out));
  Multiplexer #(.width(6), .enable("false")) multiplexer_5 (
    .in0(6'b011111), .in1(decod_tens_units_3_tens), .out(chHMS1), .sel(and_3_out));
  Multiplexer #(.width(6), .enable("false")) multiplexer_6 (
    .in0(6'b011111), .in1(decod_tens_units_3_unites), .out(chHMS0), .sel(and_3_out));
endmodule

module decod_tens_units (
  input  [5:0] nb_in,
  output [5:0] tens,
  output [5:0] unites
);

  wire and_1_out, and_2_out, and_3_out, and_4_out, and_5_out, and_6_out, and_7_out, and_8_out, and_9_out,
       and_10_out, and_11_out, and_12_out, and_13_out, and_14_out, and_15_out, and_16_out, and_17_out,
       and_18_out, and_19_out, and_20_out, and_21_out, and_22_out, and_23_out, and_24_out, and_25_out,
       and_26_out, and_27_out, and_28_out, and_29_out, and_30_out, and_31_out, and_32_out, and_33_out,
       and_34_out, and_35_out, and_36_out, and_37_out, and_38_out, not_1_out, not_2_out, not_3_out,
       not_4_out, not_5_out, not_6_out, not_7_out, not_8_out, not_9_out, not_10_out, not_11_out, not_12_out,
       not_13_out, not_14_out, not_15_out, not_16_out, not_17_out, not_18_out, not_19_out, not_20_out,
       not_21_out, not_22_out, not_23_out, not_24_out, not_25_out, not_26_out, not_27_out, not_28_out,
       not_29_out, not_30_out, not_31_out, not_32_out, not_33_out, not_34_out, not_35_out, not_36_out,
       not_37_out, not_38_out, not_39_out, not_40_out, not_41_out, not_42_out, not_43_out, not_44_out,
       not_45_out, not_46_out, not_47_out, not_48_out, not_49_out, not_50_out, not_51_out, not_52_out,
       not_53_out, not_54_out, not_55_out, not_56_out, not_57_out, not_58_out, not_59_out, not_60_out,
       not_61_out, not_62_out, not_63_out, not_64_out, not_65_out, not_66_out, not_67_out, not_68_out,
       not_69_out, not_70_out, not_71_out;

  and and_1 (and_1_out, nb_in[5], nb_in[3]);
  and and_2 (and_2_out, nb_in[5], nb_in[4]);
  not not_1 (not_1_out, nb_in[5]);
  not not_2 (not_2_out, nb_in[5]);
  not not_3 (not_3_out, nb_in[4]);
  not not_4 (not_4_out, nb_in[3]);
  not not_5 (not_5_out, nb_in[5]);
  not not_6 (not_6_out, nb_in[4]);
  not not_7 (not_7_out, nb_in[5]);
  not not_8 (not_8_out, nb_in[4]);
  not not_9 (not_9_out, nb_in[5]);
  not not_10 (not_10_out, nb_in[5]);
  not not_11 (not_11_out, nb_in[3]);
  not not_12 (not_12_out, nb_in[2]);
  not not_13 (not_13_out, nb_in[4]);
  not not_14 (not_14_out, nb_in[3]);
  not not_15 (not_15_out, nb_in[3]);
  not not_16 (not_16_out, nb_in[3]);
  not not_17 (not_17_out, nb_in[2]);
  not not_18 (not_18_out, nb_in[5]);
  not not_19 (not_19_out, nb_in[4]);
  not not_20 (not_20_out, nb_in[2]);
  not not_21 (not_21_out, nb_in[1]);
  not not_22 (not_22_out, nb_in[5]);
  not not_23 (not_23_out, nb_in[3]);
  not not_24 (not_24_out, nb_in[2]);
  not not_25 (not_25_out, nb_in[5]);
  not not_26 (not_26_out, nb_in[1]);
  not not_27 (not_27_out, nb_in[4]);
  not not_28 (not_28_out, nb_in[3]);
  not not_29 (not_29_out, nb_in[3]);
  not not_30 (not_30_out, nb_in[2]);
  not not_31 (not_31_out, nb_in[1]);
  not not_32 (not_32_out, nb_in[2]);
  not not_33 (not_33_out, nb_in[4]);
  not not_34 (not_34_out, nb_in[3]);
  not not_35 (not_35_out, nb_in[1]);
  not not_36 (not_36_out, nb_in[5]);
  not not_37 (not_37_out, nb_in[4]);
  not not_38 (not_38_out, nb_in[5]);
  not not_39 (not_39_out, nb_in[2]);
  not not_40 (not_40_out, nb_in[1]);
  not not_41 (not_41_out, nb_in[5]);
  not not_42 (not_42_out, nb_in[2]);
  not not_43 (not_43_out, nb_in[2]);
  not not_44 (not_44_out, nb_in[1]);
  not not_45 (not_45_out, nb_in[4]);
  not not_46 (not_46_out, nb_in[3]);
  not not_47 (not_47_out, nb_in[2]);
  not not_48 (not_48_out, nb_in[4]);
  not not_49 (not_49_out, nb_in[3]);
  not not_50 (not_50_out, nb_in[5]);
  not not_51 (not_51_out, nb_in[4]);
  not not_52 (not_52_out, nb_in[3]);
  not not_53 (not_53_out, nb_in[5]);
  not not_54 (not_54_out, nb_in[3]);
  not not_55 (not_55_out, nb_in[5]);
  not not_56 (not_56_out, nb_in[4]);
  not not_57 (not_57_out, nb_in[1]);
  not not_58 (not_58_out, nb_in[5]);
  not not_59 (not_59_out, nb_in[3]);
  not not_60 (not_60_out, nb_in[2]);
  not not_61 (not_61_out, nb_in[1]);
  not not_62 (not_62_out, nb_in[5]);
  not not_63 (not_63_out, nb_in[2]);
  not not_64 (not_64_out, nb_in[4]);
  not not_65 (not_65_out, nb_in[3]);
  not not_66 (not_66_out, nb_in[1]);
  not not_67 (not_67_out, nb_in[3]);
  not not_68 (not_68_out, nb_in[1]);
  not not_69 (not_69_out, nb_in[4]);
  not not_70 (not_70_out, nb_in[2]);
  not not_71 (not_71_out, nb_in[1]);
  or or_1 (tens[2], and_1_out, and_2_out);
  and and_3 (and_3_out, not_1_out, nb_in[4], nb_in[2]);
  and and_4 (and_4_out, not_2_out, nb_in[4], nb_in[3]);
  and and_5 (and_5_out, nb_in[4], nb_in[3], nb_in[2]);
  and and_6 (and_6_out, nb_in[5], not_3_out, not_4_out);
  and and_7 (and_7_out, not_5_out, not_6_out, nb_in[3], nb_in[1]);
  and and_8 (and_8_out, not_7_out, not_8_out, nb_in[3], nb_in[2]);
  and and_9 (and_9_out, not_9_out, nb_in[3], nb_in[2], nb_in[1]);
  and and_10 (and_10_out, not_10_out, nb_in[4], not_11_out, not_12_out);
  and and_11 (and_11_out, nb_in[5], not_13_out, not_14_out);
  and and_12 (and_12_out, nb_in[5], not_15_out, nb_in[1]);
  and and_13 (and_13_out, nb_in[5], not_16_out, nb_in[2]);
  and and_14 (and_14_out, nb_in[5], nb_in[4], nb_in[3], not_17_out);
  and and_15 (and_15_out, not_18_out, not_19_out, nb_in[3], not_20_out, not_21_out);
  and and_16 (and_16_out, not_22_out, nb_in[4], not_23_out, not_24_out, nb_in[1]);
  and and_17 (and_17_out, not_25_out, nb_in[4], nb_in[3], nb_in[2], not_26_out);
  and and_18 (and_18_out, nb_in[5], not_27_out, not_28_out, nb_in[2], nb_in[1]);
  and and_19 (and_19_out, nb_in[5], nb_in[4], not_29_out, not_30_out, not_31_out);
  and and_20 (and_20_out, nb_in[5], nb_in[4], nb_in[3], not_32_out, nb_in[1]);
  and and_21 (and_21_out, not_33_out, not_34_out, nb_in[2], not_35_out);
  and and_22 (and_22_out, not_36_out, not_37_out, nb_in[2], nb_in[1]);
  and and_23 (and_23_out, not_38_out, nb_in[4], not_39_out, not_40_out);
  and and_24 (and_24_out, not_41_out, nb_in[4], nb_in[3], not_42_out);
  and and_25 (and_25_out, nb_in[4], nb_in[3], not_43_out, not_44_out);
  and and_26 (and_26_out, nb_in[5], not_45_out, not_46_out, not_47_out, nb_in[1]);
  and and_27 (and_27_out, nb_in[5], not_48_out, nb_in[3], nb_in[2]);
  and and_28 (and_28_out, nb_in[5], nb_in[4], not_49_out, nb_in[2], nb_in[1]);
  and and_29 (and_29_out, not_50_out, not_51_out, not_52_out, nb_in[1]);
  and and_30 (and_30_out, not_53_out, not_54_out, nb_in[2], nb_in[1]);
  and and_31 (and_31_out, not_55_out, not_56_out, nb_in[3], nb_in[2], not_57_out);
  and and_32 (and_32_out, not_58_out, nb_in[4], not_59_out, not_60_out, not_61_out);
  and and_33 (and_33_out, not_62_out, nb_in[4], nb_in[3], not_63_out, nb_in[1]);
  and and_34 (and_34_out, nb_in[5], not_64_out, not_65_out, not_66_out);
  and and_35 (and_35_out, nb_in[5], not_67_out, nb_in[2], not_68_out);
  and and_36 (and_36_out, nb_in[5], not_69_out, nb_in[3], nb_in[1]);
  and and_37 (and_37_out, nb_in[5], nb_in[3], nb_in[2], nb_in[1]);
  and and_38 (and_38_out, nb_in[5], nb_in[4], nb_in[3], not_70_out, not_71_out);
  or or_2 (tens[1], and_3_out, and_4_out, and_5_out, and_6_out);
  or or_3 (tens[0], and_7_out, and_8_out, and_9_out, and_10_out, and_11_out, and_12_out, and_13_out, and_14_out);
  or or_4 (unites[3], and_15_out, and_16_out, and_17_out, and_18_out, and_19_out, and_20_out);
  or or_5 (unites[2], and_21_out, and_22_out, and_23_out, and_24_out, and_25_out, and_26_out, and_27_out, and_28_out);
  or or_6 (unites[1], and_29_out, and_30_out, and_31_out, and_32_out, and_33_out, and_34_out, and_35_out, and_36_out, and_37_out, and_38_out);

  assign tens[5:3] = 3'b000;
  assign {unites[5:4], unites[0]} = {2'b00, nb_in[0]};
endmodule

module encod_tens_units (
  input  [5:0] tens,
  input  [5:0] unites,
  output [5:0] nb_out
);

  wire and_1_out, and_2_out, and_3_out, and_4_out, and_5_out, and_6_out, and_7_out, and_8_out, and_9_out,
       and_10_out, and_11_out, and_12_out, and_13_out, and_14_out, and_15_out, and_16_out, and_17_out,
       and_18_out, and_19_out, and_20_out, and_21_out, and_22_out, and_23_out, and_24_out, and_25_out,
       not_1_out, not_2_out, not_3_out, not_4_out, not_5_out, not_6_out, not_7_out, not_8_out, not_9_out,
       not_10_out, not_11_out, not_12_out, not_13_out, not_14_out, not_15_out, not_16_out, not_17_out,
       not_18_out, not_19_out, not_20_out, not_21_out, not_22_out, not_23_out, not_24_out, not_25_out,
       not_26_out, not_27_out, not_28_out, not_29_out, not_30_out, not_31_out, not_32_out, not_33_out,
       not_34_out, not_35_out;

  not not_1 (not_1_out, tens[1]);
  not not_2 (not_2_out, unites[3]);
  not not_3 (not_3_out, unites[2]);
  not not_4 (not_4_out, unites[1]);
  not not_5 (not_5_out, tens[2]);
  not not_6 (not_6_out, tens[1]);
  not not_7 (not_7_out, unites[3]);
  not not_8 (not_8_out, unites[2]);
  not not_9 (not_9_out, tens[2]);
  not not_10 (not_10_out, tens[1]);
  not not_11 (not_11_out, unites[3]);
  not not_12 (not_12_out, unites[1]);
  not not_13 (not_13_out, tens[2]);
  not not_14 (not_14_out, unites[3]);
  not not_15 (not_15_out, unites[2]);
  not not_16 (not_16_out, unites[1]);
  not not_17 (not_17_out, tens[1]);
  not not_18 (not_18_out, unites[2]);
  not not_19 (not_19_out, tens[0]);
  not not_20 (not_20_out, unites[1]);
  and and_1 (and_1_out, tens[1], tens[0], unites[1]);
  and and_2 (and_2_out, tens[1], tens[0], unites[2]);
  and and_3 (and_3_out, tens[1], tens[0], unites[3]);
  and and_4 (and_4_out, not_1_out, tens[0], unites[2], unites[1]);
  not not_21 (not_21_out, tens[1]);
  and and_5 (and_5_out, not_21_out, tens[0], unites[3]);
  and and_6 (and_6_out, tens[1], not_22_out);
  not not_22 (not_22_out, tens[0]);
  and and_7 (and_7_out, tens[1], not_2_out, not_3_out, not_4_out);
  and and_8 (and_8_out, tens[2], unites[3]);
  and and_9 (and_9_out, tens[2], tens[0]);
  not not_23 (not_23_out, tens[2]);
  and and_10 (and_10_out, not_23_out, not_24_out, unites[3]);
  not not_24 (not_24_out, tens[0]);
  and and_11 (and_11_out, not_5_out, not_6_out, tens[0], not_7_out, not_8_out);
  and and_12 (and_12_out, not_9_out, not_10_out, tens[0], not_11_out, not_12_out);
  and and_13 (and_13_out, not_13_out, tens[0], not_14_out, not_15_out, not_16_out);
  not not_25 (not_25_out, tens[0]);
  and and_14 (and_14_out, tens[1], not_25_out, unites[2]);
  and and_15 (and_15_out, tens[2], not_26_out, not_27_out);
  not not_26 (not_26_out, tens[0]);
  not not_27 (not_27_out, unites[3]);
  and and_16 (and_16_out, tens[2], unites[2], unites[1]);
  and and_17 (and_17_out, tens[2], tens[0], unites[3]);
  not not_28 (not_28_out, tens[1]);
  not not_29 (not_29_out, tens[0]);
  and and_18 (and_18_out, not_28_out, not_29_out, unites[2]);
  not not_30 (not_30_out, tens[1]);
  and and_19 (and_19_out, not_30_out, unites[2], not_31_out);
  not not_31 (not_31_out, unites[1]);
  and and_20 (and_20_out, not_17_out, tens[0], not_18_out, unites[1]);
  and and_21 (and_21_out, tens[1], not_32_out, not_33_out);
  not not_32 (not_32_out, tens[0]);
  not not_33 (not_33_out, unites[2]);
  not not_34 (not_34_out, unites[2]);
  and and_22 (and_22_out, tens[1], not_34_out, not_35_out);
  not not_35 (not_35_out, unites[1]);
  and and_23 (and_23_out, tens[1], tens[0], unites[2], unites[1]);
  and and_24 (and_24_out, not_19_out, unites[1]);
  and and_25 (and_25_out, tens[0], not_20_out);
  or or_1 (nb_out[5], and_1_out, and_2_out, and_3_out, tens[2]);
  or or_2 (nb_out[1], and_24_out, and_25_out);
  or or_3 (nb_out[4], and_4_out, and_5_out, and_6_out, and_7_out, and_8_out, and_9_out);
  or or_4 (nb_out[3], and_10_out, and_11_out, and_12_out, and_13_out, and_14_out, and_15_out, and_16_out, and_17_out);
  or or_5 (nb_out[2], and_18_out, and_19_out, and_20_out, and_21_out, and_22_out, and_23_out);

  assign nb_out[0] = unites[0];
endmodule

module fsm_select_3_trans (
  input  i0,
  input  i1,
  input  click,
  output s0,
  output s1
);

  wire and_1_out, and_2_out, and_3_out, and_4_out, not_1_out, not_2_out, not_3_out, not_4_out, not_5_out,
       not_6_out, not_7_out;

  not not_1 (not_1_out, i0);
  not not_2 (not_2_out, i1);
  not not_3 (not_3_out, i1);
  not not_4 (not_4_out, click);
  not not_5 (not_5_out, i0);
  not not_6 (not_6_out, click);
  not not_7 (not_7_out, i1);
  and and_1 (and_1_out, not_1_out, not_2_out, click);
  and and_2 (and_2_out, i0, not_3_out, not_4_out);
  and and_3 (and_3_out, not_5_out, i1, not_6_out);
  and and_4 (and_4_out, i0, not_7_out, click);
  or or_1 (s0, and_1_out, and_2_out);
  or or_2 (s1, and_3_out, and_4_out);
endmodule

module decod_rotation_logic (
  input  pb,
  input  pa,
  input  b,
  input  a,
  output CW,
  output CCw,
  output EN
);

  wire and_1_out, and_2_out, and_3_out, and_4_out, and_5_out, and_6_out, and_7_out, and_8_out, and_9_out,
       and_10_out, and_11_out, and_12_out, and_13_out, and_14_out, and_15_out, and_16_out, not_1_out,
       not_2_out, not_3_out, not_4_out, not_5_out, not_6_out, not_7_out, not_8_out, not_9_out, not_10_out,
       not_11_out, not_12_out, not_13_out, not_14_out, not_15_out, not_16_out, not_17_out, not_18_out,
       not_19_out, not_20_out, not_21_out, not_22_out, not_23_out, not_24_out, not_25_out, not_26_out,
       not_27_out, not_28_out;

  not not_1 (not_1_out, pb);
  and and_1 (and_1_out, not_1_out, not_2_out, a);
  not not_2 (not_2_out, pa);
  not not_3 (not_3_out, pb);
  and and_2 (and_2_out, not_3_out, pa, b);
  not not_4 (not_4_out, b);
  and and_3 (and_3_out, pb, not_4_out, not_5_out);
  not not_5 (not_5_out, a);
  and and_4 (and_4_out, pb, pa, not_6_out);
  not not_6 (not_6_out, a);
  not not_7 (not_7_out, pb);
  and and_5 (and_5_out, not_7_out, not_8_out, b);
  not not_8 (not_8_out, pa);
  and and_6 (and_6_out, pa, not_9_out, not_10_out);
  not not_9 (not_9_out, b);
  not not_10 (not_10_out, a);
  not not_11 (not_11_out, pa);
  and and_7 (and_7_out, pb, not_11_out, a);
  and and_8 (and_8_out, pb, pa, not_12_out);
  not not_12 (not_12_out, b);
  not not_13 (not_13_out, pb);
  not not_14 (not_14_out, pa);
  not not_15 (not_15_out, b);
  not not_16 (not_16_out, pb);
  not not_17 (not_17_out, pa);
  not not_18 (not_18_out, a);
  not not_19 (not_19_out, pb);
  not not_20 (not_20_out, b);
  not not_21 (not_21_out, a);
  not not_22 (not_22_out, pb);
  not not_23 (not_23_out, pa);
  not not_24 (not_24_out, b);
  not not_25 (not_25_out, a);
  not not_26 (not_26_out, pa);
  not not_27 (not_27_out, b);
  not not_28 (not_28_out, a);
  or or_1 (CW, and_1_out, and_2_out, and_3_out, and_4_out);
  or or_2 (CCw, and_5_out, and_6_out, and_7_out, and_8_out);
  and and_9 (and_9_out, not_13_out, not_14_out, not_15_out, a);
  and and_10 (and_10_out, not_16_out, not_17_out, b, not_18_out);
  and and_11 (and_11_out, not_19_out, pa, not_20_out, not_21_out);
  and and_12 (and_12_out, not_22_out, pa, b, a);
  and and_13 (and_13_out, pb, not_23_out, not_24_out, not_25_out);
  and and_14 (and_14_out, pb, not_26_out, b, a);
  and and_15 (and_15_out, pb, pa, not_27_out, a);
  and and_16 (and_16_out, pb, pa, b, not_28_out);
  or or_3 (EN, and_9_out, and_10_out, and_11_out, and_12_out, and_13_out, and_14_out, and_15_out, and_16_out);
endmodule

module decod_rotation (
  input  ChB,
  input  ChA,
  input  CLK,
  input  ChC,
  output EN,
  output CW,
  output CCW,
  output Click
);

  wire counter_1_q, d_ff_1_q, d_ff_2_q, Debounce_1_bttn_out, Debounce_2_bttn_out, Debounce_3_bttn_out,
       decod_rotation_logic_1_ccw, decod_rotation_logic_1_cw, decod_rotation_logic_1_en;

  Debounce Debounce_1 (.BTTN(ChB), .CLK(CLK), .BTTN_OUT(Debounce_1_bttn_out));
  Debounce Debounce_2 (.BTTN(ChA), .CLK(CLK), .BTTN_OUT(Debounce_2_bttn_out));
  D_Flip_Flop d_ff_1 (.D(Debounce_1_bttn_out), .clk(CLK), .Q(d_ff_1_q));  // open: Qn, preset, reset
  D_Flip_Flop d_ff_2 (.D(Debounce_2_bttn_out), .clk(CLK), .Q(d_ff_2_q));  // open: Qn, preset, reset
  Debounce Debounce_3 (.BTTN(ChC), .CLK(CLK), .BTTN_OUT(Debounce_3_bttn_out));
  detect_pos_edge detect_pos_edge_4 (.in_in(Debounce_3_bttn_out), .clk(CLK), .pos_edge(Click));
  decod_rotation_logic decod_rotation_logic_1 (
    .pb(d_ff_1_q), .pa(d_ff_2_q), .b(Debounce_1_bttn_out), .a(Debounce_2_bttn_out),
    .CW(decod_rotation_logic_1_cw), .CCw(decod_rotation_logic_1_ccw), .EN(decod_rotation_logic_1_en));
  Counter #(.width(1), .max('h1)) counter_1 (
    .up(1'b1), .clk(decod_rotation_logic_1_en), .Q(counter_1_q));  // open: clr, load, count, D, carry
  detect_pos_edge detect_pos_edge_1 (.in_in(counter_1_q), .clk(CLK), .pos_edge(EN));
  detect_pos_edge detect_pos_edge_2 (.in_in(decod_rotation_logic_1_cw), .clk(CLK), .pos_edge(CW));
  detect_pos_edge detect_pos_edge_3 (.in_in(decod_rotation_logic_1_ccw), .clk(CLK), .pos_edge(CCW));
endmodule

module detect_pos_edge (
  input  in_in,
  input  clk,
  output pos_edge
);

  wire d_ff_1_q;

  D_Flip_Flop d_ff_1 (.D(in_in), .clk(clk), .Q(d_ff_1_q));  // open: Qn, preset, reset
  and and_1 (pos_edge, ~d_ff_1_q, in_in);  // AND_Gate
endmodule

module detect_neg_edge (
  input  in_in,
  input  clk,
  output neg_edge
);

  wire d_ff_1_q;

  D_Flip_Flop d_ff_1 (.D(in_in), .clk(clk), .Q(d_ff_1_q));  // open: Qn, preset, reset
  and and_1 (neg_edge, d_ff_1_q, ~in_in);  // AND_Gate
endmodule

module AlarmBuzzer (
  input  EN,
  input  [3:0] SEL,
  output BEEP
);

  wire clock_1_out, toneSelector_1_tone;

  toneMaker toneSelector_1 (.SEL(SEL), .TONE(toneSelector_1_tone));
  Clock #(.highDuration(1000), .lowDuration(500)) clock_1 (.out(clock_1_out));
  and and_1 (BEEP, EN, clock_1_out, toneSelector_1_tone);
endmodule

module toneMaker (
  input  [3:0] SEL,
  output TONE
);

  wire clock_1_out, clock_2_out, clock_3_out, clock_4_out, clock_5_out, clock_6_out, clock_7_out,
       clock_8_out, clock_9_out, clock_10_out, clock_11_out, clock_12_out, clock_13_out, clock_14_out,
       clock_15_out, clock_16_out;

  Clock clock_1 (.out(clock_1_out));
  Clock #(.highDuration(2)) clock_2 (.out(clock_2_out));
  Clock #(.highDuration(3)) clock_3 (.out(clock_3_out));
  Clock #(.highDuration(4)) clock_4 (.out(clock_4_out));
  Clock #(.highDuration(5)) clock_5 (.out(clock_5_out));
  Clock #(.highDuration(6)) clock_6 (.out(clock_6_out));
  Clock #(.highDuration(7)) clock_7 (.out(clock_7_out));
  Clock #(.highDuration(8)) clock_8 (.out(clock_8_out));
  Clock #(.highDuration(9)) clock_9 (.out(clock_9_out));
  Clock #(.highDuration(10)) clock_10 (.out(clock_10_out));
  Clock #(.highDuration(11)) clock_11 (.out(clock_11_out));
  Clock #(.highDuration(12)) clock_12 (.out(clock_12_out));
  Clock #(.highDuration(13)) clock_13 (.out(clock_13_out));
  Clock #(.highDuration(13)) clock_14 (.out(clock_14_out));
  Clock #(.highDuration(14)) clock_15 (.out(clock_15_out));
  Clock #(.highDuration(15)) clock_16 (.out(clock_16_out));
  Multiplexer #(.select(4), .enable("false")) multiplexer_1 (
    .in0(clock_1_out), .in1(clock_2_out), .in2(clock_3_out), .in3(clock_4_out), .in4(clock_5_out),
    .in5(clock_6_out), .in6(clock_7_out), .in7(clock_8_out), .in8(clock_9_out), .in9(clock_10_out),
    .in10(clock_11_out), .in11(clock_12_out), .in12(clock_13_out), .in13(clock_14_out), .in14(clock_15_out),
    .in15(clock_16_out), .out(TONE), .sel(SEL));
endmodule

module ALARM (
  input  EN,
  input  [5:0] HIN,
  input  [5:0] MIN,
  input  [5:0] SIN,
  input  UP,
  input  DN,
  input  CLICK,
  input  CLK,
  input  AL_RST,
  input  EN_AL,
  input  [3:0] TONE_SEL,
  input  set_tone,
  output [5:0] DSP_H1,
  output [5:0] DSP_H0,
  output [5:0] DSP_M1,
  output [5:0] DSP_M0,
  output [5:0] DSP_S1,
  output [5:0] DSP_S0,
  output BUZZ
);

  wire alarm_comp_1_eq, and_1_out, and_2_out, and_3_out, and_4_out, clk_div_1_clk_out, CLK_t,
       demultiplexer_1_out0, demultiplexer_1_out1, demultiplexer_2_out0, demultiplexer_2_out1,
       demultiplexer_3_out0, demultiplexer_3_out1, detect_neg_edge_1_neg_edge, or_1_out, or_2_out,
       s_r_ff_1_q, sel;
  wire [3:0] counter_2_q;
  wire [5:0] ALH, ALM, decod_tens_units_2_tens, decod_tens_units_2_unites, decod_tens_units_3_tens,
       decod_tens_units_3_unites;

  Clock clock_1 (.out(CLK_t));
  Counter #(.width(1), .max('h1)) counter_1 (.up(1'b1), .clk(CLICK), .carry(sel));  // open: clr, load, count, D, Q
  Demultiplexer #(.enable("false")) demultiplexer_1 (
    .out0(demultiplexer_1_out0), .out1(demultiplexer_1_out1), .in(UP), .sel(sel));
  Demultiplexer #(.enable("false")) demultiplexer_2 (
    .out0(demultiplexer_2_out0), .out1(demultiplexer_2_out1), .in(DN), .sel(sel));
  or or_1 (or_1_out, demultiplexer_1_out0, demultiplexer_2_out0);
  or or_2 (or_2_out, demultiplexer_1_out1, demultiplexer_2_out1);
  clk_div clk_div_1 (.CLK_IN(CLK_t), .CLK_SEL(4'b1000), .CLK_OUT(clk_div_1_clk_out));
  Counter #(.width(4), .max('hf)) counter_2 (
    .clr(1'b0), .load(1'b1), .clk(set_tone), .D(TONE_SEL), .Q(counter_2_q));  // open: up, count, carry
  Demultiplexer #(.enable("false")) demultiplexer_3 (
    .out0(demultiplexer_3_out0), .out1(demultiplexer_3_out1), .in(clk_div_1_clk_out), .sel(sel));
  base_24_count base_24_count_1 (
    .UP_DN(demultiplexer_2_out0), .CIN(or_1_out), .SVAL(6'b001100), .VAL(ALH));  // open: RST, SET, COUT
  base_60_count base_60_count_2 (
    .UP_DN(demultiplexer_2_out1), .CIN(or_2_out), .VAL(ALM));  // open: RST, SET, SVAL, COUT
  and and_1 (and_1_out, EN_AL, ~EN);  // AND_Gate
  and and_2 (and_2_out, EN, ~demultiplexer_3_out0);  // AND_Gate
  and and_3 (and_3_out, EN, ~demultiplexer_3_out1);  // AND_Gate
  decod_tens_units decod_tens_units_2 (.nb_in(ALH), .tens(decod_tens_units_2_tens), .unites(decod_tens_units_2_unites));
  decod_tens_units decod_tens_units_3 (.nb_in(ALM), .tens(decod_tens_units_3_tens), .unites(decod_tens_units_3_unites));
  alarm_comp alarm_comp_1 (.EN(and_1_out), .HIN(HIN), .MIN(MIN), .SEC(SIN), .ALH(ALH), .ALM(ALM), .EQ(alarm_comp_1_eq));
  Multiplexer #(.width(6), .enable("false")) multiplexer_1 (.in0(6'b011111), .in1(6'b001010), .out(DSP_H1), .sel(EN));
  Multiplexer #(.width(6), .enable("false")) multiplexer_2 (.in0(6'b011111), .in1(6'b110100), .out(DSP_H0), .sel(EN));
  Multiplexer #(.width(6), .enable("false")) multiplexer_3 (
    .in0(6'b011111), .in1(decod_tens_units_2_tens), .out(DSP_M1), .sel(and_2_out));
  Multiplexer #(.width(6), .enable("false")) multiplexer_4 (
    .in0(6'b011111), .in1(decod_tens_units_2_unites), .out(DSP_M0), .sel(and_2_out));
  Multiplexer #(.width(6), .enable("false")) multiplexer_5 (
    .in0(6'b011111), .in1(decod_tens_units_3_tens), .out(DSP_S1), .sel(and_3_out));
  Multiplexer #(.width(6), .enable("false")) multiplexer_6 (
    .in0(6'b011111), .in1(decod_tens_units_3_unites), .out(DSP_S0), .sel(and_3_out));
  detect_neg_edge detect_neg_edge_1 (.in_in(EN_AL), .clk(CLK_t), .neg_edge(detect_neg_edge_1_neg_edge));
  S_R_Flip_Flop s_r_ff_1 (
    .S(alarm_comp_1_eq), .R(AL_RST), .clk(CLK_t), .Q(s_r_ff_1_q), .reset(detect_neg_edge_1_neg_edge));  // open: Qn, preset
  and and_4 (and_4_out, EN_AL, s_r_ff_1_q);
  AlarmBuzzer AlarmBuzzer_1 (.EN(and_4_out), .SEL(counter_2_q), .BEEP(BUZZ));

  // Notes on the sheet:
  //   Blinker
endmodule

module alarm_comp (
  input  EN,
  input  [5:0] HIN,
  input  [5:0] MIN,
  input  [5:0] SEC,
  input  [5:0] ALH,
  input  [5:0] ALM,
  output EQ
);

  wire comparator_1_eq, comparator_2_eq, comparator_3_eq;

  Comparator #(.width(6)) comparator_1 (.a(HIN), .b(ALH), .eq(comparator_1_eq));  // open: gt, lt
  Comparator #(.width(6)) comparator_2 (.a(SEC), .b({6{1'b0}}), .eq(comparator_2_eq));  // open: gt, lt
  Comparator #(.width(6)) comparator_3 (.a(MIN), .b(ALM), .eq(comparator_3_eq));  // open: gt, lt
  and and_1 (EQ, EN, comparator_1_eq, comparator_2_eq, comparator_3_eq);
endmodule

module Rot_decode_selector (
  input  [2:0] SEL,
  input  EN,
  input  CW,
  input  CCW,
  input  Click,
  output [7:0] EN_OUT,
  output [7:0] CW_OUT,
  output [7:0] CCW_OUT,
  output [7:0] CLICK_OUT
);

  Demultiplexer #(.select(3), .enable("false")) demultiplexer_1 (
    .out0(EN_OUT[0]), .out1(EN_OUT[1]), .out2(EN_OUT[2]), .out3(EN_OUT[3]), .out4(EN_OUT[4]),
    .out5(EN_OUT[5]), .out6(EN_OUT[6]), .out7(EN_OUT[7]), .in(EN), .sel(SEL));
  Demultiplexer #(.select(3), .enable("false")) demultiplexer_2 (
    .out0(CCW_OUT[0]), .out1(CCW_OUT[1]), .out2(CCW_OUT[2]), .out3(CCW_OUT[3]), .out4(CCW_OUT[4]),
    .out5(CCW_OUT[5]), .out6(CCW_OUT[6]), .out7(CCW_OUT[7]), .in(CCW), .sel(SEL));
  Demultiplexer #(.select(3), .enable("false")) demultiplexer_3 (
    .out0(CW_OUT[0]), .out1(CW_OUT[1]), .out2(CW_OUT[2]), .out3(CW_OUT[3]), .out4(CW_OUT[4]),
    .out5(CW_OUT[5]), .out6(CW_OUT[6]), .out7(CW_OUT[7]), .in(CW), .sel(SEL));
  Demultiplexer #(.select(3), .enable("false")) demultiplexer_4 (
    .out0(CLICK_OUT[0]), .out1(CLICK_OUT[1]), .out2(CLICK_OUT[2]), .out3(CLICK_OUT[3]), .out4(CLICK_OUT[4]),
    .out5(CLICK_OUT[5]), .out6(CLICK_OUT[6]), .out7(CLICK_OUT[7]), .in(Click), .sel(SEL));
endmodule

module tDispTxt (
  output [5:0] Output_bus_1,
  output [5:0] Output_bus_2,
  output [5:0] Output_bus_3,
  output [5:0] Output_bus_4,
  output [5:0] Output_bus_5,
  output [5:0] Output_bus_6
);


  assign Output_bus_1 = 6'b111011;
  assign Output_bus_2 = 6'b011111;
  assign Output_bus_3 = 6'b001101;
  assign Output_bus_4 = 6'b010010;
  assign Output_bus_5 = 6'b011010;
  assign Output_bus_6 = 6'b110111;
endmodule

module tSetTxt (
  output [5:0] out_1,
  output [5:0] out_2,
  output [5:0] out_3,
  output [5:0] out_4,
  output [5:0] out_5,
  output [5:0] out_6
);


  assign out_1 = 6'b111011;
  assign out_2 = 6'b011111;
  assign out_3 = 6'b011010;
  assign out_4 = 6'b001110;
  assign out_5 = 6'b011011;
  assign out_6 = 6'b011111;
endmodule

module alarTxt (
  output [5:0] out_1,
  output [5:0] out_2,
  output [5:0] out_3,
  output [5:0] out_4,
  output [5:0] out_5,
  output [5:0] out_6
);


  assign out_1 = 6'b001010;
  assign out_2 = 6'b010100;
  assign out_3 = 6'b001010;
  assign out_4 = 6'b111001;
  assign out_5 = 6'b011111;
  assign out_6 = 6'b011111;
endmodule

module chronoTxt (
  output [5:0] Output_bus_1,
  output [5:0] Output_bus_2,
  output [5:0] Output_bus_3,
  output [5:0] Output_bus_4,
  output [5:0] Output_bus_5,
  output [5:0] Output_bus_6
);


  assign Output_bus_1 = 6'b001100;
  assign Output_bus_2 = 6'b010001;
  assign Output_bus_3 = 6'b011001;
  assign Output_bus_4 = 6'b010110;
  assign Output_bus_5 = 6'b010101;
  assign Output_bus_6 = 6'b010110;
endmodule

module txtFSM_trans (
  input  p0,
  input  p1,
  input  RIS,
  input  FAL,
  input  CIN,
  output bit0,
  output bit1
);

  wire and_1_out, and_2_out, and_3_out, and_4_out, and_5_out, and_6_out, and_7_out, and_8_out, not_1_out,
       not_2_out, not_3_out, not_4_out, not_5_out, not_6_out, not_7_out, not_8_out, not_9_out, not_10_out,
       not_11_out, not_12_out, not_13_out, not_14_out;

  not not_1 (not_1_out, p0);
  not not_2 (not_2_out, RIS);
  not not_3 (not_3_out, FAL);
  not not_4 (not_4_out, p1);
  not not_5 (not_5_out, FAL);
  not not_6 (not_6_out, p1);
  not not_7 (not_7_out, p1);
  not not_8 (not_8_out, p0);
  not not_9 (not_9_out, FAL);
  not not_10 (not_10_out, CIN);
  not not_11 (not_11_out, p0);
  not not_12 (not_12_out, CIN);
  not not_13 (not_13_out, p0);
  not not_14 (not_14_out, p0);
  and and_1 (and_1_out, not_1_out, p1, not_2_out, not_3_out, CIN);
  and and_2 (and_2_out, p0, not_4_out, not_5_out);
  and and_3 (and_3_out, p0, not_6_out, CIN);
  and and_4 (and_4_out, p0, not_7_out, RIS);
  and and_5 (and_5_out, not_8_out, RIS, not_9_out, not_10_out);
  and and_6 (and_6_out, not_11_out, p1, not_12_out);
  and and_7 (and_7_out, not_13_out, p1, FAL);
  and and_8 (and_8_out, not_14_out, p1, RIS);
  or or_1 (bit0, and_1_out, and_2_out, and_3_out, and_4_out);
  or or_2 (bit1, and_5_out, and_6_out, and_7_out, and_8_out);
endmodule

module txtFSM (
  input  EN,
  input  CLK,
  output [1:0] TXT
);

  wire and_1_out, and_2_out, counter_1_carry, detect_neg_edge_1_neg_edge, detect_pos_edge_1_pos_edge,
       txtFSM_trans_1_bit0, txtFSM_trans_1_bit1;

  detect_pos_edge detect_pos_edge_1 (.in_in(EN), .clk(CLK), .pos_edge(detect_pos_edge_1_pos_edge));
  detect_neg_edge detect_neg_edge_1 (.in_in(EN), .clk(CLK), .neg_edge(detect_neg_edge_1_neg_edge));
  txtFSM_trans txtFSM_trans_1 (
    .p0(TXT[1]), .p1(TXT[0]), .RIS(detect_pos_edge_1_pos_edge), .FAL(detect_neg_edge_1_neg_edge),
    .CIN(counter_1_carry), .bit0(txtFSM_trans_1_bit0), .bit1(txtFSM_trans_1_bit1));
  D_Flip_Flop d_ff_1 (.D(txtFSM_trans_1_bit0), .clk(CLK), .Q(TXT[1]));  // open: Qn, preset, reset
  D_Flip_Flop d_ff_2 (.D(txtFSM_trans_1_bit1), .clk(CLK), .Q(TXT[0]));  // open: Qn, preset, reset
  and and_1 (and_1_out, ~txtFSM_trans_1_bit0, ~txtFSM_trans_1_bit1);  // AND_Gate
  and and_2 (and_2_out, ~txtFSM_trans_1_bit0, txtFSM_trans_1_bit1);  // AND_Gate
  Counter #(.width(11), .max('h200)) counter_1 (
    .clr(and_1_out), .count(and_2_out), .clk(CLK), .carry(counter_1_carry));  // open: load, up, D, Q
endmodule

module test (
);

  wire and_1_out, Button_12324_out, Button_22345_out, comparator_1_gt, comparator_1_lt, or_1_out;
  wire [5:0] abc_val, bcd_tens, bcd_unites;
  wire [7:0] fasdfasfsa_out0, fasdfasfsa_out1;

  Button Button_12324 (.out(Button_12324_out));
  Button Button_22345 (.out(Button_22345_out));
  Comparator #(.width(6)) comparator_1 (
    .a(abc_val), .b(6'b001111), .gt(comparator_1_gt), .lt(comparator_1_lt));  // open: eq
  and and_1 (and_1_out, comparator_1_lt, Button_12324_out);
  or or_1 (or_1_out, and_1_out, Button_22345_out);
  base_24_count abc (
    .RST(comparator_1_gt), .UP_DN(Button_22345_out), .CIN(or_1_out), .SET(1'b0), .VAL(abc_val));  // open: SVAL, COUT
  decod_tens_units bcd (.nb_in(abc_val), .tens(bcd_tens), .unites(bcd_unites));
  sixSegDriver fasdfasfsa (
    .dsp0(bcd_tens), .dsp1(bcd_unites), .Out0(fasdfasfsa_out0), .Out1(fasdfasfsa_out1));  // open: dsp2, dsp3, dsp4, dsp5, Out2, Out3, Out4, Out5
  _7_Segment_Display asdfqer (
    .g(fasdfasfsa_out0[6]), .f(fasdfasfsa_out0[5]), .a(fasdfasfsa_out0[0]), .b(fasdfasfsa_out0[1]),
    .e(fasdfasfsa_out0[4]), .d(fasdfasfsa_out0[3]), .c(fasdfasfsa_out0[2]), .dp(fasdfasfsa_out0[7]));
  _7_Segment_Display adddv (
    .g(fasdfasfsa_out1[6]), .f(fasdfasfsa_out1[5]), .a(fasdfasfsa_out1[0]), .b(fasdfasfsa_out1[1]),
    .e(fasdfasfsa_out1[4]), .d(fasdfasfsa_out1[3]), .c(fasdfasfsa_out1[2]), .dp(fasdfasfsa_out1[7]));
endmodule

module TONE_SELECT (
  input  EN,
  input  [3:0] dp_switch,
  output [3:0] TONE,
  output [5:0] D0,
  output [5:0] D1,
  output [5:0] D2,
  output [5:0] D3,
  output [5:0] D4,
  output [5:0] D5,
  output buzz,
  output set_tone
);

  wire clock_1_out;
  wire [5:0] bit_extender_1_out, decod_tens_units_1_tens, decod_tens_units_1_unites;

  assign bit_extender_1_out = {{2{1'b0}}, dp_switch};  // Bit_Extender bit_extender_1
  Clock clock_1 (.out(clock_1_out));
  AlarmBuzzer AlarmBuzzer_1 (.EN(EN), .SEL(dp_switch), .BEEP(buzz));
  decod_tens_units decod_tens_units_1 (
    .nb_in(bit_extender_1_out), .tens(decod_tens_units_1_tens), .unites(decod_tens_units_1_unites));
  detect_neg_edge detect_neg_edge_1 (.in_in(EN), .clk(clock_1_out), .neg_edge(set_tone));
  Multiplexer #(.width(6), .enable("false")) multiplexer_1 (.in0(6'b011111), .in1(6'b011011), .out(D0), .sel(EN));
  Multiplexer #(.width(6), .enable("false")) multiplexer_2 (.in0(6'b011111), .in1(6'b010110), .out(D1), .sel(EN));
  Multiplexer #(.width(6), .enable("false")) multiplexer_3 (.in0(6'b011111), .in1(6'b010101), .out(D2), .sel(EN));
  Multiplexer #(.width(6), .enable("false")) multiplexer_4 (.in0(6'b011111), .in1(6'b101110), .out(D3), .sel(EN));
  Multiplexer #(.width(6), .enable("false")) multiplexer_5 (
    .in0(6'b011111), .in1(decod_tens_units_1_tens), .out(D4), .sel(EN));
  Multiplexer #(.width(6), .enable("false")) multiplexer_6 (
    .in0(6'b011111), .in1(decod_tens_units_1_unites), .out(D5), .sel(EN));

  assign TONE = dp_switch;
endmodule

module GAME (
  input  EN,
  input  CLK,
  input  RST,
  input  UP,
  input  DN,
  input  CLICK,
  output [9:0] LEDS,
  output [5:0] D0,
  output [5:0] D1,
  output [5:0] D2,
  output [5:0] D3,
  output [5:0] D4,
  output [5:0] D5
);

  wire and_1_out, and_2_out, and_3_out, comparator_1_eq, comparator_1_gt, comparator_1_lt, counter_2_carry,
       d_ff_1_q, d_ff_2_q, d_ff_3_q, or_1_out, or_2_out, s_r_ff_1_q, xor_1_out;
  wire [5:0] counter_1_q, decod_tens_units_1_tens, decod_tens_units_1_unites, multiplexer_1_out,
       shuffler_1_output_bus_1;
  wire [9:0] bit_extender_2_out, counter_2_q, multiplexer_4_out;

  xor xor_1 (xor_1_out, s_r_ff_1_q, EN);
  or or_1 (or_1_out, UP, DN);
  D_Flip_Flop d_ff_1 (.D(xor_1_out), .clk(CLK), .Q(d_ff_1_q));  // open: Qn, preset, reset
  and and_1 (and_1_out, ~d_ff_1_q, xor_1_out);  // AND_Gate
  D_Flip_Flop d_ff_2 (.D(DN), .clk(CLK), .Q(d_ff_2_q));  // open: Qn, preset, reset
  D_Flip_Flop d_ff_3 (.D(or_1_out), .clk(CLK), .Q(d_ff_3_q));  // open: Qn, preset, reset
  Counter #(.width(6), .max('h3f)) counter_1 (
    .clr(RST), .up(d_ff_2_q), .clk(d_ff_3_q), .Q(counter_1_q));  // open: load, count, D, carry
  shuffler shuffler_1 (.RST(1'b0), .SHUF(and_1_out), .Output_bus_1(shuffler_1_output_bus_1));
  // Probe on shuffler_1_output_bus_1
  // Probe on counter_1_q
  Multiplexer #(.width(6), .enable("false")) multiplexer_1 (
    .in0({6{1'b0}}), .in1(shuffler_1_output_bus_1), .out(multiplexer_1_out), .sel(EN));
  Comparator #(.width(6)) comparator_1 (
    .a(shuffler_1_output_bus_1), .b(counter_1_q), .gt(comparator_1_gt), .eq(comparator_1_eq),
    .lt(comparator_1_lt));
  assign LEDS = {{4{1'b0}}, shuffler_1_output_bus_1};  // Bit_Extender bit_extender_1
  assign bit_extender_2_out = {{4{1'b0}}, multiplexer_1_out};  // Bit_Extender bit_extender_2
  or or_2 (or_2_out, comparator_1_gt, comparator_1_lt);
  and and_2 (and_2_out, or_2_out, CLICK);
  and and_3 (and_3_out, comparator_1_eq, CLICK);
  Counter #(.width(10), .max('h3ff)) counter_2 (
    .clr(CLICK), .clk(CLK), .carry(counter_2_carry), .Q(counter_2_q));  // open: load, up, count, D
  S_R_Flip_Flop s_r_ff_1 (.Q(s_r_ff_1_q), .reset(counter_2_carry), .preset(and_3_out));  // open: S, R, clk, Qn
  decod_tens_units decod_tens_units_1 (
    .nb_in(counter_1_q), .tens(decod_tens_units_1_tens), .unites(decod_tens_units_1_unites));
  Multiplexer #(.width(6), .enable("false")) multiplexer_2 (
    .in0(6'b011111), .in1(decod_tens_units_1_tens), .out(D4), .sel(EN));
  Multiplexer #(.width(6), .enable("false")) multiplexer_3 (
    .in0(6'b011111), .in1(decod_tens_units_1_unites), .out(D5), .sel(EN));
  Multiplexer #(.width(10), .enable("false")) multiplexer_4 (
    .in0(bit_extender_2_out), .in1(counter_2_q), .out(multiplexer_4_out), .sel(s_r_ff_1_q));
  // Probe on s_r_ff_1_q
  Multiplexer #(.width(6), .enable("false")) multiplexer_5 (
    .in0(6'b011111), .in1(6'b010101), .out(D0), .sel(and_2_out));
  Multiplexer #(.width(6), .enable("false")) multiplexer_6 (
    .in0(6'b011111), .in1(6'b010110), .out(D1), .sel(and_2_out));
  Multiplexer #(.width(6), .enable("false")) multiplexer_7 (
    .in0(6'b011111), .in1(6'b010111), .out(D2), .sel(and_2_out));
  Multiplexer #(.width(6), .enable("false")) multiplexer_8 (
    .in0(6'b011111), .in1(6'b101110), .out(D3), .sel(and_2_out));
endmodule

module shuffler (
  input  RST,
  input  SHUF,
  output [5:0] Output_bus_1
);

  wire and_1_out, d_ff_1_q;

  D_Flip_Flop d_ff_1 (.D(SHUF), .Q(d_ff_1_q));  // open: clk, Qn, preset, reset
  and and_1 (and_1_out, ~d_ff_1_q, SHUF);  // AND_Gate
  Random #(.width(6)) random_1 (.clr(RST), .next(and_1_out), .clk(and_1_out), .out(Output_bus_1));
endmodule

module shufDec (
  input  b0,
  input  b1,
  input  b2,
  input  b3,
  output SHUF
);

  wire not_1_out, not_2_out;

  not not_1 (not_1_out, b0);
  not not_2 (not_2_out, b1);
  and and_1 (SHUF, not_1_out, not_2_out, b2, b3);
endmodule

module CHRONO (
  input  EN,
  input  Click,
  input  clk_sec,
  input  clk,
  input  DP_Switch,
  output [5:0] disp0,
  output [5:0] disp1,
  output [5:0] disp2,
  output [5:0] disp3,
  output [5:0] disp4,
  output [5:0] disp5
);

  wire and_1_out, base60_count_1_cout, base_100_count_1_cout, or_1_out, or_2_out;
  wire [1:0] txtFSM_1_txt;
  wire [5:0] and_2_out, base60_count_1_val, base_100_count_1_val, bit_extender_1_out,
       chronoTxt_1_output_bus_1, chronoTxt_1_output_bus_2, chronoTxt_1_output_bus_3,
       chronoTxt_1_output_bus_4, chronoTxt_1_output_bus_5, chronoTxt_1_output_bus_6, decod_tens_units_1_tens,
       decod_tens_units_1_unites, decod_tens_units_2_tens, decod_tens_units_2_unites, or_3_out;

  and and_1 (and_1_out, DP_Switch, clk_sec);
  or or_1 (or_1_out, base_100_count_1_cout, Click);
  base_100_count base_100_count_1 (
    .RST(or_1_out), .UP_ND(1'b0), .CIN(base60_count_1_cout), .SET(1'b0), .COUT(base_100_count_1_cout),
    .VAL(base_100_count_1_val));  // open: SVAL
  base60_count base60_count_1 (
    .RST(or_1_out), .UP_DN(1'b0), .CIN(and_1_out), .CLK(clk), .COUT(base60_count_1_cout),
    .VAL(base60_count_1_val));
  txtFSM txtFSM_1 (.EN(EN), .CLK(clk), .TXT(txtFSM_1_txt));
  decod_tens_units decod_tens_units_1 (
    .nb_in(base_100_count_1_val), .tens(decod_tens_units_1_tens), .unites(decod_tens_units_1_unites));
  or or_2 (or_2_out, clk_sec, ~DP_Switch);  // OR_Gate
  decod_tens_units decod_tens_units_2 (
    .nb_in(base60_count_1_val), .tens(decod_tens_units_2_tens), .unites(decod_tens_units_2_unites));
  assign and_2_out = 6'b100000 & bit_extender_1_out;  // AND_Gate and_2, 6 bits wide
  assign bit_extender_1_out = {{5{or_2_out}}, or_2_out};  // Bit_Extender bit_extender_1
  chronoTxt chronoTxt_1 (
    .Output_bus_1(chronoTxt_1_output_bus_1), .Output_bus_2(chronoTxt_1_output_bus_2),
    .Output_bus_3(chronoTxt_1_output_bus_3), .Output_bus_4(chronoTxt_1_output_bus_4),
    .Output_bus_5(chronoTxt_1_output_bus_5), .Output_bus_6(chronoTxt_1_output_bus_6));
  assign or_3_out = decod_tens_units_1_unites | and_2_out;  // OR_Gate or_3, 6 bits wide
  Multiplexer #(.select(2), .width(6), .enable("false")) multiplexer_1 (
    .in0(6'b011111), .in1(chronoTxt_1_output_bus_1), .in2(chronoTxt_1_output_bus_1),
    .in3(chronoTxt_1_output_bus_1), .out(disp0), .sel(txtFSM_1_txt));
  Multiplexer #(.select(2), .width(6), .enable("false")) multiplexer_2 (
    .in0(6'b011111), .in1(chronoTxt_1_output_bus_2), .in2(6'b110001), .in3(6'b110001), .out(disp1),
    .sel(txtFSM_1_txt));
  Multiplexer #(.select(2), .width(6), .enable("false")) multiplexer_3 (
    .in0(6'b011111), .in1(chronoTxt_1_output_bus_3), .in2(decod_tens_units_1_tens),
    .in3(decod_tens_units_1_tens), .out(disp2), .sel(txtFSM_1_txt));
  Multiplexer #(.select(2), .width(6), .enable("false")) multiplexer_4 (
    .in0(6'b011111), .in1(chronoTxt_1_output_bus_4), .in2(or_3_out), .in3(or_3_out), .out(disp3),
    .sel(txtFSM_1_txt));
  Multiplexer #(.select(2), .width(6), .enable("false")) multiplexer_5 (
    .in0(6'b011111), .in1(chronoTxt_1_output_bus_5), .in2(decod_tens_units_2_tens),
    .in3(decod_tens_units_2_tens), .out(disp4), .sel(txtFSM_1_txt));
  Multiplexer #(.select(2), .width(6), .enable("false")) multiplexer_6 (
    .in0(6'b011111), .in1(chronoTxt_1_output_bus_6), .in2(decod_tens_units_2_unites),
    .in3(decod_tens_units_2_unites), .out(disp5), .sel(txtFSM_1_txt));
endmodule

module base60_count (
  input  RST,
  input  UP_DN,
  input  CIN,
  input  CLK,
  output COUT,
  output [5:0] VAL
);

  wire counter_1_carry, detect_neg_edge_1_neg_edge, not_1_out;

  not not_1 (not_1_out, UP_DN);
  Counter #(.width(6), .max('h3b)) counter_1 (
    .clr(RST), .up(not_1_out), .clk(CIN), .carry(counter_1_carry), .Q(VAL));  // open: load, count, D
  detect_neg_edge detect_neg_edge_1 (.in_in(counter_1_carry), .clk(CLK), .neg_edge(detect_neg_edge_1_neg_edge));
  D_Flip_Flop d_ff_1 (.D(detect_neg_edge_1_neg_edge), .clk(CLK), .Q(COUT), .reset(RST));  // open: Qn, preset
endmodule

module LED_Anim (
  input  EN,
  input  SLO_CLK,
  input  [1:0] SEL,
  output [9:0] LEDOUT
);

  wire and_1_out;
  wire [9:0] bit_extender_1_out, bounce_1_ledout, multiplexer_1_out, zoom_1_led_out;

  and and_1 (and_1_out, EN, SLO_CLK);
  zoom zoom_1 (.CLK(and_1_out), .LED_OUT(zoom_1_led_out));
  bounce bounce_1 (.CLK(and_1_out), .LEDOUT(bounce_1_ledout));
  assign bit_extender_1_out = {{9{EN}}, EN};  // Bit_Extender bit_extender_1
  Multiplexer #(.select(2), .width(10), .enable("false")) multiplexer_1 (
    .in0(zoom_1_led_out), .in3(bounce_1_ledout), .out(multiplexer_1_out), .sel(SEL));  // open: in1, in2
  assign LEDOUT = bit_extender_1_out & multiplexer_1_out;  // AND_Gate and_2, 10 bits wide
endmodule

module circus (
  input  CLK,
  output [9:0] LEDOUT
);

  wire d_ff_1_qn;

  D_Flip_Flop d_ff_1 (.D(d_ff_1_qn), .clk(CLK), .Q(LEDOUT[9]), .Qn(d_ff_1_qn));  // open: preset, reset
  not not_1 (LEDOUT[0], LEDOUT[9]);
  not not_2 (LEDOUT[2], LEDOUT[9]);
  not not_3 (LEDOUT[4], LEDOUT[9]);
  not not_4 (LEDOUT[6], LEDOUT[9]);
  not not_5 (LEDOUT[8], LEDOUT[9]);

  assign {LEDOUT[7], LEDOUT[5], LEDOUT[3], LEDOUT[1]} = {4{LEDOUT[9]}};
endmodule

module zoom_tl (
  input  Input_1,
  input  Input_2,
  input  Input_3,
  input  Input_4,
  input  Input_5,
  output Output_1,
  output Output_2,
  output Output_3,
  output Output_4,
  output Output_5
);

  wire and_1_out, and_2_out, and_3_out, and_4_out, and_5_out, and_6_out, and_7_out, and_8_out, and_9_out,
       not_1_out, not_2_out, not_3_out, not_4_out, not_5_out, not_6_out, not_7_out, not_8_out, not_9_out,
       not_10_out, not_11_out, not_12_out, not_13_out, not_14_out, not_15_out, not_16_out, not_17_out,
       not_18_out, not_19_out, not_20_out, not_21_out, not_22_out, not_23_out, not_24_out, not_25_out,
       not_26_out, not_27_out, not_28_out;

  not not_1 (not_1_out, Input_1);
  not not_2 (not_2_out, Input_2);
  not not_3 (not_3_out, Input_1);
  not not_4 (not_4_out, Input_3);
  not not_5 (not_5_out, Input_4);
  not not_6 (not_6_out, Input_5);
  not not_7 (not_7_out, Input_1);
  not not_8 (not_8_out, Input_2);
  not not_9 (not_9_out, Input_3);
  not not_10 (not_10_out, Input_1);
  not not_11 (not_11_out, Input_2);
  not not_12 (not_12_out, Input_4);
  not not_13 (not_13_out, Input_1);
  not not_14 (not_14_out, Input_2);
  not not_15 (not_15_out, Input_5);
  not not_16 (not_16_out, Input_1);
  not not_17 (not_17_out, Input_2);
  not not_18 (not_18_out, Input_4);
  not not_19 (not_19_out, Input_1);
  not not_20 (not_20_out, Input_2);
  not not_21 (not_21_out, Input_5);
  not not_22 (not_22_out, Input_1);
  not not_23 (not_23_out, Input_2);
  not not_24 (not_24_out, Input_5);
  not not_25 (not_25_out, Input_1);
  not not_26 (not_26_out, Input_3);
  not not_27 (not_27_out, Input_4);
  not not_28 (not_28_out, Input_5);
  and and_1 (and_1_out, not_1_out, not_2_out, Input_3, Input_4, Input_5);
  and and_2 (and_2_out, not_3_out, Input_2, not_4_out, not_5_out, not_6_out);
  and and_3 (and_3_out, not_7_out, not_8_out, not_9_out, Input_4, Input_5);
  and and_4 (and_4_out, not_10_out, not_11_out, Input_3, not_12_out);
  and and_5 (and_5_out, not_13_out, not_14_out, Input_3, not_15_out);
  and and_6 (and_6_out, not_16_out, not_17_out, not_18_out, Input_5);
  and and_7 (and_7_out, not_19_out, not_20_out, Input_4, not_21_out);
  and and_8 (and_8_out, not_22_out, not_23_out, not_24_out);
  and and_9 (and_9_out, not_25_out, not_26_out, not_27_out, not_28_out);
  or or_1 (Output_2, and_1_out, and_2_out);
  or or_2 (Output_3, and_3_out, and_4_out, and_5_out);
  or or_3 (Output_4, and_6_out, and_7_out);
  or or_4 (Output_5, and_8_out, and_9_out);

  assign Output_1 = 1'b0;
endmodule

module zoom_dec (
  input  Input_1,
  input  Input_2,
  input  Input_3,
  input  Input_4,
  input  Input_5,
  output Output_1,
  output Output_2,
  output Output_3,
  output Output_4,
  output Output_5,
  output Output_6,
  output Output_7,
  output Output_8,
  output Output_9,
  output Output_10
);

  wire and_2_out, and_3_out, and_4_out, and_5_out, and_7_out, and_8_out, and_9_out, and_10_out, and_12_out,
       and_13_out, and_14_out, and_15_out, not_1_out, not_2_out, not_3_out, not_4_out, not_5_out, not_6_out,
       not_7_out, not_8_out, not_9_out, not_10_out, not_11_out, not_12_out, not_13_out, not_14_out,
       not_15_out, not_16_out, not_17_out, not_18_out, not_19_out, not_20_out, not_21_out, not_22_out,
       not_23_out, not_24_out, not_25_out, not_26_out, not_27_out, not_28_out, not_29_out, not_30_out,
       not_31_out, not_32_out, not_33_out, not_34_out, not_35_out, not_36_out, not_37_out, not_38_out,
       not_39_out, not_40_out, not_41_out, not_42_out, not_43_out, not_44_out, not_45_out, not_46_out,
       not_47_out, not_48_out, not_49_out, not_50_out;

  not not_1 (not_1_out, Input_1);
  not not_2 (not_2_out, Input_2);
  not not_3 (not_3_out, Input_4);
  not not_4 (not_4_out, Input_5);
  not not_5 (not_5_out, Input_1);
  not not_6 (not_6_out, Input_2);
  not not_7 (not_7_out, Input_3);
  not not_8 (not_8_out, Input_1);
  not not_9 (not_9_out, Input_2);
  not not_10 (not_10_out, Input_4);
  not not_11 (not_11_out, Input_1);
  not not_12 (not_12_out, Input_2);
  not not_13 (not_13_out, Input_5);
  not not_14 (not_14_out, Input_1);
  not not_15 (not_15_out, Input_2);
  not not_16 (not_16_out, Input_5);
  not not_17 (not_17_out, Input_1);
  not not_18 (not_18_out, Input_2);
  not not_19 (not_19_out, Input_1);
  not not_20 (not_20_out, Input_2);
  not not_21 (not_21_out, Input_5);
  not not_22 (not_22_out, Input_1);
  not not_23 (not_23_out, Input_3);
  not not_24 (not_24_out, Input_4);
  not not_25 (not_25_out, Input_5);
  not not_26 (not_26_out, Input_1);
  not not_27 (not_27_out, Input_2);
  not not_28 (not_28_out, Input_5);
  not not_29 (not_29_out, Input_1);
  not not_30 (not_30_out, Input_3);
  not not_31 (not_31_out, Input_4);
  not not_32 (not_32_out, Input_5);
  not not_33 (not_33_out, Input_1);
  not not_34 (not_34_out, Input_2);
  not not_35 (not_35_out, Input_1);
  not not_36 (not_36_out, Input_2);
  not not_37 (not_37_out, Input_5);
  not not_38 (not_38_out, Input_1);
  not not_39 (not_39_out, Input_2);
  not not_40 (not_40_out, Input_5);
  not not_41 (not_41_out, Input_1);
  not not_42 (not_42_out, Input_2);
  not not_43 (not_43_out, Input_3);
  not not_44 (not_44_out, Input_1);
  not not_45 (not_45_out, Input_2);
  not not_46 (not_46_out, Input_4);
  not not_47 (not_47_out, Input_1);
  not not_48 (not_48_out, Input_2);
  not not_49 (not_49_out, Input_4);
  not not_50 (not_50_out, Input_5);
  and and_1 (Output_1, not_1_out, not_2_out, Input_3, not_3_out, not_4_out);
  and and_2 (and_2_out, not_5_out, not_6_out, not_7_out, Input_4, Input_5);
  and and_3 (and_3_out, not_8_out, not_9_out, Input_3, not_10_out, Input_5);
  and and_4 (and_4_out, not_11_out, not_12_out, Input_4, not_13_out);
  and and_5 (and_5_out, not_14_out, not_15_out, Input_3, not_16_out);
  and and_6 (Output_4, not_17_out, not_18_out, Input_5);
  and and_7 (and_7_out, not_19_out, not_20_out, not_21_out);
  and and_8 (and_8_out, not_22_out, not_23_out, not_24_out, not_25_out);
  and and_9 (and_9_out, not_26_out, not_27_out, not_28_out);
  and and_10 (and_10_out, not_29_out, not_30_out, not_31_out, not_32_out);
  and and_11 (Output_7, not_33_out, not_34_out, Input_5);
  and and_12 (and_12_out, not_35_out, not_36_out, Input_4, not_37_out);
  and and_13 (and_13_out, not_38_out, not_39_out, Input_3, not_40_out);
  and and_14 (and_14_out, not_41_out, not_42_out, not_43_out, Input_4, Input_5);
  and and_15 (and_15_out, not_44_out, not_45_out, Input_3, not_46_out, Input_5);
  and and_16 (Output_10, not_47_out, not_48_out, Input_3, not_49_out, not_50_out);
  or or_1 (Output_2, and_2_out, and_3_out);
  or or_2 (Output_3, and_4_out, and_5_out);
  or or_3 (Output_5, and_7_out, and_8_out);
  or or_4 (Output_6, and_9_out, and_10_out);
  or or_5 (Output_8, and_12_out, and_13_out);
  or or_6 (Output_9, and_14_out, and_15_out);
endmodule

module zoom (
  input  CLK,
  output [9:0] LED_OUT
);

  wire d_ff_1_q, d_ff_2_q, d_ff_3_q, d_ff_4_q, d_ff_5_q, zoom_tl_1_output_1, zoom_tl_1_output_2,
       zoom_tl_1_output_3, zoom_tl_1_output_4, zoom_tl_1_output_5;

  zoom_tl zoom_tl_1 (
    .Input_1(d_ff_1_q), .Input_2(d_ff_2_q), .Input_3(d_ff_3_q), .Input_4(d_ff_4_q), .Input_5(d_ff_5_q),
    .Output_1(zoom_tl_1_output_1), .Output_2(zoom_tl_1_output_2), .Output_3(zoom_tl_1_output_3),
    .Output_4(zoom_tl_1_output_4), .Output_5(zoom_tl_1_output_5));
  D_Flip_Flop d_ff_1 (.D(zoom_tl_1_output_1), .clk(CLK), .Q(d_ff_1_q));  // open: Qn, preset, reset
  D_Flip_Flop d_ff_2 (.D(zoom_tl_1_output_2), .clk(CLK), .Q(d_ff_2_q));  // open: Qn, preset, reset
  D_Flip_Flop d_ff_3 (.D(zoom_tl_1_output_3), .clk(CLK), .Q(d_ff_3_q));  // open: Qn, preset, reset
  D_Flip_Flop d_ff_4 (.D(zoom_tl_1_output_4), .clk(CLK), .Q(d_ff_4_q));  // open: Qn, preset, reset
  D_Flip_Flop d_ff_5 (.D(zoom_tl_1_output_5), .clk(CLK), .Q(d_ff_5_q));  // open: Qn, preset, reset
  zoom_dec zoom_dec_1 (
    .Input_1(d_ff_1_q), .Input_2(d_ff_2_q), .Input_3(d_ff_3_q), .Input_4(d_ff_4_q), .Input_5(d_ff_5_q),
    .Output_1(LED_OUT[0]), .Output_2(LED_OUT[1]), .Output_3(LED_OUT[2]), .Output_4(LED_OUT[3]),
    .Output_5(LED_OUT[4]), .Output_6(LED_OUT[5]), .Output_7(LED_OUT[6]), .Output_8(LED_OUT[7]),
    .Output_9(LED_OUT[8]), .Output_10(LED_OUT[9]));
endmodule
module bounce_tl (
  input  a,
  input  b,
  input  c,
  input  d,
  output x,
  output y,
  output z,
  output u
);

  wire nand_1_out, nand_2_out, nand_3_out, nand_4_out, nand_5_out, nand_6_out, nand_7_out, nand_8_out,
       nand_9_out, nand_10_out, nand_11_out, nand_12_out, nand_13_out, nand_14_out, nand_15_out, nand_16_out,
       nand_17_out, nand_18_out, nand_19_out, nand_20_out, nand_21_out, nand_22_out, nand_23_out,
       nand_24_out, nand_25_out, nand_26_out, nand_27_out, nand_28_out, nand_29_out, nand_30_out,
       nand_31_out, nand_32_out, nand_33_out;

  nand nand_1 (nand_1_out, a, a);
  nand nand_2 (nand_2_out, b, b);
  nand nand_3 (nand_3_out, b, b);
  nand nand_4 (nand_4_out, a, a);
  nand nand_5 (nand_5_out, c, c);
  nand nand_6 (nand_6_out, a, a);
  nand nand_7 (nand_7_out, d, d);
  nand nand_8 (nand_8_out, a, a);
  nand nand_9 (nand_9_out, c, c);
  nand nand_10 (nand_10_out, b, b);
  nand nand_11 (nand_11_out, c, c);
  nand nand_12 (nand_12_out, a, a);
  nand nand_13 (nand_13_out, d, d);
  nand nand_14 (nand_14_out, b, b);
  nand nand_15 (nand_15_out, d, d);
  nand nand_16 (nand_16_out, a, a);
  nand nand_17 (nand_17_out, d, d);
  nand nand_18 (nand_18_out, b, b);
  nand nand_19 (nand_19_out, d, d);
  nand nand_20 (nand_20_out, c, c);
  nand nand_21 (nand_21_out, d, d);
  nand nand_22 (nand_22_out, nand_1_out, b, c, d);
  nand nand_23 (nand_23_out, a, nand_2_out);
  nand nand_24 (nand_24_out, nand_3_out, c, d);
  nand nand_25 (nand_25_out, nand_4_out, b, nand_5_out);
  nand nand_26 (nand_26_out, nand_6_out, b, nand_7_out);
  nand nand_27 (nand_27_out, nand_8_out, nand_9_out, d);
  nand nand_28 (nand_28_out, nand_10_out, nand_11_out, d);
  nand nand_29 (nand_29_out, nand_12_out, c, nand_13_out);
  nand nand_30 (nand_30_out, nand_14_out, c, nand_15_out);
  nand nand_31 (nand_31_out, nand_16_out, nand_17_out);
  nand nand_32 (nand_32_out, nand_18_out, nand_19_out);
  nand nand_33 (nand_33_out, nand_20_out, nand_21_out);
  nand nand_34 (x, nand_22_out, nand_23_out);
  nand nand_35 (y, nand_24_out, nand_25_out, nand_26_out);
  nand nand_36 (z, nand_27_out, nand_28_out, nand_29_out, nand_30_out);
  nand nand_37 (u, nand_31_out, nand_32_out, nand_33_out);
endmodule

module bounce (
  input  CLK,
  output [9:0] LEDOUT
);

  wire bounce_tl_1_u, bounce_tl_1_x, bounce_tl_1_y, bounce_tl_1_z, d_ff_1_q, d_ff_1_qn, d_ff_2_q, d_ff_2_qn,
       d_ff_3_q, d_ff_3_qn, d_ff_4_q, d_ff_4_qn;

  bounce_tl bounce_tl_1 (
    .a(d_ff_1_q), .b(d_ff_2_q), .c(d_ff_3_q), .d(d_ff_4_q), .x(bounce_tl_1_x), .y(bounce_tl_1_y),
    .z(bounce_tl_1_z), .u(bounce_tl_1_u));
  D_Flip_Flop d_ff_1 (.D(bounce_tl_1_x), .clk(CLK), .Q(d_ff_1_q), .Qn(d_ff_1_qn));  // open: preset, reset
  D_Flip_Flop d_ff_2 (.D(bounce_tl_1_y), .clk(CLK), .Q(d_ff_2_q), .Qn(d_ff_2_qn));  // open: preset, reset
  D_Flip_Flop d_ff_3 (.D(bounce_tl_1_z), .clk(CLK), .Q(d_ff_3_q), .Qn(d_ff_3_qn));  // open: preset, reset
  D_Flip_Flop d_ff_4 (.D(bounce_tl_1_u), .clk(CLK), .Q(d_ff_4_q), .Qn(d_ff_4_qn));  // open: preset, reset
  bounce_dec bounce_dec_1 (
    .Input_1(d_ff_1_q), .Input_2(d_ff_2_q), .Input_3(d_ff_3_q), .Input_4(d_ff_4_q), .Output_1(LEDOUT[0]),
    .Output_2(LEDOUT[1]), .Output_3(LEDOUT[2]), .Output_4(LEDOUT[3]), .Output_5(LEDOUT[4]),
    .Output_6(LEDOUT[5]), .Output_7(LEDOUT[6]), .Output_8(LEDOUT[7]), .Output_9(LEDOUT[8]),
    .Output_10(LEDOUT[9]));
endmodule

module bounce_dec (
  input  Input_1,
  input  Input_2,
  input  Input_3,
  input  Input_4,
  output Output_1,
  output Output_2,
  output Output_3,
  output Output_4,
  output Output_5,
  output Output_6,
  output Output_7,
  output Output_8,
  output Output_9,
  output Output_10
);

  wire nand_1_out, nand_2_out, nand_3_out, nand_4_out, nand_5_out, nand_6_out, nand_7_out, nand_8_out,
       nand_9_out, nand_10_out, nand_11_out, nand_12_out, nand_13_out, nand_14_out, nand_15_out, nand_16_out,
       nand_17_out, nand_18_out, nand_19_out, nand_20_out, nand_21_out, nand_22_out, nand_23_out,
       nand_24_out, nand_25_out, nand_26_out, nand_27_out, nand_28_out, nand_29_out, nand_30_out,
       nand_31_out, nand_32_out, nand_33_out, nand_34_out, nand_35_out, nand_36_out, nand_37_out,
       nand_38_out, nand_39_out, nand_40_out, nand_41_out, nand_42_out, nand_43_out, nand_44_out,
       nand_45_out, nand_46_out, nand_47_out, nand_48_out, nand_49_out, nand_50_out, nand_51_out,
       nand_52_out, nand_53_out, nand_54_out, nand_55_out, nand_56_out, nand_57_out, nand_58_out,
       nand_59_out, nand_60_out, nand_61_out, nand_62_out, nand_63_out, nand_64_out, nand_65_out,
       nand_66_out, nand_67_out, nand_68_out, nand_69_out, nand_70_out, nand_71_out, nand_72_out,
       nand_73_out, nand_74_out, nand_75_out, nand_76_out, nand_77_out, nand_78_out, nand_79_out,
       nand_80_out, nand_81_out, nand_82_out, nand_83_out;

  nand nand_1 (nand_1_out, Input_1, Input_1);
  nand nand_2 (nand_2_out, Input_2, Input_2);
  nand nand_3 (nand_3_out, Input_3, Input_3);
  nand nand_4 (nand_4_out, Input_4, Input_4);
  nand nand_5 (nand_5_out, Input_3, Input_3);
  nand nand_6 (nand_6_out, Input_4, Input_4);
  nand nand_7 (nand_7_out, Input_1, Input_1);
  nand nand_8 (nand_8_out, Input_2, Input_2);
  nand nand_9 (nand_9_out, Input_3, Input_3);
  nand nand_10 (nand_10_out, Input_2, Input_2);
  nand nand_11 (nand_11_out, Input_3, Input_3);
  nand nand_12 (nand_12_out, Input_4, Input_4);
  nand nand_13 (nand_13_out, Input_1, Input_1);
  nand nand_14 (nand_14_out, Input_2, Input_2);
  nand nand_15 (nand_15_out, Input_3, Input_3);
  nand nand_16 (nand_16_out, Input_2, Input_2);
  nand nand_17 (nand_17_out, Input_4, Input_4);
  nand nand_18 (nand_18_out, Input_2, Input_2);
  nand nand_19 (nand_19_out, Input_3, Input_3);
  nand nand_20 (nand_20_out, Input_4, Input_4);
  nand nand_21 (nand_21_out, Input_1, Input_1);
  nand nand_22 (nand_22_out, Input_2, Input_2);
  nand nand_23 (nand_23_out, Input_2, Input_2);
  nand nand_24 (nand_24_out, Input_2, Input_2);
  nand nand_25 (nand_25_out, Input_3, Input_3);
  nand nand_26 (nand_26_out, Input_4, Input_4);
  nand nand_27 (nand_27_out, Input_2, Input_2);
  nand nand_28 (nand_28_out, Input_2, Input_2);
  nand nand_29 (nand_29_out, Input_1, Input_1);
  nand nand_30 (nand_30_out, Input_3, Input_3);
  nand nand_31 (nand_31_out, Input_4, Input_4);
  nand nand_32 (nand_32_out, Input_2, Input_2);
  nand nand_33 (nand_33_out, Input_1, Input_1);
  nand nand_34 (nand_34_out, Input_2, Input_2);
  nand nand_35 (nand_35_out, Input_1, Input_1);
  nand nand_36 (nand_36_out, Input_3, Input_3);
  nand nand_37 (nand_37_out, Input_1, Input_1);
  nand nand_38 (nand_38_out, Input_2, Input_2);
  nand nand_39 (nand_39_out, Input_3, Input_3);
  nand nand_40 (nand_40_out, Input_2, Input_2);
  nand nand_41 (nand_41_out, Input_4, Input_4);
  nand nand_42 (nand_42_out, Input_1, Input_1);
  nand nand_43 (nand_43_out, Input_1, Input_1);
  nand nand_44 (nand_44_out, Input_2, Input_2);
  nand nand_45 (nand_45_out, Input_3, Input_3);
  nand nand_46 (nand_46_out, Input_1, Input_1);
  nand nand_47 (nand_47_out, Input_2, Input_2);
  nand nand_48 (nand_48_out, Input_3, Input_3);
  nand nand_49 (nand_49_out, Input_4, Input_4);
  nand nand_50 (nand_50_out, Input_1, Input_1);
  nand nand_51 (nand_51_out, Input_1, Input_1);
  nand nand_52 (nand_52_out, Input_1, Input_1);
  nand nand_53 (nand_53_out, Input_4, Input_4);
  nand nand_54 (nand_54_out, nand_1_out, nand_2_out, nand_3_out, nand_4_out);
  nand nand_55 (nand_55_out, Input_1, Input_2, nand_5_out, nand_6_out);
  nand nand_56 (nand_56_out, nand_7_out, nand_8_out, nand_9_out);
  nand nand_57 (nand_57_out, Input_1, nand_10_out, Input_3, Input_4);
  nand nand_58 (nand_58_out, Input_1, Input_2, nand_11_out, nand_12_out);
  nand nand_59 (nand_59_out, nand_13_out, nand_14_out, nand_15_out);
  nand nand_60 (nand_60_out, nand_16_out, Input_3, nand_17_out);
  nand nand_61 (nand_61_out, Input_1, nand_18_out, Input_3);
  nand nand_62 (nand_62_out, Input_1, Input_2, nand_19_out, nand_20_out);
  nand nand_63 (nand_63_out, nand_21_out, nand_22_out);
  nand nand_64 (nand_64_out, nand_23_out, Input_4);
  nand nand_65 (nand_65_out, nand_24_out, Input_3);
  nand nand_66 (nand_66_out, Input_1, Input_2, nand_25_out, nand_26_out);
  nand nand_67 (nand_67_out, nand_27_out, Input_4);
  nand nand_68 (nand_68_out, nand_28_out, Input_3);
  nand nand_69 (nand_69_out, nand_29_out, Input_2, nand_30_out, nand_31_out);
  nand nand_70 (nand_70_out, Input_1, nand_32_out);
  nand nand_71 (nand_71_out, nand_33_out, nand_34_out, Input_3);
  nand nand_72 (nand_72_out, nand_35_out, Input_2, nand_36_out);
  nand nand_73 (nand_73_out, nand_37_out, Input_2, Input_4);
  nand nand_74 (nand_74_out, Input_1, nand_38_out, nand_39_out);
  nand nand_75 (nand_75_out, Input_1, nand_40_out, nand_41_out);
  nand nand_76 (nand_76_out, nand_42_out, Input_3, Input_4);
  nand nand_77 (nand_77_out, nand_43_out, Input_2);
  nand nand_78 (nand_78_out, Input_1, nand_44_out, nand_45_out);
  nand nand_79 (nand_79_out, nand_46_out, Input_2);
  nand nand_80 (nand_80_out, Input_1, nand_47_out, nand_48_out, nand_49_out);
  nand nand_81 (nand_81_out, nand_50_out, Input_2, Input_4);
  nand nand_82 (nand_82_out, nand_51_out, Input_2, Input_3);
  nand nand_83 (nand_83_out, nand_52_out, Input_2, Input_3, nand_53_out);
  nand nand_84 (Output_1, nand_54_out, nand_55_out);
  nand nand_85 (Output_2, nand_56_out, nand_57_out, nand_58_out);
  nand nand_86 (Output_3, nand_59_out, nand_60_out, nand_61_out, nand_62_out);
  nand nand_87 (Output_4, nand_63_out, nand_64_out, nand_65_out, nand_66_out);
  nand nand_88 (Output_5, nand_67_out, nand_68_out, nand_69_out, nand_70_out);
  nand nand_89 (Output_6, nand_71_out, nand_72_out, nand_73_out, nand_74_out, nand_75_out);
  nand nand_90 (Output_7, nand_76_out, nand_77_out, nand_78_out);
  nand nand_91 (Output_8, nand_79_out, nand_80_out);
  nand nand_92 (Output_9, nand_81_out, nand_82_out);
  nand nand_93 (Output_10, nand_83_out, nand_83_out);
endmodule

module bump_tl (
  input  Input_1,
  input  Input_2,
  input  Input_3,
  output Output_1,
  output Output_2,
  output Output_3
);

  wire nand_1_out, nand_2_out, nand_3_out, nand_4_out, nand_5_out, nand_7_out, nand_8_out, nand_9_out,
       nand_10_out, nand_11_out;

  nand nand_1 (nand_1_out, Input_1, Input_1);
  nand nand_2 (nand_2_out, Input_2, Input_2);
  nand nand_3 (nand_3_out, Input_3, Input_3);
  nand nand_4 (nand_4_out, Input_2, Input_2);
  nand nand_5 (nand_5_out, Input_3, Input_3);
  nand nand_6 (Output_3, Input_3, Input_3);
  nand nand_7 (nand_7_out, nand_1_out, Input_2, Input_3);
  nand nand_8 (nand_8_out, Input_1, nand_2_out);
  nand nand_9 (nand_9_out, Input_1, nand_3_out);
  nand nand_10 (nand_10_out, nand_4_out, Input_3);
  nand nand_11 (nand_11_out, Input_2, nand_5_out);
  nand nand_12 (Output_1, nand_7_out, nand_8_out, nand_9_out);
  nand nand_13 (Output_2, nand_10_out, nand_11_out);
endmodule

module bump_dec (
  input  Input_1,
  input  Input_2,
  input  Input_3,
  output Output_1,
  output Output_2,
  output Output_3,
  output Output_4,
  output Output_5,
  output Output_6,
  output Output_7,
  output Output_8,
  output Output_9,
  output Output_10
);

  wire nand_1_out, nand_2_out, nand_3_out, nand_4_out, nand_5_out, nand_6_out, nand_7_out, nand_8_out,
       nand_9_out, nand_10_out, nand_11_out, nand_12_out, nand_13_out, nand_14_out, nand_15_out, nand_16_out,
       nand_17_out, nand_18_out, nand_19_out, nand_20_out, nand_21_out, nand_22_out, nand_23_out,
       nand_24_out, nand_25_out, nand_26_out, nand_27_out, nand_28_out, nand_29_out, nand_30_out,
       nand_32_out, nand_33_out, nand_34_out, nand_35_out, nand_36_out, nand_37_out, nand_38_out,
       nand_39_out, nand_40_out, nand_41_out, nand_42_out, nand_43_out, nand_44_out, nand_45_out,
       nand_46_out, nand_47_out;

  nand nand_1 (nand_1_out, Input_1, Input_1);
  nand nand_2 (nand_2_out, Input_2, Input_2);
  nand nand_3 (nand_3_out, Input_3, Input_3);
  nand nand_4 (nand_4_out, Input_1, Input_1);
  nand nand_5 (nand_5_out, Input_1, Input_1);
  nand nand_6 (nand_6_out, Input_2, Input_2);
  nand nand_7 (nand_7_out, Input_3, Input_3);
  nand nand_8 (nand_8_out, Input_1, Input_1);
  nand nand_9 (nand_9_out, Input_1, Input_1);
  nand nand_10 (nand_10_out, Input_2, Input_2);
  nand nand_11 (nand_11_out, Input_3, Input_3);
  nand nand_12 (nand_12_out, Input_3, Input_3);
  nand nand_13 (nand_13_out, Input_1, Input_1);
  nand nand_14 (nand_14_out, Input_1, Input_1);
  nand nand_15 (nand_15_out, Input_2, Input_2);
  nand nand_16 (nand_16_out, Input_2, Input_2);
  nand nand_17 (nand_17_out, Input_3, Input_3);
  nand nand_18 (nand_18_out, Input_2, Input_2);
  nand nand_19 (nand_19_out, Input_1, Input_1);
  nand nand_20 (nand_20_out, Input_3, Input_3);
  nand nand_21 (nand_21_out, Input_1, Input_1);
  nand nand_22 (nand_22_out, Input_2, Input_2);
  nand nand_23 (nand_23_out, Input_1, Input_1);
  nand nand_24 (nand_24_out, Input_2, Input_2);
  nand nand_25 (nand_25_out, Input_3, Input_3);
  nand nand_26 (nand_26_out, Input_1, Input_1);
  nand nand_27 (nand_27_out, nand_1_out, nand_2_out, nand_3_out);
  nand nand_28 (nand_28_out, nand_4_out, Input_2, Input_3);
  nand nand_29 (nand_29_out, nand_5_out, nand_6_out);
  nand nand_30 (nand_30_out, Input_3, Input_3);
  nand nand_31 (Output_3, nand_7_out, nand_8_out);
  nand nand_32 (nand_32_out, nand_9_out, nand_10_out, Input_3);
  nand nand_33 (nand_33_out, Input_2, nand_11_out);
  nand nand_34 (nand_34_out, Input_1, nand_12_out);
  nand nand_35 (nand_35_out, nand_13_out, Input_2);
  nand nand_36 (nand_36_out, nand_14_out, Input_2);
  nand nand_37 (nand_37_out, Input_1, nand_15_out, Input_3);
  nand nand_38 (nand_38_out, nand_16_out, Input_3);
  nand nand_39 (nand_39_out, Input_2, nand_17_out);
  nand nand_40 (nand_40_out, Input_1, nand_18_out);
  nand nand_41 (nand_41_out, nand_19_out, Input_3);
  nand nand_42 (nand_42_out, Input_1, nand_20_out);
  nand nand_43 (nand_43_out, Input_1, Input_2);
  nand nand_44 (nand_44_out, nand_21_out, nand_22_out);
  nand nand_45 (nand_45_out, Input_2, Input_3);
  nand nand_46 (nand_46_out, nand_23_out, nand_24_out, nand_25_out);
  nand nand_47 (nand_47_out, nand_26_out, Input_2, Input_3);
  nand nand_48 (Output_1, nand_27_out, nand_28_out);
  nand nand_49 (Output_2, nand_29_out, nand_30_out);
  nand nand_50 (Output_4, nand_32_out, nand_33_out, nand_34_out);
  nand nand_51 (Output_5, nand_35_out, nand_35_out);
  nand nand_52 (Output_6, nand_36_out, nand_37_out);
  nand nand_53 (Output_7, nand_38_out, nand_39_out, nand_40_out);
  nand nand_54 (Output_8, nand_41_out, nand_42_out, nand_43_out);
  nand nand_55 (Output_9, nand_44_out, nand_45_out);
  nand nand_56 (Output_10, nand_46_out, nand_47_out);
endmodule

module bump (
  input  CLK,
  output [9:0] LEDOUT
);

  wire bump_tl_1_output_1, bump_tl_1_output_2, bump_tl_1_output_3, d_ff_1_q, d_ff_2_q, d_ff_3_q;

  bump_tl bump_tl_1 (
    .Input_1(d_ff_1_q), .Input_2(d_ff_2_q), .Input_3(d_ff_3_q), .Output_1(bump_tl_1_output_1),
    .Output_2(bump_tl_1_output_2), .Output_3(bump_tl_1_output_3));
  D_Flip_Flop d_ff_1 (.D(bump_tl_1_output_1), .clk(CLK), .Q(d_ff_1_q));  // open: Qn, preset, reset
  D_Flip_Flop d_ff_2 (.D(bump_tl_1_output_2), .clk(CLK), .Q(d_ff_2_q));  // open: Qn, preset, reset
  D_Flip_Flop d_ff_3 (.D(bump_tl_1_output_3), .clk(CLK), .Q(d_ff_3_q));  // open: Qn, preset, reset
  bump_dec bump_dec_1 (
    .Input_1(d_ff_1_q), .Input_2(d_ff_2_q), .Input_3(d_ff_3_q), .Output_1(LEDOUT[0]), .Output_2(LEDOUT[1]),
    .Output_3(LEDOUT[2]), .Output_4(LEDOUT[3]), .Output_5(LEDOUT[4]), .Output_6(LEDOUT[5]),
    .Output_7(LEDOUT[6]), .Output_8(LEDOUT[7]), .Output_9(LEDOUT[8]), .Output_10(LEDOUT[9]));
endmodule

module COUNTDOWN (
  input  EN,
  input  UP,
  input  DN,
  input  CLICK,
  input  CLK_SEC,
  input  CLK,
  output [5:0] DISP0,
  output [5:0] DISP1,
  output [5:0] DISP2,
  output [5:0] DISP3,
  output [5:0] DISP4,
  output [5:0] DISP5
);

  wire and_1_out, and_2_out, and_3_out, base60_count_1_cout, demultiplexer_1_out0, demultiplexer_2_out0,
       detect_pos_edge_2_pos_edge, not_1_out, or_1_out, or_2_out, or_3_out, or_4_out, por, sel, sel_mode,
       t_ff_1_q, undriven;
  wire [1:0] txtFSM_1_txt;
  wire [5:0] and_4_out, base60_count_1_val, base_100_count_1_val, bit_extender_1_out,
       decod_tens_units_1_tens, decod_tens_units_1_unites, decod_tens_units_2_tens,
       decod_tens_units_2_unites, or_5_out;

  Counter #(.width(1), .max('h1)) counter_1 (.up(1'b1), .clk(and_1_out), .carry(sel));  // open: clr, load, count, D, Q
  and and_1 (and_1_out, sel_mode, CLICK);
  Demultiplexer #(.enable("false")) demultiplexer_1 (.out0(demultiplexer_1_out0), .in(UP), .sel(sel));  // open: out1
  Demultiplexer #(.enable("false")) demultiplexer_2 (.out0(demultiplexer_2_out0), .in(DN), .sel(sel));  // open: out1
  detect_pos_edge detect_pos_edge_1 (.in_in(EN), .clk(CLK), .pos_edge(por));
  detect_pos_edge detect_pos_edge_2 (.in_in(CLICK), .clk(CLK), .pos_edge(detect_pos_edge_2_pos_edge));
  and and_2 (and_2_out, undriven, t_ff_1_q);
  T_Flip_Flop t_ff_1 (.T(1'b1), .clk(or_1_out), .Q(t_ff_1_q), .reset(por));  // open: Qn, preset
  or or_1 (or_1_out, and_2_out, detect_pos_edge_2_pos_edge);
  or or_2 (or_2_out, demultiplexer_1_out0, base60_count_1_cout, demultiplexer_2_out0);
  T_Flip_Flop t_ff_2 (.T(1'b1), .clk(undriven), .Q(sel_mode), .reset(por));  // open: Qn, preset
  not not_1 (not_1_out, sel_mode);
  and and_3 (and_3_out, t_ff_1_q, CLK_SEC);
  buf or_3 (or_3_out, demultiplexer_2_out0);  // OR_Gate
  base_100_count base_100_count_1 (
    .RST(1'b0), .UP_ND(or_3_out), .CIN(or_2_out), .SET(1'b0), .VAL(base_100_count_1_val));  // open: SVAL, COUT
  base60_count base60_count_1 (
    .RST(1'b0), .UP_DN(1'b1), .CIN(and_3_out), .CLK(CLK), .COUT(base60_count_1_cout), .VAL(base60_count_1_val));
  txtFSM txtFSM_1 (.EN(EN), .CLK(CLK), .TXT(txtFSM_1_txt));
  decod_tens_units decod_tens_units_1 (
    .nb_in(base_100_count_1_val), .tens(decod_tens_units_1_tens), .unites(decod_tens_units_1_unites));
  or or_4 (or_4_out, CLK_SEC, ~t_ff_1_q);  // OR_Gate
  decod_tens_units decod_tens_units_2 (
    .nb_in(base60_count_1_val), .tens(decod_tens_units_2_tens), .unites(decod_tens_units_2_unites));
  assign and_4_out = 6'b100000 & bit_extender_1_out;  // AND_Gate and_4, 6 bits wide
  assign bit_extender_1_out = {{5{or_4_out}}, or_4_out};  // Bit_Extender bit_extender_1
  assign or_5_out = decod_tens_units_1_unites | and_4_out;  // OR_Gate or_5, 6 bits wide
  Multiplexer #(.select(2), .width(6), .enable("false")) multiplexer_1 (
    .in0(6'b011111), .in1(6'b001100), .in2(6'b001100), .in3(6'b001100), .out(DISP0), .sel(txtFSM_1_txt));
  Multiplexer #(.select(2), .width(6), .enable("false")) multiplexer_2 (
    .in0(6'b011111), .in1(6'b010110), .in2(6'b110001), .in3(6'b110001), .out(DISP1), .sel(txtFSM_1_txt));
  Multiplexer #(.select(2), .width(6), .enable("false")) multiplexer_3 (
    .in0(6'b011111), .in1(6'b011100), .in2(decod_tens_units_1_tens), .in3(decod_tens_units_1_tens),
    .out(DISP2), .sel(txtFSM_1_txt));
  Multiplexer #(.select(2), .width(6), .enable("false")) multiplexer_4 (
    .in0(6'b011111), .in1(6'b001101), .in2(or_5_out), .in3(or_5_out), .out(DISP3), .sel(txtFSM_1_txt));
  Multiplexer #(.select(2), .width(6), .enable("false")) multiplexer_5 (
    .in0(6'b011111), .in1(6'b010110), .in2(decod_tens_units_2_tens), .in3(decod_tens_units_2_tens),
    .out(DISP4), .sel(txtFSM_1_txt));
  Multiplexer #(.select(2), .width(6), .enable("false")) multiplexer_6 (
    .in0(6'b011111), .in1(6'b011111), .in2(decod_tens_units_2_unites), .in3(decod_tens_units_2_unites),
    .out(DISP5), .sel(txtFSM_1_txt));
endmodule

module wait_pm_debounce (
  input  in_in,
  input  clk,
  input  rst,
  output out_out
);

  wire and_1_out, d_ff_1_q, d_ff_2_q, d_ff_3_q, not_1_out;

  D_Flip_Flop d_ff_1 (.D(in_in), .clk(clk), .Q(d_ff_1_q), .reset(rst));  // open: Qn, preset
  not not_1 (not_1_out, in_in);
  D_Flip_Flop d_ff_2 (.D(d_ff_1_q), .clk(clk), .Q(d_ff_2_q), .reset(rst));  // open: Qn, preset
  D_Flip_Flop d_ff_3 (.D(d_ff_2_q), .clk(clk), .Q(d_ff_3_q), .reset(rst));  // open: Qn, preset
  D_Flip_Flop d_ff_4 (.D(d_ff_3_q), .clk(clk), .reset(rst));  // open: Q, Qn, preset
  and and_1 (and_1_out, d_ff_1_q, d_ff_2_q, d_ff_3_q);
  S_R_Flip_Flop s_r_ff_1 (.Q(out_out), .reset(not_1_out), .preset(and_1_out));  // open: S, R, clk, Qn
endmodule

module FUN (
  input  EN,
  output [9:0] leds,
  output buzz
);

  wire clock_1_out, clock_2_out;
  wire [1:0] bit_extender_1_out;

  Clock #(.highDuration(10000), .lowDuration(10000)) clock_1 (.out(clock_1_out));
  assign bit_extender_1_out = {{1{clock_1_out}}, clock_1_out};  // Bit_Extender bit_extender_1
  Clock #(.highDuration(500)) clock_2 (.out(clock_2_out));
  musique musique_1 (.EN(EN), .clk(clock_2_out), .TONE(buzz));
  LED_Anim LED_Anim_1 (.EN(EN), .SLO_CLK(clock_2_out), .SEL(bit_extender_1_out), .LEDOUT(leds));
endmodule

module musique (
  input  EN,
  input  clk,
  output TONE
);

  wire clock_1_out, clock_2_out, clock_3_out, clock_4_out, clock_5_out, clock_6_out, clock_7_out,
       clock_8_out, clock_9_out, clock_10_out, clock_11_out, clock_12_out, clock_13_out, clock_14_out,
       clock_15_out, clock_16_out, multiplexer_1_out;
  wire [3:0] random_1_out;

  Random #(.width(4)) random_1 (.clr(1'b0), .clk(clk), .out(random_1_out));  // open: next
  Clock clock_1 (.out(clock_1_out));
  Clock #(.highDuration(2), .lowDuration(2)) clock_2 (.out(clock_2_out));
  Clock #(.highDuration(3), .lowDuration(3)) clock_3 (.out(clock_3_out));
  Clock #(.highDuration(4), .lowDuration(4)) clock_4 (.out(clock_4_out));
  Clock #(.highDuration(5), .lowDuration(5)) clock_5 (.out(clock_5_out));
  Clock #(.highDuration(6), .lowDuration(6)) clock_6 (.out(clock_6_out));
  Clock #(.highDuration(7), .lowDuration(7)) clock_7 (.out(clock_7_out));
  Clock #(.highDuration(8), .lowDuration(8)) clock_8 (.out(clock_8_out));
  Clock #(.highDuration(9), .lowDuration(9)) clock_9 (.out(clock_9_out));
  Clock #(.highDuration(10), .lowDuration(10)) clock_10 (.out(clock_10_out));
  Clock #(.highDuration(11), .lowDuration(11)) clock_11 (.out(clock_11_out));
  Clock #(.highDuration(12), .lowDuration(12)) clock_12 (.out(clock_12_out));
  Clock #(.highDuration(13), .lowDuration(2)) clock_13 (.out(clock_13_out));
  Clock #(.highDuration(13), .lowDuration(2)) clock_14 (.out(clock_14_out));
  Clock #(.highDuration(14), .lowDuration(14)) clock_15 (.out(clock_15_out));
  Clock #(.highDuration(15), .lowDuration(15)) clock_16 (.out(clock_16_out));
  Multiplexer #(.select(4), .enable("false")) multiplexer_1 (
    .in0(clock_1_out), .in1(clock_2_out), .in2(clock_3_out), .in3(clock_4_out), .in4(clock_5_out),
    .in5(clock_6_out), .in6(clock_7_out), .in7(clock_8_out), .in8(clock_9_out), .in9(clock_10_out),
    .in10(clock_11_out), .in11(clock_12_out), .in12(clock_13_out), .in13(clock_14_out), .in14(clock_15_out),
    .in15(clock_16_out), .out(multiplexer_1_out), .sel(random_1_out));
  and and_1 (TONE, EN, multiplexer_1_out);
endmodule
