// Logisim project TONETEST.circ as structural Verilog: 1 circuit, main circuit main
module main (
  output TONE
);

  wire clock_1_out, clock_2_out, clock_3_out, clock_4_out, clock_5_out, clock_6_out, clock_7_out,
       clock_8_out, clock_9_out, clock_10_out, clock_11_out, clock_12_out, clock_13_out, clock_14_out,
       clock_15_out, clock_16_out, EN_out, multiplexer_1_out, RST_out;
  wire [3:0] random_1_out;

  Button RST (.out(RST_out));
  Button EN (.out(EN_out));
  Random #(.width(4)) random_1 (.clr(RST_out), .clk(clock_1_out), .out(random_1_out));  // open: next
  Clock clock_1 (.out(clock_1_out));
  Clock #(.highDuration(2), .lowDuration(2)) clock_2 (.out(clock_2_out));
  Clock #(.highDuration(3), .lowDuration(3)) clock_3 (.out(clock_3_out));
  Clock #(.highDuration(4), .lowDuration(4)) clock_4 (.out(clock_4_out));
  Clock #(.highDuration(5), .lowDuration(5)) clock_5 (.out(clock_5_out));
  Clock #(.highDuration(6), .lowDuration(6)) clock_6 (.out(clock_6_out));
  Clock #(.highDuration(7), .lowDuration(7)) clock_7 (.out(clock_7_out));
  Clock #(.highDuration(8), .lowDuration(8)) clock_8 (.out(clock_8_out));
  Clock #(.highDuration(9), .lowDuration(9)) clock_9 (.out(clock_9_out));
  Clock #(.highDuration(10), .lowDuration(10)) clock_10 (.out(clock_10_out));
  Clock #(.highDuration(11), .lowDuration(11)) clock_11 (.out(clock_11_out));
  Clock #(.highDuration(12), .lowDuration(12)) clock_12 (.out(clock_12_out));
  Clock #(.highDuration(13), .lowDuration(2)) clock_13 (.out(clock_13_out));
  Clock #(.highDuration(13), .lowDuration(2)) clock_14 (.out(clock_14_out));
  Clock #(.highDuration(14), .lowDuration(14)) clock_15 (.out(clock_15_out));
  Clock #(.highDuration(15), .lowDuration(15)) clock_16 (.out(clock_16_out));
  Multiplexer #(.select(4), .enable("false")) multiplexer_1 (
    .in0(clock_1_out), .in1(clock_2_out), .in2(clock_3_out), .in3(clock_4_out), .in4(clock_5_out),
    .in5(clock_6_out), .in6(clock_7_out), .in7(clock_8_out), .in8(clock_9_out), .in9(clock_10_out),
    .in10(clock_11_out), .in11(clock_12_out), .in12(clock_13_out), .in13(clock_14_out), .in14(clock_15_out),
    .in15(clock_16_out), .out(multiplexer_1_out), .sel(random_1_out));
  and and_1 (TONE, EN_out, multiplexer_1_out);
endmodule
