// Logisim project ledanim.circ as structural Verilog: 11 circuits, main circuit LED_Anim
module LED_Anim (
  input  EN,
  input  SLO_CLK,
  input  [1:0] SEL,
  output [9:0] LEDOUT
);

  wire and_1_out;
  wire [9:0] bounce_1_ledout, bump_1_ledout, circus_1_ledout, zoom_1_led_out;

  and and_1 (and_1_out, EN, SLO_CLK);
  circus circus_1 (.CLK(and_1_out), .LEDOUT(circus_1_ledout));
  zoom zoom_1 (.CLK(and_1_out), .LED_OUT(zoom_1_led_out));
  bounce bounce_1 (.CLK(and_1_out), .LEDOUT(bounce_1_ledout));
  bump bump_1 (.CLK(and_1_out), .LEDOUT(bump_1_ledout));
  Multiplexer #(.select(2), .width(10), .enable("false")) multiplexer_1 (
    .in0(circus_1_ledout), .in1(zoom_1_led_out), .in2(bounce_1_ledout), .in3(bump_1_ledout), .out(LEDOUT),
    .sel(SEL));
endmodule

module circus (
  input  CLK,
  output [9:0] LEDOUT
);

  wire d_ff_1_qn;

  D_Flip_Flop d_ff_1 (.D(d_ff_1_qn), .clk(CLK), .Q(LEDOUT[9]), .Qn(d_ff_1_qn));  // open: preset, reset
  not not_1 (LEDOUT[0], LEDOUT[9]);
  not not_2 (LEDOUT[2], LEDOUT[9]);
  not not_3 (LEDOUT[4], LEDOUT[9]);
  not not_4 (LEDOUT[6], LEDOUT[9]);
  not not_5 (LEDOUT[8], LEDOUT[9]);

  assign {LEDOUT[7], LEDOUT[5], LEDOUT[3], LEDOUT[1]} = {4{LEDOUT[9]}};
endmodule

module zoom_tl (
  input  Input_1,
  input  Input_2,
  input  Input_3,
  input  Input_4,
  input  Input_5,
  output Output_1,
  output Output_2,
  output Output_3,
  output Output_4,
  output Output_5
);

  wire and_1_out, and_2_out, and_3_out, and_4_out, and_5_out, and_6_out, and_7_out, and_8_out, and_9_out,
       not_1_out, not_2_out, not_3_out, not_4_out, not_5_out, not_6_out, not_7_out, not_8_out, not_9_out,
       not_10_out, not_11_out, not_12_out, not_13_out, not_14_out, not_15_out, not_16_out, not_17_out,
       not_18_out, not_19_out, not_20_out, not_21_out, not_22_out, not_23_out, not_24_out, not_25_out,
       not_26_out, not_27_out, not_28_out;

  not not_1 (not_1_out, Input_1);
  not not_2 (not_2_out, Input_2);
  not not_3 (not_3_out, Input_1);
  not not_4 (not_4_out, Input_3);
  not not_5 (not_5_out, Input_4);
  not not_6 (not_6_out, Input_5);
  not not_7 (not_7_out, Input_1);
  not not_8 (not_8_out, Input_2);
  not not_9 (not_9_out, Input_3);
  not not_10 (not_10_out, Input_1);
  not not_11 (not_11_out, Input_2);
  not not_12 (not_12_out, Input_4);
  not not_13 (not_13_out, Input_1);
  not not_14 (not_14_out, Input_2);
  not not_15 (not_15_out, Input_5);
  not not_16 (not_16_out, Input_1);
  not not_17 (not_17_out, Input_2);
  not not_18 (not_18_out, Input_4);
  not not_19 (not_19_out, Input_1);
  not not_20 (not_20_out, Input_2);
  not not_21 (not_21_out, Input_5);
  not not_22 (not_22_out, Input_1);
  not not_23 (not_23_out, Input_2);
  not not_24 (not_24_out, Input_5);
  not not_25 (not_25_out, Input_1);
  not not_26 (not_26_out, Input_3);
  not not_27 (not_27_out, Input_4);
  not not_28 (not_28_out, Input_5);
  and and_1 (and_1_out, not_1_out, not_2_out, Input_3, Input_4, Input_5);
  and and_2 (and_2_out, not_3_out, Input_2, not_4_out, not_5_out, not_6_out);
  and and_3 (and_3_out, not_7_out, not_8_out, not_9_out, Input_4, Input_5);
  and and_4 (and_4_out, not_10_out, not_11_out, Input_3, not_12_out);
  and and_5 (and_5_out, not_13_out, not_14_out, Input_3, not_15_out);
  and and_6 (and_6_out, not_16_out, not_17_out, not_18_out, Input_5);
  and and_7 (and_7_out, not_19_out, not_20_out, Input_4, not_21_out);
  and and_8 (and_8_out, not_22_out, not_23_out, not_24_out);
  and and_9 (and_9_out, not_25_out, not_26_out, not_27_out, not_28_out);
  or or_1 (Output_2, and_1_out, and_2_out);
  or or_2 (Output_3, and_3_out, and_4_out, and_5_out);
  or or_3 (Output_4, and_6_out, and_7_out);
  or or_4 (Output_5, and_8_out, and_9_out);

  assign Output_1 = 1'b0;
endmodule

module zoom_dec (
  input  Input_1,
  input  Input_2,
  input  Input_3,
  input  Input_4,
  input  Input_5,
  output Output_1,
  output Output_2,
  output Output_3,
  output Output_4,
  output Output_5,
  output Output_6,
  output Output_7,
  output Output_8,
  output Output_9,
  output Output_10
);

  wire and_2_out, and_3_out, and_4_out, and_5_out, and_7_out, and_8_out, and_9_out, and_10_out, and_12_out,
       and_13_out, and_14_out, and_15_out, not_1_out, not_2_out, not_3_out, not_4_out, not_5_out, not_6_out,
       not_7_out, not_8_out, not_9_out, not_10_out, not_11_out, not_12_out, not_13_out, not_14_out,
       not_15_out, not_16_out, not_17_out, not_18_out, not_19_out, not_20_out, not_21_out, not_22_out,
       not_23_out, not_24_out, not_25_out, not_26_out, not_27_out, not_28_out, not_29_out, not_30_out,
       not_31_out, not_32_out, not_33_out, not_34_out, not_35_out, not_36_out, not_37_out, not_38_out,
       not_39_out, not_40_out, not_41_out, not_42_out, not_43_out, not_44_out, not_45_out, not_46_out,
       not_47_out, not_48_out, not_49_out, not_50_out;

  not not_1 (not_1_out, Input_1);
  not not_2 (not_2_out, Input_2);
  not not_3 (not_3_out, Input_4);
  not not_4 (not_4_out, Input_5);
  not not_5 (not_5_out, Input_1);
  not not_6 (not_6_out, Input_2);
  not not_7 (not_7_out, Input_3);
  not not_8 (not_8_out, Input_1);
  not not_9 (not_9_out, Input_2);
  not not_10 (not_10_out, Input_4);
  not not_11 (not_11_out, Input_1);
  not not_12 (not_12_out, Input_2);
  not not_13 (not_13_out, Input_5);
  not not_14 (not_14_out, Input_1);
  not not_15 (not_15_out, Input_2);
  not not_16 (not_16_out, Input_5);
  not not_17 (not_17_out, Input_1);
  not not_18 (not_18_out, Input_2);
  not not_19 (not_19_out, Input_1);
  not not_20 (not_20_out, Input_2);
  not not_21 (not_21_out, Input_5);
  not not_22 (not_22_out, Input_1);
  not not_23 (not_23_out, Input_3);
  not not_24 (not_24_out, Input_4);
  not not_25 (not_25_out, Input_5);
  not not_26 (not_26_out, Input_1);
  not not_27 (not_27_out, Input_2);
  not not_28 (not_28_out, Input_5);
  not not_29 (not_29_out, Input_1);
  not not_30 (not_30_out, Input_3);
  not not_31 (not_31_out, Input_4);
  not not_32 (not_32_out, Input_5);
  not not_33 (not_33_out, Input_1);
  not not_34 (not_34_out, Input_2);
  not not_35 (not_35_out, Input_1);
  not not_36 (not_36_out, Input_2);
  not not_37 (not_37_out, Input_5);
  not not_38 (not_38_out, Input_1);
  not not_39 (not_39_out, Input_2);
  not not_40 (not_40_out, Input_5);
  not not_41 (not_41_out, Input_1);
  not not_42 (not_42_out, Input_2);
  not not_43 (not_43_out, Input_3);
  not not_44 (not_44_out, Input_1);
  not not_45 (not_45_out, Input_2);
  not not_46 (not_46_out, Input_4);
  not not_47 (not_47_out, Input_1);
  not not_48 (not_48_out, Input_2);
  not not_49 (not_49_out, Input_4);
  not not_50 (not_50_out, Input_5);
  and and_1 (Output_1, not_1_out, not_2_out, Input_3, not_3_out, not_4_out);
  and and_2 (and_2_out, not_5_out, not_6_out, not_7_out, Input_4, Input_5);
  and and_3 (and_3_out, not_8_out, not_9_out, Input_3, not_10_out, Input_5);
  and and_4 (and_4_out, not_11_out, not_12_out, Input_4, not_13_out);
  and and_5 (and_5_out, not_14_out, not_15_out, Input_3, not_16_out);
  and and_6 (Output_4, not_17_out, not_18_out, Input_5);
  and and_7 (and_7_out, not_19_out, not_20_out, not_21_out);
  and and_8 (and_8_out, not_22_out, not_23_out, not_24_out, not_25_out);
  and and_9 (and_9_out, not_26_out, not_27_out, not_28_out);
  and and_10 (and_10_out, not_29_out, not_30_out, not_31_out, not_32_out);
  and and_11 (Output_7, not_33_out, not_34_out, Input_5);
  and and_12 (and_12_out, not_35_out, not_36_out, Input_4, not_37_out);
  and and_13 (and_13_out, not_38_out, not_39_out, Input_3, not_40_out);
  and and_14 (and_14_out, not_41_out, not_42_out, not_43_out, Input_4, Input_5);
  and and_15 (and_15_out, not_44_out, not_45_out, Input_3, not_46_out, Input_5);
  and and_16 (Output_10, not_47_out, not_48_out, Input_3, not_49_out, not_50_out);
  or or_1 (Output_2, and_2_out, and_3_out);
  or or_2 (Output_3, and_4_out, and_5_out);
  or or_3 (Output_5, and_7_out, and_8_out);
  or or_4 (Output_6, and_9_out, and_10_out);
  or or_5 (Output_8, and_12_out, and_13_out);
  or or_6 (Output_9, and_14_out, and_15_out);
endmodule

module zoom (
  input  CLK,
  output [9:0] LED_OUT
);

  wire d_ff_1_q, d_ff_2_q, d_ff_3_q, d_ff_4_q, d_ff_5_q, zoom_tl_1_output_1, zoom_tl_1_output_2,
       zoom_tl_1_output_3, zoom_tl_1_output_4, zoom_tl_1_output_5;

  zoom_tl zoom_tl_1 (
    .Input_1(d_ff_1_q), .Input_2(d_ff_2_q), .Input_3(d_ff_3_q), .Input_4(d_ff_4_q), .Input_5(d_ff_5_q),
    .Output_1(zoom_tl_1_output_1), .Output_2(zoom_tl_1_output_2), .Output_3(zoom_tl_1_output_3),
    .Output_4(zoom_tl_1_output_4), .Output_5(zoom_tl_1_output_5));
  D_Flip_Flop d_ff_1 (.D(zoom_tl_1_output_1), .clk(CLK), .Q(d_ff_1_q));  // open: Qn, preset, reset
  D_Flip_Flop d_ff_2 (.D(zoom_tl_1_output_2), .clk(CLK), .Q(d_ff_2_q));  // open: Qn, preset, reset
  D_Flip_Flop d_ff_3 (.D(zoom_tl_1_output_3), .clk(CLK), .Q(d_ff_3_q));  // open: Qn, preset, reset
  D_Flip_Flop d_ff_4 (.D(zoom_tl_1_output_4), .clk(CLK), .Q(d_ff_4_q));  // open: Qn, preset, reset
  D_Flip_Flop d_ff_5 (.D(zoom_tl_1_output_5), .clk(CLK), .Q(d_ff_5_q));  // open: Qn, preset, reset
  zoom_dec zoom_dec_1 (
    .Input_1(d_ff_1_q), .Input_2(d_ff_2_q), .Input_3(d_ff_3_q), .Input_4(d_ff_4_q), .Input_5(d_ff_5_q),
    .Output_1(LED_OUT[0]), .Output_2(LED_OUT[1]), .Output_3(LED_OUT[2]), .Output_4(LED_OUT[3]),
    .Output_5(LED_OUT[4]), .Output_6(LED_OUT[5]), .Output_7(LED_OUT[6]), .Output_8(LED_OUT[7]),
    .Output_9(LED_OUT[8]), .Output_10(LED_OUT[9]));
endmodule

module bounce_tl (
  input  a,
  input  b,
  input  c,
  input  d,
  output x,
  output y,
  output z,
  output u
);

  wire nand_1_out, nand_2_out, nand_3_out, nand_4_out, nand_5_out, nand_6_out, nand_7_out, nand_8_out,
       nand_9_out, nand_10_out, nand_11_out, nand_12_out, nand_13_out, nand_14_out, nand_15_out, nand_16_out,
       nand_17_out, nand_18_out, nand_19_out, nand_20_out, nand_21_out, nand_22_out, nand_23_out,
       nand_24_out, nand_25_out, nand_26_out, nand_27_out, nand_28_out, nand_29_out, nand_30_out,
       nand_31_out, nand_32_out, nand_33_out;

  nand nand_1 (nand_1_out, a, a);
  nand nand_2 (nand_2_out, b, b);
  nand nand_3 (nand_3_out, b, b);
  nand nand_4 (nand_4_out, a, a);
  nand nand_5 (nand_5_out, c, c);
  nand nand_6 (nand_6_out, a, a);
  nand nand_7 (nand_7_out, d, d);
  nand nand_8 (nand_8_out, a, a);
  nand nand_9 (nand_9_out, c, c);
  nand nand_10 (nand_10_out, b, b);
  nand nand_11 (nand_11_out, c, c);
  nand nand_12 (nand_12_out, a, a);
  nand nand_13 (nand_13_out, d, d);
  nand nand_14 (nand_14_out, b, b);
  nand nand_15 (nand_15_out, d, d);
  nand nand_16 (nand_16_out, a, a);
  nand nand_17 (nand_17_out, d, d);
  nand nand_18 (nand_18_out, b, b);
  nand nand_19 (nand_19_out, d, d);
  nand nand_20 (nand_20_out, c, c);
  nand nand_21 (nand_21_out, d, d);
  nand nand_22 (nand_22_out, nand_1_out, b, c, d);
  nand nand_23 (nand_23_out, a, nand_2_out);
  nand nand_24 (nand_24_out, nand_3_out, c, d);
  nand nand_25 (nand_25_out, nand_4_out, b, nand_5_out);
  nand nand_26 (nand_26_out, nand_6_out, b, nand_7_out);
  nand nand_27 (nand_27_out, nand_8_out, nand_9_out, d);
  nand nand_28 (nand_28_out, nand_10_out, nand_11_out, d);
  nand nand_29 (nand_29_out, nand_12_out, c, nand_13_out);
  nand nand_30 (nand_30_out, nand_14_out, c, nand_15_out);
  nand nand_31 (nand_31_out, nand_16_out, nand_17_out);
  nand nand_32 (nand_32_out, nand_18_out, nand_19_out);
  nand nand_33 (nand_33_out, nand_20_out, nand_21_out);
  nand nand_34 (x, nand_22_out, nand_23_out);
  nand nand_35 (y, nand_24_out, nand_25_out, nand_26_out);
  nand nand_36 (z, nand_27_out, nand_28_out, nand_29_out, nand_30_out);
  nand nand_37 (u, nand_31_out, nand_32_out, nand_33_out);
endmodule

module bounce (
  input  CLK,
  output [9:0] LEDOUT
);

  wire bounce_tl_1_u, bounce_tl_1_x, bounce_tl_1_y, bounce_tl_1_z, d_ff_1_q, d_ff_1_qn, d_ff_2_q, d_ff_2_qn,
       d_ff_3_q, d_ff_3_qn, d_ff_4_q, d_ff_4_qn;

  bounce_tl bounce_tl_1 (
    .a(d_ff_1_q), .b(d_ff_2_q), .c(d_ff_3_q), .d(d_ff_4_q), .x(bounce_tl_1_x), .y(bounce_tl_1_y),
    .z(bounce_tl_1_z), .u(bounce_tl_1_u));
  D_Flip_Flop d_ff_1 (.D(bounce_tl_1_x), .clk(CLK), .Q(d_ff_1_q), .Qn(d_ff_1_qn));  // open: preset, reset
  D_Flip_Flop d_ff_2 (.D(bounce_tl_1_y), .clk(CLK), .Q(d_ff_2_q), .Qn(d_ff_2_qn));  // open: preset, reset
  D_Flip_Flop d_ff_3 (.D(bounce_tl_1_z), .clk(CLK), .Q(d_ff_3_q), .Qn(d_ff_3_qn));  // open: preset, reset
  D_Flip_Flop d_ff_4 (.D(bounce_tl_1_u), .clk(CLK), .Q(d_ff_4_q), .Qn(d_ff_4_qn));  // open: preset, reset
  bounce_dec bounce_dec_1 (
    .Input_1(d_ff_1_q), .Input_2(d_ff_2_q), .Input_3(d_ff_3_q), .Input_4(d_ff_4_q), .Output_1(LEDOUT[0]),
    .Output_2(LEDOUT[1]), .Output_3(LEDOUT[2]), .Output_4(LEDOUT[3]), .Output_5(LEDOUT[4]),
    .Output_6(LEDOUT[5]), .Output_7(LEDOUT[6]), .Output_8(LEDOUT[7]), .Output_9(LEDOUT[8]),
    .Output_10(LEDOUT[9]));
  LED led_1 (.in(LEDOUT[9]));
  LED led_2 (.in(LEDOUT[6]));
  LED led_3 (.in(LEDOUT[5]));
  LED led_4 (.in(LEDOUT[7]));
  LED led_5 (.in(LEDOUT[8]));
  LED led_6 (.in(LEDOUT[3]));
  LED led_7 (.in(LEDOUT[2]));
  LED led_8 (.in(LEDOUT[4]));
  LED led_9 (.in(LEDOUT[1]));
  LED led_10 (.in(LEDOUT[0]));
endmodule

module bounce_dec (
  input  Input_1,
  input  Input_2,
  input  Input_3,
  input  Input_4,
  output Output_1,
  output Output_2,
  output Output_3,
  output Output_4,
  output Output_5,
  output Output_6,
  output Output_7,
  output Output_8,
  output Output_9,
  output Output_10
);

  wire nand_1_out, nand_2_out, nand_3_out, nand_4_out, nand_5_out, nand_6_out, nand_7_out, nand_8_out,
       nand_9_out, nand_10_out, nand_11_out, nand_12_out, nand_13_out, nand_14_out, nand_15_out, nand_16_out,
       nand_17_out, nand_18_out, nand_19_out, nand_20_out, nand_21_out, nand_22_out, nand_23_out,
       nand_24_out, nand_25_out, nand_26_out, nand_27_out, nand_28_out, nand_29_out, nand_30_out,
       nand_31_out, nand_32_out, nand_33_out, nand_34_out, nand_35_out, nand_36_out, nand_37_out,
       nand_38_out, nand_39_out, nand_40_out, nand_41_out, nand_42_out, nand_43_out, nand_44_out,
       nand_45_out, nand_46_out, nand_47_out, nand_48_out, nand_49_out, nand_50_out, nand_51_out,
       nand_52_out, nand_53_out, nand_54_out, nand_55_out, nand_56_out, nand_57_out, nand_58_out,
       nand_59_out, nand_60_out, nand_61_out, nand_62_out, nand_63_out, nand_64_out, nand_65_out,
       nand_66_out, nand_67_out, nand_68_out, nand_69_out, nand_70_out, nand_71_out, nand_72_out,
       nand_73_out, nand_74_out, nand_75_out, nand_76_out, nand_77_out, nand_78_out, nand_79_out,
       nand_80_out, nand_81_out, nand_82_out, nand_83_out;

  nand nand_1 (nand_1_out, Input_1, Input_1);
  nand nand_2 (nand_2_out, Input_2, Input_2);
  nand nand_3 (nand_3_out, Input_3, Input_3);
  nand nand_4 (nand_4_out, Input_4, Input_4);
  nand nand_5 (nand_5_out, Input_3, Input_3);
  nand nand_6 (nand_6_out, Input_4, Input_4);
  nand nand_7 (nand_7_out, Input_1, Input_1);
  nand nand_8 (nand_8_out, Input_2, Input_2);
  nand nand_9 (nand_9_out, Input_3, Input_3);
  nand nand_10 (nand_10_out, Input_2, Input_2);
  nand nand_11 (nand_11_out, Input_3, Input_3);
  nand nand_12 (nand_12_out, Input_4, Input_4);
  nand nand_13 (nand_13_out, Input_1, Input_1);
  nand nand_14 (nand_14_out, Input_2, Input_2);
  nand nand_15 (nand_15_out, Input_3, Input_3);
  nand nand_16 (nand_16_out, Input_2, Input_2);
  nand nand_17 (nand_17_out, Input_4, Input_4);
  nand nand_18 (nand_18_out, Input_2, Input_2);
  nand nand_19 (nand_19_out, Input_3, Input_3);
  nand nand_20 (nand_20_out, Input_4, Input_4);
  nand nand_21 (nand_21_out, Input_1, Input_1);
  nand nand_22 (nand_22_out, Input_2, Input_2);
  nand nand_23 (nand_23_out, Input_2, Input_2);
  nand nand_24 (nand_24_out, Input_2, Input_2);
  nand nand_25 (nand_25_out, Input_3, Input_3);
  nand nand_26 (nand_26_out, Input_4, Input_4);
  nand nand_27 (nand_27_out, Input_2, Input_2);
  nand nand_28 (nand_28_out, Input_2, Input_2);
  nand nand_29 (nand_29_out, Input_1, Input_1);
  nand nand_30 (nand_30_out, Input_3, Input_3);
  nand nand_31 (nand_31_out, Input_4, Input_4);
  nand nand_32 (nand_32_out, Input_2, Input_2);
  nand nand_33 (nand_33_out, Input_1, Input_1);
  nand nand_34 (nand_34_out, Input_2, Input_2);
  nand nand_35 (nand_35_out, Input_1, Input_1);
  nand nand_36 (nand_36_out, Input_3, Input_3);
  nand nand_37 (nand_37_out, Input_1, Input_1);
  nand nand_38 (nand_38_out, Input_2, Input_2);
  nand nand_39 (nand_39_out, Input_3, Input_3);
  nand nand_40 (nand_40_out, Input_2, Input_2);
  nand nand_41 (nand_41_out, Input_4, Input_4);
  nand nand_42 (nand_42_out, Input_1, Input_1);
  nand nand_43 (nand_43_out, Input_1, Input_1);
  nand nand_44 (nand_44_out, Input_2, Input_2);
  nand nand_45 (nand_45_out, Input_3, Input_3);
  nand nand_46 (nand_46_out, Input_1, Input_1);
  nand nand_47 (nand_47_out, Input_2, Input_2);
  nand nand_48 (nand_48_out, Input_3, Input_3);
  nand nand_49 (nand_49_out, Input_4, Input_4);
  nand nand_50 (nand_50_out, Input_1, Input_1);
  nand nand_51 (nand_51_out, Input_1, Input_1);
  nand nand_52 (nand_52_out, Input_1, Input_1);
  nand nand_53 (nand_53_out, Input_4, Input_4);
  nand nand_54 (nand_54_out, nand_1_out, nand_2_out, nand_3_out, nand_4_out);
  nand nand_55 (nand_55_out, Input_1, Input_2, nand_5_out, nand_6_out);
  nand nand_56 (nand_56_out, nand_7_out, nand_8_out, nand_9_out);
  nand nand_57 (nand_57_out, Input_1, nand_10_out, Input_3, Input_4);
  nand nand_58 (nand_58_out, Input_1, Input_2, nand_11_out, nand_12_out);
  nand nand_59 (nand_59_out, nand_13_out, nand_14_out, nand_15_out);
  nand nand_60 (nand_60_out, nand_16_out, Input_3, nand_17_out);
  nand nand_61 (nand_61_out, Input_1, nand_18_out, Input_3);
  nand nand_62 (nand_62_out, Input_1, Input_2, nand_19_out, nand_20_out);
  nand nand_63 (nand_63_out, nand_21_out, nand_22_out);
  nand nand_64 (nand_64_out, nand_23_out, Input_4);
  nand nand_65 (nand_65_out, nand_24_out, Input_3);
  nand nand_66 (nand_66_out, Input_1, Input_2, nand_25_out, nand_26_out);
  nand nand_67 (nand_67_out, nand_27_out, Input_4);
  nand nand_68 (nand_68_out, nand_28_out, Input_3);
  nand nand_69 (nand_69_out, nand_29_out, Input_2, nand_30_out, nand_31_out);
  nand nand_70 (nand_70_out, Input_1, nand_32_out);
  nand nand_71 (nand_71_out, nand_33_out, nand_34_out, Input_3);
  nand nand_72 (nand_72_out, nand_35_out, Input_2, nand_36_out);
  nand nand_73 (nand_73_out, nand_37_out, Input_2, Input_4);
  nand nand_74 (nand_74_out, Input_1, nand_38_out, nand_39_out);
  nand nand_75 (nand_75_out, Input_1, nand_40_out, nand_41_out);
  nand nand_76 (nand_76_out, nand_42_out, Input_3, Input_4);
  nand nand_77 (nand_77_out, nand_43_out, Input_2);
  nand nand_78 (nand_78_out, Input_1, nand_44_out, nand_45_out);
  nand nand_79 (nand_79_out, nand_46_out, Input_2);
  nand nand_80 (nand_80_out, Input_1, nand_47_out, nand_48_out, nand_49_out);
  nand nand_81 (nand_81_out, nand_50_out, Input_2, Input_4);
  nand nand_82 (nand_82_out, nand_51_out, Input_2, Input_3);
  nand nand_83 (nand_83_out, nand_52_out, Input_2, Input_3, nand_53_out);
  nand nand_84 (Output_1, nand_54_out, nand_55_out);
  nand nand_85 (Output_2, nand_56_out, nand_57_out, nand_58_out);
  nand nand_86 (Output_3, nand_59_out, nand_60_out, nand_61_out, nand_62_out);
  nand nand_87 (Output_4, nand_63_out, nand_64_out, nand_65_out, nand_66_out);
  nand nand_88 (Output_5, nand_67_out, nand_68_out, nand_69_out, nand_70_out);
  nand nand_89 (Output_6, nand_71_out, nand_72_out, nand_73_out, nand_74_out, nand_75_out);
  nand nand_90 (Output_7, nand_76_out, nand_77_out, nand_78_out);
  nand nand_91 (Output_8, nand_79_out, nand_80_out);
  nand nand_92 (Output_9, nand_81_out, nand_82_out);
  nand nand_93 (Output_10, nand_83_out, nand_83_out);
endmodule

module bump_tl (
  input  Input_1,
  input  Input_2,
  input  Input_3,
  output Output_1,
  output Output_2,
  output Output_3
);

  wire nand_1_out, nand_2_out, nand_3_out, nand_4_out, nand_5_out, nand_7_out, nand_8_out, nand_9_out,
       nand_10_out, nand_11_out;

  nand nand_1 (nand_1_out, Input_1, Input_1);
  nand nand_2 (nand_2_out, Input_2, Input_2);
  nand nand_3 (nand_3_out, Input_3, Input_3);
  nand nand_4 (nand_4_out, Input_2, Input_2);
  nand nand_5 (nand_5_out, Input_3, Input_3);
  nand nand_6 (Output_3, Input_3, Input_3);
  nand nand_7 (nand_7_out, nand_1_out, Input_2, Input_3);
  nand nand_8 (nand_8_out, Input_1, nand_2_out);
  nand nand_9 (nand_9_out, Input_1, nand_3_out);
  nand nand_10 (nand_10_out, nand_4_out, Input_3);
  nand nand_11 (nand_11_out, Input_2, nand_5_out);
  nand nand_12 (Output_1, nand_7_out, nand_8_out, nand_9_out);
  nand nand_13 (Output_2, nand_10_out, nand_11_out);
endmodule

module bump_dec (
  input  Input_1,
  input  Input_2,
  input  Input_3,
  output Output_1,
  output Output_2,
  output Output_3,
  output Output_4,
  output Output_5,
  output Output_6,
  output Output_7,
  output Output_8,
  output Output_9,
  output Output_10
);

  wire nand_1_out, nand_2_out, nand_3_out, nand_4_out, nand_5_out, nand_6_out, nand_7_out, nand_8_out,
       nand_9_out, nand_10_out, nand_11_out, nand_12_out, nand_13_out, nand_14_out, nand_15_out, nand_16_out,
       nand_17_out, nand_18_out, nand_19_out, nand_20_out, nand_21_out, nand_22_out, nand_23_out,
       nand_24_out, nand_25_out, nand_26_out, nand_27_out, nand_28_out, nand_29_out, nand_30_out,
       nand_32_out, nand_33_out, nand_34_out, nand_35_out, nand_36_out, nand_37_out, nand_38_out,
       nand_39_out, nand_40_out, nand_41_out, nand_42_out, nand_43_out, nand_44_out, nand_45_out,
       nand_46_out, nand_47_out;

  nand nand_1 (nand_1_out, Input_1, Input_1);
  nand nand_2 (nand_2_out, Input_2, Input_2);
  nand nand_3 (nand_3_out, Input_3, Input_3);
  nand nand_4 (nand_4_out, Input_1, Input_1);
  nand nand_5 (nand_5_out, Input_1, Input_1);
  nand nand_6 (nand_6_out, Input_2, Input_2);
  nand nand_7 (nand_7_out, Input_3, Input_3);
  nand nand_8 (nand_8_out, Input_1, Input_1);
  nand nand_9 (nand_9_out, Input_1, Input_1);
  nand nand_10 (nand_10_out, Input_2, Input_2);
  nand nand_11 (nand_11_out, Input_3, Input_3);
  nand nand_12 (nand_12_out, Input_3, Input_3);
  nand nand_13 (nand_13_out, Input_1, Input_1);
  nand nand_14 (nand_14_out, Input_1, Input_1);
  nand nand_15 (nand_15_out, Input_2, Input_2);
  nand nand_16 (nand_16_out, Input_2, Input_2);
  nand nand_17 (nand_17_out, Input_3, Input_3);
  nand nand_18 (nand_18_out, Input_2, Input_2);
  nand nand_19 (nand_19_out, Input_1, Input_1);
  nand nand_20 (nand_20_out, Input_3, Input_3);
  nand nand_21 (nand_21_out, Input_1, Input_1);
  nand nand_22 (nand_22_out, Input_2, Input_2);
  nand nand_23 (nand_23_out, Input_1, Input_1);
  nand nand_24 (nand_24_out, Input_2, Input_2);
  nand nand_25 (nand_25_out, Input_3, Input_3);
  nand nand_26 (nand_26_out, Input_1, Input_1);
  nand nand_27 (nand_27_out, nand_1_out, nand_2_out, nand_3_out);
  nand nand_28 (nand_28_out, nand_4_out, Input_2, Input_3);
  nand nand_29 (nand_29_out, nand_5_out, nand_6_out);
  nand nand_30 (nand_30_out, Input_3, Input_3);
  nand nand_31 (Output_3, nand_7_out, nand_8_out);
  nand nand_32 (nand_32_out, nand_9_out, nand_10_out, Input_3);
  nand nand_33 (nand_33_out, Input_2, nand_11_out);
  nand nand_34 (nand_34_out, Input_1, nand_12_out);
  nand nand_35 (nand_35_out, nand_13_out, Input_2);
  nand nand_36 (nand_36_out, nand_14_out, Input_2);
  nand nand_37 (nand_37_out, Input_1, nand_15_out, Input_3);
  nand nand_38 (nand_38_out, nand_16_out, Input_3);
  nand nand_39 (nand_39_out, Input_2, nand_17_out);
  nand nand_40 (nand_40_out, Input_1, nand_18_out);
  nand nand_41 (nand_41_out, nand_19_out, Input_3);
  nand nand_42 (nand_42_out, Input_1, nand_20_out);
  nand nand_43 (nand_43_out, Input_1, Input_2);
  nand nand_44 (nand_44_out, nand_21_out, nand_22_out);
  nand nand_45 (nand_45_out, Input_2, Input_3);
  nand nand_46 (nand_46_out, nand_23_out, nand_24_out, nand_25_out);
  nand nand_47 (nand_47_out, nand_26_out, Input_2, Input_3);
  nand nand_48 (Output_1, nand_27_out, nand_28_out);
  nand nand_49 (Output_2, nand_29_out, nand_30_out);
  nand nand_50 (Output_4, nand_32_out, nand_33_out, nand_34_out);
  nand nand_51 (Output_5, nand_35_out, nand_35_out);
  nand nand_52 (Output_6, nand_36_out, nand_37_out);
  nand nand_53 (Output_7, nand_38_out, nand_39_out, nand_40_out);
  nand nand_54 (Output_8, nand_41_out, nand_42_out, nand_43_out);
  nand nand_55 (Output_9, nand_44_out, nand_45_out);
  nand nand_56 (Output_10, nand_46_out, nand_47_out);
endmodule

module bump (
  input  CLK,
  output [9:0] LEDOUT
);

  wire bump_tl_1_output_1, bump_tl_1_output_2, bump_tl_1_output_3, d_ff_1_q, d_ff_2_q, d_ff_3_q;

  bump_tl bump_tl_1 (
    .Input_1(d_ff_1_q), .Input_2(d_ff_2_q), .Input_3(d_ff_3_q), .Output_1(bump_tl_1_output_1),
    .Output_2(bump_tl_1_output_2), .Output_3(bump_tl_1_output_3));
  D_Flip_Flop d_ff_1 (.D(bump_tl_1_output_1), .clk(CLK), .Q(d_ff_1_q));  // open: Qn, preset, reset
  D_Flip_Flop d_ff_2 (.D(bump_tl_1_output_2), .clk(CLK), .Q(d_ff_2_q));  // open: Qn, preset, reset
  D_Flip_Flop d_ff_3 (.D(bump_tl_1_output_3), .clk(CLK), .Q(d_ff_3_q));  // open: Qn, preset, reset
  bump_dec bump_dec_1 (
    .Input_1(d_ff_1_q), .Input_2(d_ff_2_q), .Input_3(d_ff_3_q), .Output_1(LEDOUT[0]), .Output_2(LEDOUT[1]),
    .Output_3(LEDOUT[2]), .Output_4(LEDOUT[3]), .Output_5(LEDOUT[4]), .Output_6(LEDOUT[5]),
    .Output_7(LEDOUT[6]), .Output_8(LEDOUT[7]), .Output_9(LEDOUT[8]), .Output_10(LEDOUT[9]));
endmodule
